// Logisim project HW2_SalihYESİR_24bitALU.circ as structural Verilog: 13 circuits, main circuit main
module main (
  input  [23:0] A,
  input  [23:0] B,
  input  ADD_0__SUB_1,
  input  [2:0] SECIM,
  output [23:0] RESULT,
  output Overflow,
  output Carry,
  output CLA_Overflow,
  output CLA_Carry,
  output Zero,
  output Negative
);

  _24_bit_ALU u_24_bit_alu_1 (
    .A(A), .B(B), .ADD_0__SUB_1(ADD_0__SUB_1), .Negative(Negative), .RESULT(RESULT), .Zero(Zero),
    .Overflow(Overflow), .Carry(Carry), .CLA_Overflow(CLA_Overflow), .CLA_Carry(CLA_Carry), .SECIM(SECIM));

  // Notes on the sheet:
  //   000:AND
  //   001: OR
  //   010:XOR
  //   011:NOR
  //   100:Ripple
  //   101:CLA
  //   110:Multiply LO
  //   111:Multiply HI
  //   Salih YESİR 1850144004
  //   Ripple işlemi seçilmediyse burayı ciddiye almayın
  //   CLA işlemi seçilmediyse burayı ciddiye almayın
  //   Bu kısım tüm sonuçları kapsar
endmodule

module _24_bit_AND (
  input  [23:0] A,
  input  [23:0] B,
  output [23:0] Result
);

  and AND (Result[0], A[0], B[0]);
  and AND_2 (Result[1], A[1], B[1]);
  and AND_3 (Result[2], A[2], B[2]);
  and AND_4 (Result[3], A[3], B[3]);
  and AND_5 (Result[4], A[4], B[4]);
  and AND_6 (Result[5], A[5], B[5]);
  and AND_7 (Result[6], A[6], B[6]);
  and AND_8 (Result[7], A[7], B[7]);
  and AND_9 (Result[8], A[8], B[8]);
  and AND_10 (Result[9], A[9], B[9]);
  and AND_11 (Result[10], A[10], B[10]);
  and AND_12 (Result[11], A[11], B[11]);
  and AND_13 (Result[12], A[12], B[12]);
  and AND_14 (Result[13], A[13], B[13]);
  and AND_15 (Result[14], A[14], B[14]);
  and AND_16 (Result[15], A[15], B[15]);
  and AND_17 (Result[16], A[16], B[16]);
  and AND_18 (Result[17], A[17], B[17]);
  and AND_19 (Result[18], A[18], B[18]);
  and AND_20 (Result[19], A[19], B[19]);
  and AND_21 (Result[20], A[20], B[20]);
  and AND_22 (Result[21], A[21], B[21]);
  and AND_23 (Result[22], A[22], B[22]);
  and AND_24 (Result[23], A[23], B[23]);

  // Notes on the sheet:
  //   Result: pull=up
  //   24-bit AND
endmodule

module _24_bit_OR (
  input  [23:0] A,
  input  [23:0] B,
  output [23:0] Result
);

  or OR (Result[0], A[0], B[0]);
  or OR_2 (Result[1], A[1], B[1]);
  or OR_3 (Result[2], A[2], B[2]);
  or OR_4 (Result[3], A[3], B[3]);
  or OR_5 (Result[4], A[4], B[4]);
  or OR_6 (Result[5], A[5], B[5]);
  or OR_7 (Result[6], A[6], B[6]);
  or OR_8 (Result[7], A[7], B[7]);
  or OR_9 (Result[8], A[8], B[8]);
  or OR_10 (Result[9], A[9], B[9]);
  or OR_11 (Result[10], A[10], B[10]);
  or OR_12 (Result[11], A[11], B[11]);
  or OR_13 (Result[12], A[12], B[12]);
  or OR_14 (Result[13], A[13], B[13]);
  or OR_15 (Result[14], A[14], B[14]);
  or OR_16 (Result[15], A[15], B[15]);
  or OR_17 (Result[16], A[16], B[16]);
  or OR_18 (Result[17], A[17], B[17]);
  or OR_19 (Result[18], A[18], B[18]);
  or OR_20 (Result[19], A[19], B[19]);
  or OR_21 (Result[20], A[20], B[20]);
  or OR_22 (Result[21], A[21], B[21]);
  or OR_23 (Result[22], A[22], B[22]);
  or OR_24 (Result[23], A[23], B[23]);

  // Notes on the sheet:
  //   Result: pull=up
  //   24-bit OR
endmodule

module _24_bit_XOR (
  input  [23:0] A,
  input  [23:0] B,
  output [23:0] Result
);

  xor XOR (Result[0], A[0], B[0]);
  xor XOR_2 (Result[1], A[1], B[1]);
  xor XOR_3 (Result[2], A[2], B[2]);
  xor XOR_4 (Result[3], A[3], B[3]);
  xor XOR_5 (Result[4], A[4], B[4]);
  xor XOR_6 (Result[5], A[5], B[5]);
  xor XOR_7 (Result[6], A[6], B[6]);
  xor XOR_8 (Result[7], A[7], B[7]);
  xor XOR_9 (Result[8], A[8], B[8]);
  xor XOR_10 (Result[9], A[9], B[9]);
  xor XOR_11 (Result[10], A[10], B[10]);
  xor XOR_12 (Result[11], A[11], B[11]);
  xor XOR_13 (Result[12], A[12], B[12]);
  xor XOR_14 (Result[13], A[13], B[13]);
  xor XOR_15 (Result[14], A[14], B[14]);
  xor XOR_16 (Result[15], A[15], B[15]);
  xor XOR_17 (Result[16], A[16], B[16]);
  xor XOR_18 (Result[17], A[17], B[17]);
  xor XOR_19 (Result[18], A[18], B[18]);
  xor XOR_20 (Result[19], A[19], B[19]);
  xor XOR_21 (Result[20], A[20], B[20]);
  xor XOR_22 (Result[21], A[21], B[21]);
  xor XOR_23 (Result[22], A[22], B[22]);
  xor XOR_24 (Result[23], A[23], B[23]);

  // Notes on the sheet:
  //   Result: pull=up
  //   24-bit XOR
endmodule

module _24_bit_NOR (
  input  [23:0] A,
  input  [23:0] B,
  output [23:0] Result
);

  nor NOR (Result[0], A[0], B[0]);
  nor NOR_2 (Result[1], A[1], B[1]);
  nor NOR_3 (Result[2], A[2], B[2]);
  nor NOR_4 (Result[3], A[3], B[3]);
  nor NOR_5 (Result[4], A[4], B[4]);
  nor NOR_6 (Result[5], A[5], B[5]);
  nor NOR_7 (Result[6], A[6], B[6]);
  nor NOR_8 (Result[7], A[7], B[7]);
  nor NOR_9 (Result[8], A[8], B[8]);
  nor NOR_10 (Result[9], A[9], B[9]);
  nor NOR_11 (Result[10], A[10], B[10]);
  nor NOR_12 (Result[11], A[11], B[11]);
  nor NOR_13 (Result[12], A[12], B[12]);
  nor NOR_14 (Result[13], A[13], B[13]);
  nor NOR_15 (Result[14], A[14], B[14]);
  nor NOR_16 (Result[15], A[15], B[15]);
  nor NOR_17 (Result[16], A[16], B[16]);
  nor NOR_18 (Result[17], A[17], B[17]);
  nor NOR_19 (Result[18], A[18], B[18]);
  nor NOR_20 (Result[19], A[19], B[19]);
  nor NOR_21 (Result[20], A[20], B[20]);
  nor NOR_22 (Result[21], A[21], B[21]);
  nor NOR_23 (Result[22], A[22], B[22]);
  nor NOR_24 (Result[23], A[23], B[23]);

  // Notes on the sheet:
  //   Result: pull=up
  //   24-bit NOR
endmodule

// Ripple
module _24_bit_ADD_SUB (
  input  Add_0__Sub_1,
  input  [23:0] A,
  input  [23:0] B,
  output [23:0] RESULT,
  output Overflow,
  output Carry_Out
);

  wire and_1_out, and_2_out, B0, B1, B2, B3, B4, B5, B6, B7, B8, B9, B10, B11, B12, B13, B14, B15, B16, B17,
       B18, B19, B20, B21, B22, B23, LSB_carry_out, n1_bit_adder_1_carry_out, n1_bit_adder_2_carry_out,
       n1_bit_adder_3_carry_out, n1_bit_adder_4_carry_out, n1_bit_adder_5_carry_out,
       n1_bit_adder_6_carry_out, n1_bit_adder_7_carry_out, n1_bit_adder_8_carry_out,
       n1_bit_adder_9_carry_out, n1_bit_adder_10_carry_out, n1_bit_adder_11_carry_out,
       n1_bit_adder_12_carry_out, n1_bit_adder_13_carry_out, n1_bit_adder_14_carry_out,
       n1_bit_adder_15_carry_out, n1_bit_adder_16_carry_out, n1_bit_adder_17_carry_out,
       n1_bit_adder_18_carry_out, n1_bit_adder_19_carry_out, n1_bit_adder_20_carry_out,
       n1_bit_adder_21_carry_out, n1_bit_adder_22_carry_out, not_1_out, not_2_out, not_3_out;

  _1_bit_Adder u_1_bit_adder_1 (
    .Carry_In(n1_bit_adder_4_carry_out), .A(A[15]), .B(B15), .Sum(RESULT[15]),
    .Carry_Out(n1_bit_adder_1_carry_out));
  _1_bit_Adder u_1_bit_adder_2 (
    .Carry_In(n1_bit_adder_1_carry_out), .A(A[16]), .B(B16), .Sum(RESULT[16]),
    .Carry_Out(n1_bit_adder_2_carry_out));
  _1_bit_Adder u_1_bit_adder_3 (
    .Carry_In(n1_bit_adder_8_carry_out), .A(A[13]), .B(B13), .Sum(RESULT[13]),
    .Carry_Out(n1_bit_adder_3_carry_out));
  _1_bit_Adder u_1_bit_adder_4 (
    .Carry_In(n1_bit_adder_3_carry_out), .A(A[14]), .B(B14), .Sum(RESULT[14]),
    .Carry_Out(n1_bit_adder_4_carry_out));
  _1_bit_Adder u_1_bit_adder_5 (
    .Carry_In(n1_bit_adder_2_carry_out), .A(A[17]), .B(B17), .Sum(RESULT[17]),
    .Carry_Out(n1_bit_adder_5_carry_out));
  _1_bit_Adder u_1_bit_adder_6 (
    .Carry_In(n1_bit_adder_5_carry_out), .A(A[18]), .B(B18), .Sum(RESULT[18]),
    .Carry_Out(n1_bit_adder_6_carry_out));
  _1_bit_Adder u_1_bit_adder_7 (
    .Carry_In(n1_bit_adder_11_carry_out), .A(A[11]), .B(B11), .Sum(RESULT[11]),
    .Carry_Out(n1_bit_adder_7_carry_out));
  _1_bit_Adder u_1_bit_adder_8 (
    .Carry_In(n1_bit_adder_7_carry_out), .A(A[12]), .B(B12), .Sum(RESULT[12]),
    .Carry_Out(n1_bit_adder_8_carry_out));
  _1_bit_Adder u_1_bit_adder_9 (
    .Carry_In(n1_bit_adder_6_carry_out), .A(A[19]), .B(B19), .Sum(RESULT[19]),
    .Carry_Out(n1_bit_adder_9_carry_out));
  _1_bit_Adder u_1_bit_adder_10 (
    .Carry_In(n1_bit_adder_14_carry_out), .A(A[9]), .B(B9), .Sum(RESULT[9]),
    .Carry_Out(n1_bit_adder_10_carry_out));
  _1_bit_Adder u_1_bit_adder_11 (
    .Carry_In(n1_bit_adder_10_carry_out), .A(A[10]), .B(B10), .Sum(RESULT[10]),
    .Carry_Out(n1_bit_adder_11_carry_out));
  _1_bit_Adder u_1_bit_adder_12 (
    .Carry_In(n1_bit_adder_13_carry_out), .A(A[21]), .B(B21), .Sum(RESULT[21]),
    .Carry_Out(n1_bit_adder_12_carry_out));
  _1_bit_Adder u_1_bit_adder_13 (
    .Carry_In(n1_bit_adder_9_carry_out), .A(A[20]), .B(B20), .Sum(RESULT[20]),
    .Carry_Out(n1_bit_adder_13_carry_out));
  _1_bit_Adder u_1_bit_adder_14 (
    .Carry_In(n1_bit_adder_16_carry_out), .A(A[8]), .B(B8), .Sum(RESULT[8]),
    .Carry_Out(n1_bit_adder_14_carry_out));
  _1_bit_Adder u_1_bit_adder_15 (
    .Carry_In(n1_bit_adder_12_carry_out), .A(A[22]), .B(B22), .Sum(RESULT[22]),
    .Carry_Out(n1_bit_adder_15_carry_out));
  _1_bit_Adder u_1_bit_adder_16 (
    .Carry_In(n1_bit_adder_17_carry_out), .A(A[7]), .B(B7), .Sum(RESULT[7]),
    .Carry_Out(n1_bit_adder_16_carry_out));
  _1_bit_Adder u_1_bit_adder_17 (
    .Carry_In(n1_bit_adder_18_carry_out), .A(A[6]), .B(B6), .Sum(RESULT[6]),
    .Carry_Out(n1_bit_adder_17_carry_out));
  not not_1 (not_1_out, B23);
  _1_bit_Adder MSB (.Carry_In(n1_bit_adder_15_carry_out), .A(A[23]), .B(B23), .Sum(RESULT[23]), .Carry_Out(Carry_Out));
  not not_2 (not_2_out, n1_bit_adder_15_carry_out);
  xor xor_1 (B23, B[23], Add_0__Sub_1);
  xor xor_2 (B21, B[21], Add_0__Sub_1);
  xor xor_3 (B22, B[22], Add_0__Sub_1);
  _1_bit_Adder u_1_bit_adder_18 (
    .Carry_In(n1_bit_adder_19_carry_out), .A(A[5]), .B(B5), .Sum(RESULT[5]),
    .Carry_Out(n1_bit_adder_18_carry_out));
  _1_bit_Adder u_1_bit_adder_19 (
    .Carry_In(n1_bit_adder_20_carry_out), .A(A[4]), .B(B4), .Sum(RESULT[4]),
    .Carry_Out(n1_bit_adder_19_carry_out));
  not not_3 (not_3_out, A[23]);
  and and_1 (and_1_out, not_3_out, not_1_out, n1_bit_adder_15_carry_out);
  and and_2 (and_2_out, not_2_out, B23, A[23]);
  xor xor_4 (B19, B[19], Add_0__Sub_1);
  xor xor_5 (B20, B[20], Add_0__Sub_1);
  _1_bit_Adder u_1_bit_adder_20 (
    .Carry_In(n1_bit_adder_21_carry_out), .A(A[3]), .B(B3), .Sum(RESULT[3]),
    .Carry_Out(n1_bit_adder_20_carry_out));
  _1_bit_Adder u_1_bit_adder_21 (
    .Carry_In(n1_bit_adder_22_carry_out), .A(A[2]), .B(B2), .Sum(RESULT[2]),
    .Carry_Out(n1_bit_adder_21_carry_out));
  or or_1 (Overflow, and_1_out, and_2_out);
  xor xor_6 (B16, B[16], Add_0__Sub_1);
  xor xor_7 (B17, B[17], Add_0__Sub_1);
  xor xor_8 (B18, B[18], Add_0__Sub_1);
  _1_bit_Adder LSB (.Carry_In(Add_0__Sub_1), .A(A[0]), .B(B0), .Sum(RESULT[0]), .Carry_Out(LSB_carry_out));
  _1_bit_Adder u_1_bit_adder_22 (
    .Carry_In(LSB_carry_out), .A(A[1]), .B(B1), .Sum(RESULT[1]), .Carry_Out(n1_bit_adder_22_carry_out));
  xor xor_9 (B13, B[13], Add_0__Sub_1);
  xor xor_10 (B15, B[15], Add_0__Sub_1);
  xor xor_11 (B14, B[14], Add_0__Sub_1);
  xor xor_12 (B12, B[12], Add_0__Sub_1);
  xor xor_13 (B11, B[11], Add_0__Sub_1);
  xor xor_14 (B10, B[10], Add_0__Sub_1);
  xor xor_15 (B9, B[9], Add_0__Sub_1);
  xor xor_16 (B8, B[8], Add_0__Sub_1);
  xor xor_17 (B7, B[7], Add_0__Sub_1);
  xor xor_18 (B6, B[6], Add_0__Sub_1);
  xor xor_19 (B3, B[3], Add_0__Sub_1);
  xor xor_20 (B5, B[5], Add_0__Sub_1);
  xor xor_21 (B4, B[4], Add_0__Sub_1);
  xor xor_22 (B1, B[1], Add_0__Sub_1);
  xor xor_23 (B2, B[2], Add_0__Sub_1);
  xor xor_24 (B0, B[0], Add_0__Sub_1);

  // Other names for the same wires on the sheet: A_S = Add_0__Sub_1; _0 = RESULT[0]; _1 = RESULT[1]; _2 = RESULT[2];
  //   _3 = RESULT[3]; _4 = RESULT[4]; _5 = RESULT[5]; _6 = RESULT[6]; _7 = RESULT[7]; _8 = RESULT[8]; _9 = RESULT[9];
  //   _10 = RESULT[10]; _11 = RESULT[11]; _12 = RESULT[12]; _13 = RESULT[13]; _14 = RESULT[14]; _15 = RESULT[15];
  //   _16 = RESULT[16]; _17 = RESULT[17]; _18 = RESULT[18]; _19 = RESULT[19]; _20 = RESULT[20]; _21 = RESULT[21];
  //   _22 = RESULT[22]; _23 = RESULT[23]

  // Notes on the sheet:
  //   Elde kullanılamaz
  //   24 bit Add/Sub
  //   Sayı overflow yüzünden negatif olabilir. Bunu bildirir
endmodule

// +
module _1_bit_Adder (
  input  Carry_In,
  input  A,
  input  B,
  output Sum,
  output Carry_Out
);

  wire and_1_out, and_2_out, xor_1_out;

  xor xor_1 (xor_1_out, A, B);
  xor xor_2 (Sum, xor_1_out, Carry_In);
  and and_1 (and_1_out, Carry_In, xor_1_out);
  and and_2 (and_2_out, B, A);
  or or_1 (Carry_Out, and_1_out, and_2_out);

  // Notes on the sheet:
  //   1-bit Adder
endmodule

// MUL
module _1_bit_MUL (
  input  Carry_In,
  input  Sum_In,
  input  A,
  input  B,
  output Sum,
  output Carry
);

  wire and_1_out;

  _1_bit_Adder u_1_bit_adder_1 (.Carry_In(Carry_In), .A(Sum_In), .B(and_1_out), .Sum(Sum), .Carry_Out(Carry));
  and and_1 (and_1_out, A, B);

  // Notes on the sheet:
  //   1-bit MUL
endmodule
// MUL
module _24_BIT_MUL (
  input  [23:0] A,
  input  [23:0] B,
  output [23:0] HI,
  output [23:0] LO
);

  wire n1_bit_mul_2_carry, n1_bit_mul_2_sum, n1_bit_mul_3_carry, n1_bit_mul_4_carry, n1_bit_mul_4_sum,
       n1_bit_mul_5_carry, n1_bit_mul_5_sum, n1_bit_mul_6_carry, n1_bit_mul_7_carry, n1_bit_mul_7_sum,
       n1_bit_mul_8_carry, n1_bit_mul_8_sum, n1_bit_mul_9_carry, n1_bit_mul_9_sum, n1_bit_mul_10_carry,
       n1_bit_mul_10_sum, n1_bit_mul_11_carry, n1_bit_mul_11_sum, n1_bit_mul_12_carry, n1_bit_mul_12_sum,
       n1_bit_mul_13_carry, n1_bit_mul_13_sum, n1_bit_mul_14_carry, n1_bit_mul_15_carry, n1_bit_mul_16_carry,
       n1_bit_mul_16_sum, n1_bit_mul_17_carry, n1_bit_mul_17_sum, n1_bit_mul_18_carry, n1_bit_mul_18_sum,
       n1_bit_mul_19_carry, n1_bit_mul_19_sum, n1_bit_mul_20_carry, n1_bit_mul_20_sum, n1_bit_mul_21_carry,
       n1_bit_mul_22_carry, n1_bit_mul_22_sum, n1_bit_mul_23_carry, n1_bit_mul_23_sum, n1_bit_mul_24_carry,
       n1_bit_mul_24_sum, n1_bit_mul_25_carry, n1_bit_mul_25_sum, n1_bit_mul_26_carry, n1_bit_mul_26_sum,
       n1_bit_mul_27_carry, n1_bit_mul_27_sum, n1_bit_mul_28_carry, n1_bit_mul_28_sum, n1_bit_mul_29_carry,
       n1_bit_mul_29_sum, n1_bit_mul_30_carry, n1_bit_mul_31_carry, n1_bit_mul_31_sum, n1_bit_mul_32_carry,
       n1_bit_mul_32_sum, n1_bit_mul_33_carry, n1_bit_mul_33_sum, n1_bit_mul_34_carry, n1_bit_mul_34_sum,
       n1_bit_mul_35_carry, n1_bit_mul_35_sum, n1_bit_mul_36_carry, n1_bit_mul_36_sum, n1_bit_mul_37_carry,
       n1_bit_mul_37_sum, n1_bit_mul_38_carry, n1_bit_mul_38_sum, n1_bit_mul_39_carry, n1_bit_mul_39_sum,
       n1_bit_mul_40_carry, n1_bit_mul_40_sum, n1_bit_mul_41_carry, n1_bit_mul_41_sum, n1_bit_mul_42_carry,
       n1_bit_mul_42_sum, n1_bit_mul_43_carry, n1_bit_mul_43_sum, n1_bit_mul_44_carry, n1_bit_mul_45_carry,
       n1_bit_mul_46_carry, n1_bit_mul_46_sum, n1_bit_mul_47_carry, n1_bit_mul_47_sum, n1_bit_mul_48_carry,
       n1_bit_mul_48_sum, n1_bit_mul_49_carry, n1_bit_mul_49_sum, n1_bit_mul_50_carry, n1_bit_mul_50_sum,
       n1_bit_mul_51_carry, n1_bit_mul_51_sum, n1_bit_mul_52_carry, n1_bit_mul_52_sum, n1_bit_mul_53_carry,
       n1_bit_mul_53_sum, n1_bit_mul_54_carry, n1_bit_mul_54_sum, n1_bit_mul_55_carry, n1_bit_mul_55_sum,
       n1_bit_mul_56_carry, n1_bit_mul_56_sum, n1_bit_mul_57_carry, n1_bit_mul_57_sum, n1_bit_mul_58_carry,
       n1_bit_mul_59_carry, n1_bit_mul_59_sum, n1_bit_mul_60_carry, n1_bit_mul_60_sum, n1_bit_mul_61_carry,
       n1_bit_mul_61_sum, n1_bit_mul_62_carry, n1_bit_mul_62_sum, n1_bit_mul_63_carry, n1_bit_mul_63_sum,
       n1_bit_mul_64_carry, n1_bit_mul_64_sum, n1_bit_mul_65_carry, n1_bit_mul_65_sum, n1_bit_mul_66_carry,
       n1_bit_mul_66_sum, n1_bit_mul_67_carry, n1_bit_mul_67_sum, n1_bit_mul_68_carry, n1_bit_mul_68_sum,
       n1_bit_mul_69_carry, n1_bit_mul_69_sum, n1_bit_mul_70_carry, n1_bit_mul_70_sum, n1_bit_mul_71_carry,
       n1_bit_mul_71_sum, n1_bit_mul_72_carry, n1_bit_mul_72_sum, n1_bit_mul_73_carry, n1_bit_mul_74_carry,
       n1_bit_mul_74_sum, n1_bit_mul_75_carry, n1_bit_mul_75_sum, n1_bit_mul_76_carry, n1_bit_mul_76_sum,
       n1_bit_mul_77_carry, n1_bit_mul_77_sum, n1_bit_mul_78_carry, n1_bit_mul_78_sum, n1_bit_mul_79_carry,
       n1_bit_mul_79_sum, n1_bit_mul_80_carry, n1_bit_mul_80_sum, n1_bit_mul_81_carry, n1_bit_mul_81_sum,
       n1_bit_mul_82_carry, n1_bit_mul_82_sum, n1_bit_mul_83_carry, n1_bit_mul_83_sum, n1_bit_mul_84_carry,
       n1_bit_mul_84_sum, n1_bit_mul_85_carry, n1_bit_mul_85_sum, n1_bit_mul_86_carry, n1_bit_mul_86_sum,
       n1_bit_mul_87_carry, n1_bit_mul_87_sum, n1_bit_mul_88_carry, n1_bit_mul_88_sum, n1_bit_mul_89_carry,
       n1_bit_mul_89_sum, n1_bit_mul_90_carry, n1_bit_mul_91_carry, n1_bit_mul_92_carry, n1_bit_mul_92_sum,
       n1_bit_mul_93_carry, n1_bit_mul_93_sum, n1_bit_mul_94_carry, n1_bit_mul_94_sum, n1_bit_mul_95_carry,
       n1_bit_mul_95_sum, n1_bit_mul_96_carry, n1_bit_mul_96_sum, n1_bit_mul_97_carry, n1_bit_mul_97_sum,
       n1_bit_mul_98_carry, n1_bit_mul_98_sum, n1_bit_mul_99_carry, n1_bit_mul_99_sum, n1_bit_mul_100_carry,
       n1_bit_mul_100_sum, n1_bit_mul_101_carry, n1_bit_mul_101_sum, n1_bit_mul_102_carry,
       n1_bit_mul_102_sum, n1_bit_mul_103_carry, n1_bit_mul_103_sum, n1_bit_mul_104_carry,
       n1_bit_mul_104_sum, n1_bit_mul_105_carry, n1_bit_mul_105_sum, n1_bit_mul_106_carry,
       n1_bit_mul_106_sum, n1_bit_mul_107_carry, n1_bit_mul_107_sum, n1_bit_mul_108_carry,
       n1_bit_mul_108_sum, n1_bit_mul_109_carry, n1_bit_mul_109_sum, n1_bit_mul_110_carry,
       n1_bit_mul_110_sum, n1_bit_mul_111_carry, n1_bit_mul_111_sum, n1_bit_mul_112_carry,
       n1_bit_mul_113_carry, n1_bit_mul_113_sum, n1_bit_mul_114_carry, n1_bit_mul_114_sum,
       n1_bit_mul_115_carry, n1_bit_mul_115_sum, n1_bit_mul_116_carry, n1_bit_mul_116_sum,
       n1_bit_mul_117_carry, n1_bit_mul_117_sum, n1_bit_mul_118_carry, n1_bit_mul_118_sum,
       n1_bit_mul_119_carry, n1_bit_mul_119_sum, n1_bit_mul_120_carry, n1_bit_mul_120_sum,
       n1_bit_mul_121_carry, n1_bit_mul_121_sum, n1_bit_mul_122_carry, n1_bit_mul_122_sum,
       n1_bit_mul_123_carry, n1_bit_mul_123_sum, n1_bit_mul_124_carry, n1_bit_mul_124_sum,
       n1_bit_mul_125_carry, n1_bit_mul_125_sum, n1_bit_mul_126_carry, n1_bit_mul_126_sum,
       n1_bit_mul_127_carry, n1_bit_mul_127_sum, n1_bit_mul_128_carry, n1_bit_mul_128_sum,
       n1_bit_mul_129_carry, n1_bit_mul_129_sum, n1_bit_mul_130_carry, n1_bit_mul_130_sum,
       n1_bit_mul_131_carry, n1_bit_mul_131_sum, n1_bit_mul_132_carry, n1_bit_mul_132_sum,
       n1_bit_mul_133_carry, n1_bit_mul_134_carry, n1_bit_mul_134_sum, n1_bit_mul_135_carry,
       n1_bit_mul_135_sum, n1_bit_mul_136_carry, n1_bit_mul_136_sum, n1_bit_mul_137_carry,
       n1_bit_mul_137_sum, n1_bit_mul_138_carry, n1_bit_mul_138_sum, n1_bit_mul_139_carry,
       n1_bit_mul_139_sum, n1_bit_mul_140_carry, n1_bit_mul_140_sum, n1_bit_mul_141_carry,
       n1_bit_mul_141_sum, n1_bit_mul_142_carry, n1_bit_mul_142_sum, n1_bit_mul_143_carry,
       n1_bit_mul_143_sum, n1_bit_mul_144_carry, n1_bit_mul_144_sum, n1_bit_mul_145_carry,
       n1_bit_mul_145_sum, n1_bit_mul_146_carry, n1_bit_mul_146_sum, n1_bit_mul_147_carry,
       n1_bit_mul_147_sum, n1_bit_mul_148_carry, n1_bit_mul_148_sum, n1_bit_mul_149_carry,
       n1_bit_mul_149_sum, n1_bit_mul_150_carry, n1_bit_mul_150_sum, n1_bit_mul_151_carry,
       n1_bit_mul_151_sum, n1_bit_mul_152_carry, n1_bit_mul_153_carry, n1_bit_mul_154_carry,
       n1_bit_mul_154_sum, n1_bit_mul_155_carry, n1_bit_mul_155_sum, n1_bit_mul_156_carry,
       n1_bit_mul_156_sum, n1_bit_mul_157_carry, n1_bit_mul_157_sum, n1_bit_mul_158_carry,
       n1_bit_mul_158_sum, n1_bit_mul_159_carry, n1_bit_mul_159_sum, n1_bit_mul_160_carry,
       n1_bit_mul_160_sum, n1_bit_mul_161_carry, n1_bit_mul_161_sum, n1_bit_mul_162_carry,
       n1_bit_mul_162_sum, n1_bit_mul_163_carry, n1_bit_mul_163_sum, n1_bit_mul_164_carry,
       n1_bit_mul_164_sum, n1_bit_mul_165_carry, n1_bit_mul_165_sum, n1_bit_mul_166_carry,
       n1_bit_mul_166_sum, n1_bit_mul_167_carry, n1_bit_mul_167_sum, n1_bit_mul_168_carry,
       n1_bit_mul_168_sum, n1_bit_mul_169_carry, n1_bit_mul_169_sum, n1_bit_mul_170_carry,
       n1_bit_mul_170_sum, n1_bit_mul_171_carry, n1_bit_mul_171_sum, n1_bit_mul_172_carry,
       n1_bit_mul_172_sum, n1_bit_mul_173_carry, n1_bit_mul_173_sum, n1_bit_mul_174_carry,
       n1_bit_mul_174_sum, n1_bit_mul_175_carry, n1_bit_mul_175_sum, n1_bit_mul_176_carry,
       n1_bit_mul_176_sum, n1_bit_mul_177_carry, n1_bit_mul_177_sum, n1_bit_mul_178_carry,
       n1_bit_mul_178_sum, n1_bit_mul_179_carry, n1_bit_mul_179_sum, n1_bit_mul_180_carry,
       n1_bit_mul_180_sum, n1_bit_mul_181_carry, n1_bit_mul_181_sum, n1_bit_mul_182_carry,
       n1_bit_mul_183_carry, n1_bit_mul_183_sum, n1_bit_mul_184_carry, n1_bit_mul_184_sum,
       n1_bit_mul_185_carry, n1_bit_mul_185_sum, n1_bit_mul_186_carry, n1_bit_mul_186_sum,
       n1_bit_mul_187_carry, n1_bit_mul_187_sum, n1_bit_mul_188_carry, n1_bit_mul_188_sum,
       n1_bit_mul_189_carry, n1_bit_mul_189_sum, n1_bit_mul_190_carry, n1_bit_mul_190_sum,
       n1_bit_mul_191_carry, n1_bit_mul_191_sum, n1_bit_mul_192_carry, n1_bit_mul_192_sum,
       n1_bit_mul_193_carry, n1_bit_mul_193_sum, n1_bit_mul_194_carry, n1_bit_mul_194_sum,
       n1_bit_mul_195_carry, n1_bit_mul_195_sum, n1_bit_mul_196_carry, n1_bit_mul_196_sum,
       n1_bit_mul_197_carry, n1_bit_mul_197_sum, n1_bit_mul_198_carry, n1_bit_mul_198_sum,
       n1_bit_mul_199_carry, n1_bit_mul_199_sum, n1_bit_mul_200_carry, n1_bit_mul_200_sum,
       n1_bit_mul_201_carry, n1_bit_mul_201_sum, n1_bit_mul_202_carry, n1_bit_mul_202_sum,
       n1_bit_mul_203_carry, n1_bit_mul_203_sum, n1_bit_mul_204_carry, n1_bit_mul_204_sum,
       n1_bit_mul_205_carry, n1_bit_mul_205_sum, n1_bit_mul_206_carry, n1_bit_mul_206_sum,
       n1_bit_mul_207_carry, n1_bit_mul_207_sum, n1_bit_mul_208_carry, n1_bit_mul_209_carry,
       n1_bit_mul_209_sum, n1_bit_mul_210_carry, n1_bit_mul_210_sum, n1_bit_mul_211_carry,
       n1_bit_mul_211_sum, n1_bit_mul_212_carry, n1_bit_mul_212_sum, n1_bit_mul_213_carry,
       n1_bit_mul_213_sum, n1_bit_mul_214_carry, n1_bit_mul_214_sum, n1_bit_mul_215_carry,
       n1_bit_mul_215_sum, n1_bit_mul_216_carry, n1_bit_mul_216_sum, n1_bit_mul_217_carry,
       n1_bit_mul_217_sum, n1_bit_mul_218_carry, n1_bit_mul_218_sum, n1_bit_mul_219_carry,
       n1_bit_mul_219_sum, n1_bit_mul_220_carry, n1_bit_mul_220_sum, n1_bit_mul_221_carry,
       n1_bit_mul_221_sum, n1_bit_mul_222_carry, n1_bit_mul_222_sum, n1_bit_mul_223_carry,
       n1_bit_mul_223_sum, n1_bit_mul_224_carry, n1_bit_mul_224_sum, n1_bit_mul_225_carry,
       n1_bit_mul_225_sum, n1_bit_mul_226_carry, n1_bit_mul_226_sum, n1_bit_mul_227_carry,
       n1_bit_mul_227_sum, n1_bit_mul_228_carry, n1_bit_mul_228_sum, n1_bit_mul_229_carry,
       n1_bit_mul_229_sum, n1_bit_mul_230_carry, n1_bit_mul_230_sum, n1_bit_mul_231_carry,
       n1_bit_mul_231_sum, n1_bit_mul_232_carry, n1_bit_mul_232_sum, n1_bit_mul_233_carry,
       n1_bit_mul_233_sum, n1_bit_mul_234_carry, n1_bit_mul_235_carry, n1_bit_mul_236_carry,
       n1_bit_mul_236_sum, n1_bit_mul_237_carry, n1_bit_mul_237_sum, n1_bit_mul_238_carry,
       n1_bit_mul_238_sum, n1_bit_mul_239_carry, n1_bit_mul_239_sum, n1_bit_mul_240_carry,
       n1_bit_mul_240_sum, n1_bit_mul_241_carry, n1_bit_mul_241_sum, n1_bit_mul_242_carry,
       n1_bit_mul_242_sum, n1_bit_mul_243_carry, n1_bit_mul_243_sum, n1_bit_mul_244_carry,
       n1_bit_mul_244_sum, n1_bit_mul_245_carry, n1_bit_mul_245_sum, n1_bit_mul_246_carry,
       n1_bit_mul_246_sum, n1_bit_mul_247_carry, n1_bit_mul_247_sum, n1_bit_mul_248_carry,
       n1_bit_mul_248_sum, n1_bit_mul_249_carry, n1_bit_mul_249_sum, n1_bit_mul_250_carry,
       n1_bit_mul_250_sum, n1_bit_mul_251_carry, n1_bit_mul_251_sum, n1_bit_mul_252_carry,
       n1_bit_mul_252_sum, n1_bit_mul_253_carry, n1_bit_mul_253_sum, n1_bit_mul_254_carry,
       n1_bit_mul_254_sum, n1_bit_mul_255_carry, n1_bit_mul_255_sum, n1_bit_mul_256_carry,
       n1_bit_mul_256_sum, n1_bit_mul_257_carry, n1_bit_mul_257_sum, n1_bit_mul_258_carry,
       n1_bit_mul_258_sum, n1_bit_mul_259_carry, n1_bit_mul_259_sum, n1_bit_mul_260_carry,
       n1_bit_mul_260_sum, n1_bit_mul_261_carry, n1_bit_mul_261_sum, n1_bit_mul_262_carry,
       n1_bit_mul_262_sum, n1_bit_mul_263_carry, n1_bit_mul_263_sum, n1_bit_mul_264_carry,
       n1_bit_mul_264_sum, n1_bit_mul_265_carry, n1_bit_mul_265_sum, n1_bit_mul_266_carry,
       n1_bit_mul_266_sum, n1_bit_mul_267_carry, n1_bit_mul_267_sum, n1_bit_mul_268_carry,
       n1_bit_mul_269_carry, n1_bit_mul_269_sum, n1_bit_mul_270_carry, n1_bit_mul_270_sum,
       n1_bit_mul_271_carry, n1_bit_mul_271_sum, n1_bit_mul_272_carry, n1_bit_mul_272_sum,
       n1_bit_mul_273_carry, n1_bit_mul_273_sum, n1_bit_mul_274_carry, n1_bit_mul_274_sum,
       n1_bit_mul_275_carry, n1_bit_mul_275_sum, n1_bit_mul_276_carry, n1_bit_mul_276_sum,
       n1_bit_mul_277_carry, n1_bit_mul_277_sum, n1_bit_mul_278_carry, n1_bit_mul_278_sum,
       n1_bit_mul_279_carry, n1_bit_mul_279_sum, n1_bit_mul_280_carry, n1_bit_mul_280_sum,
       n1_bit_mul_281_carry, n1_bit_mul_281_sum, n1_bit_mul_282_carry, n1_bit_mul_282_sum,
       n1_bit_mul_283_carry, n1_bit_mul_283_sum, n1_bit_mul_284_carry, n1_bit_mul_284_sum,
       n1_bit_mul_285_carry, n1_bit_mul_285_sum, n1_bit_mul_286_carry, n1_bit_mul_286_sum,
       n1_bit_mul_287_carry, n1_bit_mul_287_sum, n1_bit_mul_288_carry, n1_bit_mul_288_sum,
       n1_bit_mul_289_carry, n1_bit_mul_289_sum, n1_bit_mul_290_carry, n1_bit_mul_290_sum,
       n1_bit_mul_291_carry, n1_bit_mul_291_sum, n1_bit_mul_292_carry, n1_bit_mul_292_sum,
       n1_bit_mul_293_carry, n1_bit_mul_293_sum, n1_bit_mul_294_carry, n1_bit_mul_294_sum,
       n1_bit_mul_295_carry, n1_bit_mul_295_sum, n1_bit_mul_296_carry, n1_bit_mul_296_sum,
       n1_bit_mul_297_carry, n1_bit_mul_297_sum, n1_bit_mul_298_carry, n1_bit_mul_298_sum,
       n1_bit_mul_299_carry, n1_bit_mul_299_sum, n1_bit_mul_300_carry, n1_bit_mul_300_sum,
       n1_bit_mul_301_carry, n1_bit_mul_302_carry, n1_bit_mul_302_sum, n1_bit_mul_303_carry,
       n1_bit_mul_303_sum, n1_bit_mul_304_carry, n1_bit_mul_304_sum, n1_bit_mul_305_carry,
       n1_bit_mul_305_sum, n1_bit_mul_306_carry, n1_bit_mul_306_sum, n1_bit_mul_307_carry,
       n1_bit_mul_307_sum, n1_bit_mul_308_carry, n1_bit_mul_308_sum, n1_bit_mul_309_carry,
       n1_bit_mul_309_sum, n1_bit_mul_310_carry, n1_bit_mul_310_sum, n1_bit_mul_311_carry,
       n1_bit_mul_311_sum, n1_bit_mul_312_carry, n1_bit_mul_312_sum, n1_bit_mul_313_carry,
       n1_bit_mul_313_sum, n1_bit_mul_314_carry, n1_bit_mul_314_sum, n1_bit_mul_315_carry,
       n1_bit_mul_315_sum, n1_bit_mul_316_carry, n1_bit_mul_316_sum, n1_bit_mul_317_carry,
       n1_bit_mul_317_sum, n1_bit_mul_318_carry, n1_bit_mul_318_sum, n1_bit_mul_319_carry,
       n1_bit_mul_319_sum, n1_bit_mul_320_carry, n1_bit_mul_320_sum, n1_bit_mul_321_carry,
       n1_bit_mul_321_sum, n1_bit_mul_322_carry, n1_bit_mul_322_sum, n1_bit_mul_323_carry,
       n1_bit_mul_323_sum, n1_bit_mul_324_carry, n1_bit_mul_324_sum, n1_bit_mul_325_carry,
       n1_bit_mul_325_sum, n1_bit_mul_326_carry, n1_bit_mul_326_sum, n1_bit_mul_327_carry,
       n1_bit_mul_327_sum, n1_bit_mul_328_carry, n1_bit_mul_328_sum, n1_bit_mul_329_carry,
       n1_bit_mul_329_sum, n1_bit_mul_330_carry, n1_bit_mul_331_carry, n1_bit_mul_331_sum,
       n1_bit_mul_332_carry, n1_bit_mul_333_carry, n1_bit_mul_333_sum, n1_bit_mul_334_carry,
       n1_bit_mul_334_sum, n1_bit_mul_335_carry, n1_bit_mul_335_sum, n1_bit_mul_336_carry,
       n1_bit_mul_336_sum, n1_bit_mul_337_carry, n1_bit_mul_337_sum, n1_bit_mul_338_carry,
       n1_bit_mul_338_sum, n1_bit_mul_339_carry, n1_bit_mul_339_sum, n1_bit_mul_340_carry,
       n1_bit_mul_340_sum, n1_bit_mul_341_carry, n1_bit_mul_341_sum, n1_bit_mul_342_carry,
       n1_bit_mul_342_sum, n1_bit_mul_343_carry, n1_bit_mul_343_sum, n1_bit_mul_344_carry,
       n1_bit_mul_344_sum, n1_bit_mul_345_carry, n1_bit_mul_345_sum, n1_bit_mul_346_carry,
       n1_bit_mul_346_sum, n1_bit_mul_347_carry, n1_bit_mul_347_sum, n1_bit_mul_348_carry,
       n1_bit_mul_348_sum, n1_bit_mul_349_carry, n1_bit_mul_349_sum, n1_bit_mul_350_carry,
       n1_bit_mul_350_sum, n1_bit_mul_351_carry, n1_bit_mul_351_sum, n1_bit_mul_352_carry,
       n1_bit_mul_352_sum, n1_bit_mul_353_carry, n1_bit_mul_353_sum, n1_bit_mul_354_carry,
       n1_bit_mul_354_sum, n1_bit_mul_355_carry, n1_bit_mul_355_sum, n1_bit_mul_356_carry,
       n1_bit_mul_356_sum, n1_bit_mul_357_carry, n1_bit_mul_357_sum, n1_bit_mul_358_carry,
       n1_bit_mul_358_sum, n1_bit_mul_359_carry, n1_bit_mul_359_sum, n1_bit_mul_360_carry,
       n1_bit_mul_360_sum, n1_bit_mul_361_carry, n1_bit_mul_362_carry, n1_bit_mul_362_sum,
       n1_bit_mul_363_carry, n1_bit_mul_363_sum, n1_bit_mul_364_carry, n1_bit_mul_364_sum,
       n1_bit_mul_365_carry, n1_bit_mul_365_sum, n1_bit_mul_366_carry, n1_bit_mul_366_sum,
       n1_bit_mul_367_carry, n1_bit_mul_367_sum, n1_bit_mul_368_carry, n1_bit_mul_368_sum,
       n1_bit_mul_369_carry, n1_bit_mul_369_sum, n1_bit_mul_370_carry, n1_bit_mul_370_sum,
       n1_bit_mul_371_carry, n1_bit_mul_371_sum, n1_bit_mul_372_carry, n1_bit_mul_372_sum,
       n1_bit_mul_373_carry, n1_bit_mul_373_sum, n1_bit_mul_374_carry, n1_bit_mul_374_sum,
       n1_bit_mul_375_carry, n1_bit_mul_375_sum, n1_bit_mul_376_carry, n1_bit_mul_376_sum,
       n1_bit_mul_377_carry, n1_bit_mul_377_sum, n1_bit_mul_378_carry, n1_bit_mul_378_sum,
       n1_bit_mul_379_carry, n1_bit_mul_379_sum, n1_bit_mul_380_carry, n1_bit_mul_380_sum,
       n1_bit_mul_381_carry, n1_bit_mul_381_sum, n1_bit_mul_382_carry, n1_bit_mul_382_sum,
       n1_bit_mul_383_carry, n1_bit_mul_383_sum, n1_bit_mul_384_carry, n1_bit_mul_384_sum,
       n1_bit_mul_385_carry, n1_bit_mul_385_sum, n1_bit_mul_386_carry, n1_bit_mul_386_sum,
       n1_bit_mul_387_carry, n1_bit_mul_387_sum, n1_bit_mul_388_carry, n1_bit_mul_388_sum,
       n1_bit_mul_389_carry, n1_bit_mul_390_carry, n1_bit_mul_391_carry, n1_bit_mul_391_sum,
       n1_bit_mul_392_carry, n1_bit_mul_392_sum, n1_bit_mul_393_carry, n1_bit_mul_393_sum,
       n1_bit_mul_394_carry, n1_bit_mul_394_sum, n1_bit_mul_395_carry, n1_bit_mul_395_sum,
       n1_bit_mul_396_carry, n1_bit_mul_396_sum, n1_bit_mul_397_carry, n1_bit_mul_397_sum,
       n1_bit_mul_398_carry, n1_bit_mul_398_sum, n1_bit_mul_399_carry, n1_bit_mul_399_sum,
       n1_bit_mul_400_carry, n1_bit_mul_400_sum, n1_bit_mul_401_carry, n1_bit_mul_401_sum,
       n1_bit_mul_402_carry, n1_bit_mul_402_sum, n1_bit_mul_403_carry, n1_bit_mul_403_sum,
       n1_bit_mul_404_carry, n1_bit_mul_404_sum, n1_bit_mul_405_carry, n1_bit_mul_405_sum,
       n1_bit_mul_406_carry, n1_bit_mul_406_sum, n1_bit_mul_407_carry, n1_bit_mul_407_sum,
       n1_bit_mul_408_carry, n1_bit_mul_408_sum, n1_bit_mul_409_carry, n1_bit_mul_409_sum,
       n1_bit_mul_410_carry, n1_bit_mul_410_sum, n1_bit_mul_411_carry, n1_bit_mul_411_sum,
       n1_bit_mul_412_carry, n1_bit_mul_412_sum, n1_bit_mul_413_carry, n1_bit_mul_413_sum,
       n1_bit_mul_414_carry, n1_bit_mul_415_carry, n1_bit_mul_415_sum, n1_bit_mul_416_carry,
       n1_bit_mul_416_sum, n1_bit_mul_417_carry, n1_bit_mul_417_sum, n1_bit_mul_418_carry,
       n1_bit_mul_418_sum, n1_bit_mul_419_carry, n1_bit_mul_419_sum, n1_bit_mul_420_carry,
       n1_bit_mul_420_sum, n1_bit_mul_421_carry, n1_bit_mul_421_sum, n1_bit_mul_422_carry,
       n1_bit_mul_422_sum, n1_bit_mul_423_carry, n1_bit_mul_423_sum, n1_bit_mul_424_carry,
       n1_bit_mul_424_sum, n1_bit_mul_425_carry, n1_bit_mul_425_sum, n1_bit_mul_426_carry,
       n1_bit_mul_426_sum, n1_bit_mul_427_carry, n1_bit_mul_427_sum, n1_bit_mul_428_carry,
       n1_bit_mul_428_sum, n1_bit_mul_429_carry, n1_bit_mul_429_sum, n1_bit_mul_430_carry,
       n1_bit_mul_430_sum, n1_bit_mul_431_carry, n1_bit_mul_431_sum, n1_bit_mul_432_carry,
       n1_bit_mul_432_sum, n1_bit_mul_433_carry, n1_bit_mul_433_sum, n1_bit_mul_434_carry,
       n1_bit_mul_434_sum, n1_bit_mul_435_carry, n1_bit_mul_435_sum, n1_bit_mul_436_carry,
       n1_bit_mul_436_sum, n1_bit_mul_437_carry, n1_bit_mul_437_sum, n1_bit_mul_438_carry,
       n1_bit_mul_438_sum, n1_bit_mul_439_carry, n1_bit_mul_440_carry, n1_bit_mul_440_sum,
       n1_bit_mul_441_carry, n1_bit_mul_441_sum, n1_bit_mul_442_carry, n1_bit_mul_442_sum,
       n1_bit_mul_443_carry, n1_bit_mul_443_sum, n1_bit_mul_444_carry, n1_bit_mul_444_sum,
       n1_bit_mul_445_carry, n1_bit_mul_445_sum, n1_bit_mul_446_carry, n1_bit_mul_446_sum,
       n1_bit_mul_447_carry, n1_bit_mul_447_sum, n1_bit_mul_448_carry, n1_bit_mul_448_sum,
       n1_bit_mul_449_carry, n1_bit_mul_449_sum, n1_bit_mul_450_carry, n1_bit_mul_450_sum,
       n1_bit_mul_451_carry, n1_bit_mul_451_sum, n1_bit_mul_452_carry, n1_bit_mul_452_sum,
       n1_bit_mul_453_carry, n1_bit_mul_453_sum, n1_bit_mul_454_carry, n1_bit_mul_454_sum,
       n1_bit_mul_455_carry, n1_bit_mul_455_sum, n1_bit_mul_456_carry, n1_bit_mul_456_sum,
       n1_bit_mul_457_carry, n1_bit_mul_457_sum, n1_bit_mul_458_carry, n1_bit_mul_458_sum,
       n1_bit_mul_459_carry, n1_bit_mul_460_carry, n1_bit_mul_461_carry, n1_bit_mul_461_sum,
       n1_bit_mul_462_carry, n1_bit_mul_462_sum, n1_bit_mul_463_carry, n1_bit_mul_463_sum,
       n1_bit_mul_464_carry, n1_bit_mul_464_sum, n1_bit_mul_465_carry, n1_bit_mul_465_sum,
       n1_bit_mul_466_carry, n1_bit_mul_466_sum, n1_bit_mul_467_carry, n1_bit_mul_467_sum,
       n1_bit_mul_468_carry, n1_bit_mul_468_sum, n1_bit_mul_469_carry, n1_bit_mul_469_sum,
       n1_bit_mul_470_carry, n1_bit_mul_470_sum, n1_bit_mul_471_carry, n1_bit_mul_471_sum,
       n1_bit_mul_472_carry, n1_bit_mul_472_sum, n1_bit_mul_473_carry, n1_bit_mul_473_sum,
       n1_bit_mul_474_carry, n1_bit_mul_474_sum, n1_bit_mul_475_carry, n1_bit_mul_475_sum,
       n1_bit_mul_476_carry, n1_bit_mul_476_sum, n1_bit_mul_477_carry, n1_bit_mul_477_sum,
       n1_bit_mul_478_carry, n1_bit_mul_478_sum, n1_bit_mul_479_carry, n1_bit_mul_479_sum,
       n1_bit_mul_480_carry, n1_bit_mul_481_carry, n1_bit_mul_481_sum, n1_bit_mul_482_carry,
       n1_bit_mul_482_sum, n1_bit_mul_483_carry, n1_bit_mul_483_sum, n1_bit_mul_484_carry,
       n1_bit_mul_484_sum, n1_bit_mul_485_carry, n1_bit_mul_485_sum, n1_bit_mul_486_carry,
       n1_bit_mul_486_sum, n1_bit_mul_487_carry, n1_bit_mul_487_sum, n1_bit_mul_488_carry,
       n1_bit_mul_488_sum, n1_bit_mul_489_carry, n1_bit_mul_489_sum, n1_bit_mul_490_carry,
       n1_bit_mul_490_sum, n1_bit_mul_491_carry, n1_bit_mul_491_sum, n1_bit_mul_492_carry,
       n1_bit_mul_492_sum, n1_bit_mul_493_carry, n1_bit_mul_493_sum, n1_bit_mul_494_carry,
       n1_bit_mul_494_sum, n1_bit_mul_495_carry, n1_bit_mul_495_sum, n1_bit_mul_496_carry,
       n1_bit_mul_497_carry, n1_bit_mul_497_sum, n1_bit_mul_498_carry, n1_bit_mul_499_carry,
       n1_bit_mul_499_sum, n1_bit_mul_500_carry, n1_bit_mul_500_sum, n1_bit_mul_501_carry,
       n1_bit_mul_501_sum, n1_bit_mul_502_carry, n1_bit_mul_502_sum, n1_bit_mul_503_carry,
       n1_bit_mul_503_sum, n1_bit_mul_504_carry, n1_bit_mul_504_sum, n1_bit_mul_505_carry,
       n1_bit_mul_505_sum, n1_bit_mul_506_carry, n1_bit_mul_506_sum, n1_bit_mul_507_carry,
       n1_bit_mul_507_sum, n1_bit_mul_508_carry, n1_bit_mul_508_sum, n1_bit_mul_509_carry,
       n1_bit_mul_509_sum, n1_bit_mul_510_carry, n1_bit_mul_510_sum, n1_bit_mul_511_carry,
       n1_bit_mul_511_sum, n1_bit_mul_512_carry, n1_bit_mul_512_sum, n1_bit_mul_513_carry,
       n1_bit_mul_513_sum, n1_bit_mul_514_carry, n1_bit_mul_515_carry, n1_bit_mul_515_sum,
       n1_bit_mul_516_carry, n1_bit_mul_516_sum, n1_bit_mul_517_carry, n1_bit_mul_517_sum,
       n1_bit_mul_518_carry, n1_bit_mul_518_sum, n1_bit_mul_519_carry, n1_bit_mul_519_sum,
       n1_bit_mul_520_carry, n1_bit_mul_520_sum, n1_bit_mul_521_carry, n1_bit_mul_521_sum,
       n1_bit_mul_522_carry, n1_bit_mul_522_sum, n1_bit_mul_523_carry, n1_bit_mul_523_sum,
       n1_bit_mul_524_carry, n1_bit_mul_524_sum, n1_bit_mul_525_carry, n1_bit_mul_525_sum,
       n1_bit_mul_526_carry, n1_bit_mul_526_sum, n1_bit_mul_527_carry, n1_bit_mul_527_sum,
       n1_bit_mul_528_carry, n1_bit_mul_528_sum, n1_bit_mul_529_carry, n1_bit_mul_529_sum,
       n1_bit_mul_530_carry, n1_bit_mul_531_carry, n1_bit_mul_531_sum, n1_bit_mul_532_carry,
       n1_bit_mul_532_sum, n1_bit_mul_533_carry, n1_bit_mul_533_sum, n1_bit_mul_534_carry,
       n1_bit_mul_534_sum, n1_bit_mul_535_carry, n1_bit_mul_535_sum, n1_bit_mul_536_carry,
       n1_bit_mul_536_sum, n1_bit_mul_537_carry, n1_bit_mul_537_sum, n1_bit_mul_538_carry,
       n1_bit_mul_538_sum, n1_bit_mul_539_carry, n1_bit_mul_540_carry, n1_bit_mul_541_carry,
       n1_bit_mul_541_sum, n1_bit_mul_542_carry, n1_bit_mul_542_sum, n1_bit_mul_543_carry,
       n1_bit_mul_543_sum, n1_bit_mul_544_carry, n1_bit_mul_544_sum, n1_bit_mul_545_carry,
       n1_bit_mul_545_sum, n1_bit_mul_546_carry, n1_bit_mul_546_sum, n1_bit_mul_547_carry,
       n1_bit_mul_547_sum, n1_bit_mul_548_carry, n1_bit_mul_548_sum, n1_bit_mul_549_carry,
       n1_bit_mul_549_sum, n1_bit_mul_550_carry, n1_bit_mul_550_sum, n1_bit_mul_551_carry,
       n1_bit_mul_551_sum, n1_bit_mul_552_carry, n1_bit_mul_553_carry, n1_bit_mul_553_sum,
       n1_bit_mul_554_carry, n1_bit_mul_554_sum, n1_bit_mul_555_carry, n1_bit_mul_555_sum,
       n1_bit_mul_556_carry, n1_bit_mul_556_sum, n1_bit_mul_557_carry, n1_bit_mul_557_sum,
       n1_bit_mul_558_carry, n1_bit_mul_558_sum, n1_bit_mul_559_carry, n1_bit_mul_559_sum,
       n1_bit_mul_560_carry, n1_bit_mul_561_carry, n1_bit_mul_562_carry, n1_bit_mul_562_sum,
       n1_bit_mul_563_carry, n1_bit_mul_563_sum, n1_bit_mul_564_carry, n1_bit_mul_564_sum,
       n1_bit_mul_565_carry, n1_bit_mul_565_sum, n1_bit_mul_566_carry, n1_bit_mul_567_carry,
       n1_bit_mul_567_sum, n1_bit_mul_568_carry, n1_bit_mul_568_sum, n1_bit_mul_569_carry,
       n1_bit_mul_569_sum, n1_bit_mul_570_carry, n1_bit_mul_570_sum, n1_bit_mul_571_carry,
       n1_bit_mul_571_sum, n1_bit_mul_572_carry, n1_bit_mul_573_carry, n1_bit_mul_574_carry,
       n1_bit_mul_574_sum, n1_bit_mul_575_carry, n1_bit_mul_576_carry;

  _1_bit_MUL u_1_bit_mul_1 (
    .Carry_In(n1_bit_mul_3_carry), .Sum_In(n1_bit_mul_2_carry), .A(A[23]), .B(B[23]), .Sum(HI[22]),
    .Carry(HI[23]));
  _1_bit_MUL u_1_bit_mul_2 (
    .Carry_In(n1_bit_mul_5_carry), .Sum_In(n1_bit_mul_4_carry), .A(A[23]), .B(B[22]), .Sum(n1_bit_mul_2_sum),
    .Carry(n1_bit_mul_2_carry));
  _1_bit_MUL u_1_bit_mul_3 (
    .Carry_In(n1_bit_mul_6_carry), .Sum_In(n1_bit_mul_2_sum), .A(A[22]), .B(B[23]), .Sum(HI[21]),
    .Carry(n1_bit_mul_3_carry));
  _1_bit_MUL u_1_bit_mul_4 (
    .Carry_In(n1_bit_mul_11_carry), .Sum_In(n1_bit_mul_8_carry), .A(A[23]), .B(B[21]),
    .Sum(n1_bit_mul_4_sum), .Carry(n1_bit_mul_4_carry));
  _1_bit_MUL u_1_bit_mul_5 (
    .Carry_In(n1_bit_mul_12_carry), .Sum_In(n1_bit_mul_4_sum), .A(A[22]), .B(B[22]), .Sum(n1_bit_mul_5_sum),
    .Carry(n1_bit_mul_5_carry));
  _1_bit_MUL u_1_bit_mul_6 (
    .Carry_In(n1_bit_mul_14_carry), .Sum_In(n1_bit_mul_5_sum), .A(A[21]), .B(B[23]), .Sum(HI[20]),
    .Carry(n1_bit_mul_6_carry));
  _1_bit_MUL u_1_bit_mul_7 (
    .Carry_In(n1_bit_mul_17_carry), .Sum_In(n1_bit_mul_16_carry), .A(A[23]), .B(B[19]),
    .Sum(n1_bit_mul_7_sum), .Carry(n1_bit_mul_7_carry));
  _1_bit_MUL u_1_bit_mul_8 (
    .Carry_In(n1_bit_mul_9_carry), .Sum_In(n1_bit_mul_7_carry), .A(A[23]), .B(B[20]), .Sum(n1_bit_mul_8_sum),
    .Carry(n1_bit_mul_8_carry));
  _1_bit_MUL u_1_bit_mul_9 (
    .Carry_In(n1_bit_mul_18_carry), .Sum_In(n1_bit_mul_7_sum), .A(A[22]), .B(B[20]), .Sum(n1_bit_mul_9_sum),
    .Carry(n1_bit_mul_9_carry));
  _1_bit_MUL u_1_bit_mul_10 (
    .Carry_In(n1_bit_mul_19_carry), .Sum_In(n1_bit_mul_9_sum), .A(A[21]), .B(B[21]), .Sum(n1_bit_mul_10_sum),
    .Carry(n1_bit_mul_10_carry));
  _1_bit_MUL u_1_bit_mul_11 (
    .Carry_In(n1_bit_mul_10_carry), .Sum_In(n1_bit_mul_8_sum), .A(A[22]), .B(B[21]), .Sum(n1_bit_mul_11_sum),
    .Carry(n1_bit_mul_11_carry));
  _1_bit_MUL u_1_bit_mul_12 (
    .Carry_In(n1_bit_mul_13_carry), .Sum_In(n1_bit_mul_11_sum), .A(A[21]), .B(B[22]),
    .Sum(n1_bit_mul_12_sum), .Carry(n1_bit_mul_12_carry));
  _1_bit_MUL u_1_bit_mul_13 (
    .Carry_In(n1_bit_mul_20_carry), .Sum_In(n1_bit_mul_10_sum), .A(A[20]), .B(B[22]),
    .Sum(n1_bit_mul_13_sum), .Carry(n1_bit_mul_13_carry));
  _1_bit_MUL u_1_bit_mul_14 (
    .Carry_In(n1_bit_mul_15_carry), .Sum_In(n1_bit_mul_12_sum), .A(A[20]), .B(B[23]), .Sum(HI[19]),
    .Carry(n1_bit_mul_14_carry));
  _1_bit_MUL u_1_bit_mul_15 (
    .Carry_In(n1_bit_mul_21_carry), .Sum_In(n1_bit_mul_13_sum), .A(A[19]), .B(B[23]), .Sum(HI[18]),
    .Carry(n1_bit_mul_15_carry));
  _1_bit_MUL u_1_bit_mul_16 (
    .Carry_In(n1_bit_mul_25_carry), .Sum_In(n1_bit_mul_24_carry), .A(A[23]), .B(B[18]),
    .Sum(n1_bit_mul_16_sum), .Carry(n1_bit_mul_16_carry));
  _1_bit_MUL u_1_bit_mul_17 (
    .Carry_In(n1_bit_mul_26_carry), .Sum_In(n1_bit_mul_16_sum), .A(A[22]), .B(B[19]),
    .Sum(n1_bit_mul_17_sum), .Carry(n1_bit_mul_17_carry));
  _1_bit_MUL u_1_bit_mul_18 (
    .Carry_In(n1_bit_mul_27_carry), .Sum_In(n1_bit_mul_17_sum), .A(A[21]), .B(B[20]),
    .Sum(n1_bit_mul_18_sum), .Carry(n1_bit_mul_18_carry));
  _1_bit_MUL u_1_bit_mul_19 (
    .Carry_In(n1_bit_mul_28_carry), .Sum_In(n1_bit_mul_18_sum), .A(A[20]), .B(B[21]),
    .Sum(n1_bit_mul_19_sum), .Carry(n1_bit_mul_19_carry));
  _1_bit_MUL u_1_bit_mul_20 (
    .Carry_In(n1_bit_mul_29_carry), .Sum_In(n1_bit_mul_19_sum), .A(A[19]), .B(B[22]),
    .Sum(n1_bit_mul_20_sum), .Carry(n1_bit_mul_20_carry));
  _1_bit_MUL u_1_bit_mul_21 (
    .Carry_In(n1_bit_mul_30_carry), .Sum_In(n1_bit_mul_20_sum), .A(A[18]), .B(B[23]), .Sum(HI[17]),
    .Carry(n1_bit_mul_21_carry));
  _1_bit_MUL u_1_bit_mul_22 (
    .Carry_In(n1_bit_mul_32_carry), .Sum_In(n1_bit_mul_31_carry), .A(A[23]), .B(B[16]),
    .Sum(n1_bit_mul_22_sum), .Carry(n1_bit_mul_22_carry));
  _1_bit_MUL u_1_bit_mul_23 (
    .Carry_In(n1_bit_mul_33_carry), .Sum_In(n1_bit_mul_22_sum), .A(A[22]), .B(B[17]),
    .Sum(n1_bit_mul_23_sum), .Carry(n1_bit_mul_23_carry));
  _1_bit_MUL u_1_bit_mul_24 (
    .Carry_In(n1_bit_mul_23_carry), .Sum_In(n1_bit_mul_22_carry), .A(A[23]), .B(B[17]),
    .Sum(n1_bit_mul_24_sum), .Carry(n1_bit_mul_24_carry));
  _1_bit_MUL u_1_bit_mul_25 (
    .Carry_In(n1_bit_mul_35_carry), .Sum_In(n1_bit_mul_24_sum), .A(A[22]), .B(B[6]), .Sum(n1_bit_mul_25_sum),
    .Carry(n1_bit_mul_25_carry));
  _1_bit_MUL u_1_bit_mul_26 (
    .Carry_In(n1_bit_mul_37_carry), .Sum_In(n1_bit_mul_25_sum), .A(A[21]), .B(B[19]),
    .Sum(n1_bit_mul_26_sum), .Carry(n1_bit_mul_26_carry));
  _1_bit_MUL u_1_bit_mul_27 (
    .Carry_In(n1_bit_mul_38_carry), .Sum_In(n1_bit_mul_26_sum), .A(A[20]), .B(B[20]),
    .Sum(n1_bit_mul_27_sum), .Carry(n1_bit_mul_27_carry));
  _1_bit_MUL u_1_bit_mul_28 (
    .Carry_In(n1_bit_mul_40_carry), .Sum_In(n1_bit_mul_27_sum), .A(A[19]), .B(B[21]),
    .Sum(n1_bit_mul_28_sum), .Carry(n1_bit_mul_28_carry));
  _1_bit_MUL u_1_bit_mul_29 (
    .Carry_In(n1_bit_mul_43_carry), .Sum_In(n1_bit_mul_28_sum), .A(A[18]), .B(B[22]),
    .Sum(n1_bit_mul_29_sum), .Carry(n1_bit_mul_29_carry));
  _1_bit_MUL u_1_bit_mul_30 (
    .Carry_In(n1_bit_mul_45_carry), .Sum_In(n1_bit_mul_29_sum), .A(A[17]), .B(B[23]), .Sum(HI[16]),
    .Carry(n1_bit_mul_30_carry));
  _1_bit_MUL u_1_bit_mul_31 (
    .Carry_In(n1_bit_mul_49_carry), .Sum_In(n1_bit_mul_47_carry), .A(A[23]), .B(B[15]),
    .Sum(n1_bit_mul_31_sum), .Carry(n1_bit_mul_31_carry));
  _1_bit_MUL u_1_bit_mul_32 (
    .Carry_In(n1_bit_mul_51_carry), .Sum_In(n1_bit_mul_31_sum), .A(A[22]), .B(B[16]),
    .Sum(n1_bit_mul_32_sum), .Carry(n1_bit_mul_32_carry));
  _1_bit_MUL u_1_bit_mul_33 (
    .Carry_In(n1_bit_mul_52_carry), .Sum_In(n1_bit_mul_32_sum), .A(A[21]), .B(B[17]),
    .Sum(n1_bit_mul_33_sum), .Carry(n1_bit_mul_33_carry));
  _1_bit_MUL u_1_bit_mul_34 (
    .Carry_In(n1_bit_mul_53_carry), .Sum_In(n1_bit_mul_33_sum), .A(A[20]), .B(B[18]),
    .Sum(n1_bit_mul_34_sum), .Carry(n1_bit_mul_34_carry));
  _1_bit_MUL u_1_bit_mul_35 (
    .Carry_In(n1_bit_mul_34_carry), .Sum_In(n1_bit_mul_23_sum), .A(A[21]), .B(B[18]),
    .Sum(n1_bit_mul_35_sum), .Carry(n1_bit_mul_35_carry));
  _1_bit_MUL u_1_bit_mul_36 (
    .Carry_In(n1_bit_mul_54_carry), .Sum_In(n1_bit_mul_34_sum), .A(A[19]), .B(B[19]),
    .Sum(n1_bit_mul_36_sum), .Carry(n1_bit_mul_36_carry));
  _1_bit_MUL u_1_bit_mul_37 (
    .Carry_In(n1_bit_mul_36_carry), .Sum_In(n1_bit_mul_35_sum), .A(A[20]), .B(B[19]),
    .Sum(n1_bit_mul_37_sum), .Carry(n1_bit_mul_37_carry));
  _1_bit_MUL u_1_bit_mul_38 (
    .Carry_In(n1_bit_mul_39_carry), .Sum_In(n1_bit_mul_37_sum), .A(A[19]), .B(B[20]),
    .Sum(n1_bit_mul_38_sum), .Carry(n1_bit_mul_38_carry));
  _1_bit_MUL u_1_bit_mul_39 (
    .Carry_In(n1_bit_mul_55_carry), .Sum_In(n1_bit_mul_36_sum), .A(A[18]), .B(B[20]),
    .Sum(n1_bit_mul_39_sum), .Carry(n1_bit_mul_39_carry));
  _1_bit_MUL u_1_bit_mul_40 (
    .Carry_In(n1_bit_mul_41_carry), .Sum_In(n1_bit_mul_38_sum), .A(A[18]), .B(B[21]),
    .Sum(n1_bit_mul_40_sum), .Carry(n1_bit_mul_40_carry));
  _1_bit_MUL u_1_bit_mul_41 (
    .Carry_In(n1_bit_mul_56_carry), .Sum_In(n1_bit_mul_39_sum), .A(A[17]), .B(B[21]),
    .Sum(n1_bit_mul_41_sum), .Carry(n1_bit_mul_41_carry));
  _1_bit_MUL u_1_bit_mul_42 (
    .Carry_In(n1_bit_mul_57_carry), .Sum_In(n1_bit_mul_41_sum), .A(A[16]), .B(B[22]),
    .Sum(n1_bit_mul_42_sum), .Carry(n1_bit_mul_42_carry));
  _1_bit_MUL u_1_bit_mul_43 (
    .Carry_In(n1_bit_mul_42_carry), .Sum_In(n1_bit_mul_40_sum), .A(A[17]), .B(B[22]),
    .Sum(n1_bit_mul_43_sum), .Carry(n1_bit_mul_43_carry));
  _1_bit_MUL u_1_bit_mul_44 (
    .Carry_In(n1_bit_mul_58_carry), .Sum_In(n1_bit_mul_42_sum), .A(A[15]), .B(B[23]), .Sum(HI[14]),
    .Carry(n1_bit_mul_44_carry));
  _1_bit_MUL u_1_bit_mul_45 (
    .Carry_In(n1_bit_mul_44_carry), .Sum_In(n1_bit_mul_43_sum), .A(A[16]), .B(B[23]), .Sum(HI[15]),
    .Carry(n1_bit_mul_45_carry));
  _1_bit_MUL u_1_bit_mul_46 (
    .Carry_In(n1_bit_mul_60_carry), .Sum_In(n1_bit_mul_59_carry), .A(A[23]), .B(B[13]),
    .Sum(n1_bit_mul_46_sum), .Carry(n1_bit_mul_46_carry));
  _1_bit_MUL u_1_bit_mul_47 (
    .Carry_In(n1_bit_mul_48_carry), .Sum_In(n1_bit_mul_46_carry), .A(A[23]), .B(B[14]),
    .Sum(n1_bit_mul_47_sum), .Carry(n1_bit_mul_47_carry));
  _1_bit_MUL u_1_bit_mul_48 (
    .Carry_In(n1_bit_mul_61_carry), .Sum_In(n1_bit_mul_46_sum), .A(A[22]), .B(B[14]),
    .Sum(n1_bit_mul_48_sum), .Carry(n1_bit_mul_48_carry));
  _1_bit_MUL u_1_bit_mul_49 (
    .Carry_In(n1_bit_mul_50_carry), .Sum_In(n1_bit_mul_47_sum), .A(A[22]), .B(B[15]),
    .Sum(n1_bit_mul_49_sum), .Carry(n1_bit_mul_49_carry));
  _1_bit_MUL u_1_bit_mul_50 (
    .Carry_In(n1_bit_mul_62_carry), .Sum_In(n1_bit_mul_48_sum), .A(A[21]), .B(B[15]),
    .Sum(n1_bit_mul_50_sum), .Carry(n1_bit_mul_50_carry));
  _1_bit_MUL u_1_bit_mul_51 (
    .Carry_In(n1_bit_mul_64_carry), .Sum_In(n1_bit_mul_49_sum), .A(A[21]), .B(B[16]),
    .Sum(n1_bit_mul_51_sum), .Carry(n1_bit_mul_51_carry));
  _1_bit_MUL u_1_bit_mul_52 (
    .Carry_In(n1_bit_mul_66_carry), .Sum_In(n1_bit_mul_51_sum), .A(A[20]), .B(B[17]),
    .Sum(n1_bit_mul_52_sum), .Carry(n1_bit_mul_52_carry));
  _1_bit_MUL u_1_bit_mul_53 (
    .Carry_In(n1_bit_mul_67_carry), .Sum_In(n1_bit_mul_52_sum), .A(A[19]), .B(B[18]),
    .Sum(n1_bit_mul_53_sum), .Carry(n1_bit_mul_53_carry));
  _1_bit_MUL u_1_bit_mul_54 (
    .Carry_In(n1_bit_mul_68_carry), .Sum_In(n1_bit_mul_53_sum), .A(A[18]), .B(B[19]),
    .Sum(n1_bit_mul_54_sum), .Carry(n1_bit_mul_54_carry));
  _1_bit_MUL u_1_bit_mul_55 (
    .Carry_In(n1_bit_mul_69_carry), .Sum_In(n1_bit_mul_54_sum), .A(A[17]), .B(B[20]),
    .Sum(n1_bit_mul_55_sum), .Carry(n1_bit_mul_55_carry));
  _1_bit_MUL u_1_bit_mul_56 (
    .Carry_In(n1_bit_mul_71_carry), .Sum_In(n1_bit_mul_55_sum), .A(A[16]), .B(B[21]),
    .Sum(n1_bit_mul_56_sum), .Carry(n1_bit_mul_56_carry));
  _1_bit_MUL u_1_bit_mul_57 (
    .Carry_In(n1_bit_mul_72_carry), .Sum_In(n1_bit_mul_56_sum), .A(A[15]), .B(B[22]),
    .Sum(n1_bit_mul_57_sum), .Carry(n1_bit_mul_57_carry));
  _1_bit_MUL u_1_bit_mul_58 (
    .Carry_In(n1_bit_mul_73_carry), .Sum_In(n1_bit_mul_57_sum), .A(A[14]), .B(B[23]), .Sum(HI[13]),
    .Carry(n1_bit_mul_58_carry));
  _1_bit_MUL u_1_bit_mul_59 (
    .Carry_In(n1_bit_mul_75_carry), .Sum_In(n1_bit_mul_74_carry), .A(A[23]), .B(B[12]),
    .Sum(n1_bit_mul_59_sum), .Carry(n1_bit_mul_59_carry));
  _1_bit_MUL u_1_bit_mul_60 (
    .Carry_In(n1_bit_mul_76_carry), .Sum_In(n1_bit_mul_59_sum), .A(A[22]), .B(B[13]),
    .Sum(n1_bit_mul_60_sum), .Carry(n1_bit_mul_60_carry));
  _1_bit_MUL u_1_bit_mul_61 (
    .Carry_In(n1_bit_mul_77_carry), .Sum_In(n1_bit_mul_60_sum), .A(A[21]), .B(B[14]),
    .Sum(n1_bit_mul_61_sum), .Carry(n1_bit_mul_61_carry));
  _1_bit_MUL u_1_bit_mul_62 (
    .Carry_In(n1_bit_mul_78_carry), .Sum_In(n1_bit_mul_61_sum), .A(A[20]), .B(B[15]),
    .Sum(n1_bit_mul_62_sum), .Carry(n1_bit_mul_62_carry));
  _1_bit_MUL u_1_bit_mul_63 (
    .Carry_In(n1_bit_mul_79_carry), .Sum_In(n1_bit_mul_62_sum), .A(A[19]), .B(B[16]),
    .Sum(n1_bit_mul_63_sum), .Carry(n1_bit_mul_63_carry));
  _1_bit_MUL u_1_bit_mul_64 (
    .Carry_In(n1_bit_mul_63_carry), .Sum_In(n1_bit_mul_50_sum), .A(A[20]), .B(B[16]),
    .Sum(n1_bit_mul_64_sum), .Carry(n1_bit_mul_64_carry));
  _1_bit_MUL u_1_bit_mul_65 (
    .Carry_In(n1_bit_mul_80_carry), .Sum_In(n1_bit_mul_63_sum), .A(A[18]), .B(B[17]),
    .Sum(n1_bit_mul_65_sum), .Carry(n1_bit_mul_65_carry));
  _1_bit_MUL u_1_bit_mul_66 (
    .Carry_In(n1_bit_mul_65_carry), .Sum_In(n1_bit_mul_64_sum), .A(A[19]), .B(B[17]),
    .Sum(n1_bit_mul_66_sum), .Carry(n1_bit_mul_66_carry));
  _1_bit_MUL u_1_bit_mul_67 (
    .Carry_In(n1_bit_mul_81_carry), .Sum_In(n1_bit_mul_66_sum), .A(A[18]), .B(B[18]),
    .Sum(n1_bit_mul_67_sum), .Carry(n1_bit_mul_67_carry));
  _1_bit_MUL u_1_bit_mul_68 (
    .Carry_In(n1_bit_mul_84_carry), .Sum_In(n1_bit_mul_67_sum), .A(A[17]), .B(B[19]),
    .Sum(n1_bit_mul_68_sum), .Carry(n1_bit_mul_68_carry));
  _1_bit_MUL u_1_bit_mul_69 (
    .Carry_In(n1_bit_mul_70_carry), .Sum_In(n1_bit_mul_68_sum), .A(A[16]), .B(B[20]),
    .Sum(n1_bit_mul_69_sum), .Carry(n1_bit_mul_69_carry));
  _1_bit_MUL u_1_bit_mul_70 (
    .Carry_In(n1_bit_mul_85_carry), .Sum_In(n1_bit_mul_84_sum), .A(A[15]), .B(B[20]),
    .Sum(n1_bit_mul_70_sum), .Carry(n1_bit_mul_70_carry));
  _1_bit_MUL u_1_bit_mul_71 (
    .Carry_In(n1_bit_mul_86_carry), .Sum_In(n1_bit_mul_69_sum), .A(A[15]), .B(B[21]),
    .Sum(n1_bit_mul_71_sum), .Carry(n1_bit_mul_71_carry));
  _1_bit_MUL u_1_bit_mul_72 (
    .Carry_In(n1_bit_mul_88_carry), .Sum_In(n1_bit_mul_71_sum), .A(A[14]), .B(B[22]),
    .Sum(n1_bit_mul_72_sum), .Carry(n1_bit_mul_72_carry));
  _1_bit_MUL u_1_bit_mul_73 (
    .Carry_In(n1_bit_mul_91_carry), .Sum_In(n1_bit_mul_72_sum), .A(A[13]), .B(B[23]), .Sum(HI[12]),
    .Carry(n1_bit_mul_73_carry));
  _1_bit_MUL u_1_bit_mul_74 (
    .Carry_In(n1_bit_mul_96_carry), .Sum_In(n1_bit_mul_93_carry), .A(A[23]), .B(B[11]),
    .Sum(n1_bit_mul_74_sum), .Carry(n1_bit_mul_74_carry));
  _1_bit_MUL u_1_bit_mul_75 (
    .Carry_In(n1_bit_mul_98_carry), .Sum_In(n1_bit_mul_74_sum), .A(A[22]), .B(B[12]),
    .Sum(n1_bit_mul_75_sum), .Carry(n1_bit_mul_75_carry));
  _1_bit_MUL u_1_bit_mul_76 (
    .Carry_In(n1_bit_mul_99_carry), .Sum_In(n1_bit_mul_75_sum), .A(A[21]), .B(B[13]),
    .Sum(n1_bit_mul_76_sum), .Carry(n1_bit_mul_76_carry));
  _1_bit_MUL u_1_bit_mul_77 (
    .Carry_In(n1_bit_mul_101_carry), .Sum_In(n1_bit_mul_76_sum), .A(A[20]), .B(B[14]),
    .Sum(n1_bit_mul_77_sum), .Carry(n1_bit_mul_77_carry));
  _1_bit_MUL u_1_bit_mul_78 (
    .Carry_In(n1_bit_mul_104_carry), .Sum_In(n1_bit_mul_77_sum), .A(A[19]), .B(B[15]),
    .Sum(n1_bit_mul_78_sum), .Carry(n1_bit_mul_78_carry));
  _1_bit_MUL u_1_bit_mul_79 (
    .Carry_In(n1_bit_mul_105_carry), .Sum_In(n1_bit_mul_78_sum), .A(A[18]), .B(B[16]),
    .Sum(n1_bit_mul_79_sum), .Carry(n1_bit_mul_79_carry));
  _1_bit_MUL u_1_bit_mul_80 (
    .Carry_In(n1_bit_mul_106_carry), .Sum_In(n1_bit_mul_79_sum), .A(A[17]), .B(B[17]),
    .Sum(n1_bit_mul_80_sum), .Carry(n1_bit_mul_80_carry));
  _1_bit_MUL u_1_bit_mul_81 (
    .Carry_In(n1_bit_mul_82_carry), .Sum_In(n1_bit_mul_65_sum), .A(A[17]), .B(B[18]),
    .Sum(n1_bit_mul_81_sum), .Carry(n1_bit_mul_81_carry));
  _1_bit_MUL u_1_bit_mul_82 (
    .Carry_In(n1_bit_mul_107_carry), .Sum_In(n1_bit_mul_80_sum), .A(A[16]), .B(B[18]),
    .Sum(n1_bit_mul_82_sum), .Carry(n1_bit_mul_82_carry));
  _1_bit_MUL u_1_bit_mul_83 (
    .Carry_In(n1_bit_mul_108_carry), .Sum_In(n1_bit_mul_82_sum), .A(A[15]), .B(B[19]),
    .Sum(n1_bit_mul_83_sum), .Carry(n1_bit_mul_83_carry));
  _1_bit_MUL u_1_bit_mul_84 (
    .Carry_In(n1_bit_mul_83_carry), .Sum_In(n1_bit_mul_81_sum), .A(A[16]), .B(B[19]),
    .Sum(n1_bit_mul_84_sum), .Carry(n1_bit_mul_84_carry));
  _1_bit_MUL u_1_bit_mul_85 (
    .Carry_In(n1_bit_mul_109_carry), .Sum_In(n1_bit_mul_83_sum), .A(A[14]), .B(B[20]),
    .Sum(n1_bit_mul_85_sum), .Carry(n1_bit_mul_85_carry));
  _1_bit_MUL u_1_bit_mul_86 (
    .Carry_In(n1_bit_mul_87_carry), .Sum_In(n1_bit_mul_70_sum), .A(A[14]), .B(B[21]),
    .Sum(n1_bit_mul_86_sum), .Carry(n1_bit_mul_86_carry));
  _1_bit_MUL u_1_bit_mul_87 (
    .Carry_In(n1_bit_mul_110_carry), .Sum_In(n1_bit_mul_85_sum), .A(A[13]), .B(B[21]),
    .Sum(n1_bit_mul_87_sum), .Carry(n1_bit_mul_87_carry));
  _1_bit_MUL u_1_bit_mul_88 (
    .Carry_In(n1_bit_mul_89_carry), .Sum_In(n1_bit_mul_86_sum), .A(A[13]), .B(B[22]),
    .Sum(n1_bit_mul_88_sum), .Carry(n1_bit_mul_88_carry));
  _1_bit_MUL u_1_bit_mul_89 (
    .Carry_In(n1_bit_mul_111_carry), .Sum_In(n1_bit_mul_87_sum), .A(A[12]), .B(B[22]),
    .Sum(n1_bit_mul_89_sum), .Carry(n1_bit_mul_89_carry));
  _1_bit_MUL u_1_bit_mul_90 (
    .Carry_In(n1_bit_mul_112_carry), .Sum_In(n1_bit_mul_89_sum), .A(A[11]), .B(B[23]), .Sum(HI[10]),
    .Carry(n1_bit_mul_90_carry));
  _1_bit_MUL u_1_bit_mul_91 (
    .Carry_In(n1_bit_mul_90_carry), .Sum_In(n1_bit_mul_88_sum), .A(A[12]), .B(B[23]), .Sum(HI[11]),
    .Carry(n1_bit_mul_91_carry));
  _1_bit_MUL u_1_bit_mul_92 (
    .Carry_In(n1_bit_mul_114_carry), .Sum_In(n1_bit_mul_113_carry), .A(A[23]), .B(B[9]),
    .Sum(n1_bit_mul_92_sum), .Carry(n1_bit_mul_92_carry));
  _1_bit_MUL u_1_bit_mul_93 (
    .Carry_In(n1_bit_mul_94_carry), .Sum_In(n1_bit_mul_92_carry), .A(A[23]), .B(B[10]),
    .Sum(n1_bit_mul_93_sum), .Carry(n1_bit_mul_93_carry));
  _1_bit_MUL u_1_bit_mul_94 (
    .Carry_In(n1_bit_mul_115_carry), .Sum_In(n1_bit_mul_92_sum), .A(A[22]), .B(B[10]),
    .Sum(n1_bit_mul_94_sum), .Carry(n1_bit_mul_94_carry));
  _1_bit_MUL u_1_bit_mul_95 (
    .Carry_In(n1_bit_mul_116_carry), .Sum_In(n1_bit_mul_94_sum), .A(A[21]), .B(B[11]),
    .Sum(n1_bit_mul_95_sum), .Carry(n1_bit_mul_95_carry));
  _1_bit_MUL u_1_bit_mul_96 (
    .Carry_In(n1_bit_mul_95_carry), .Sum_In(n1_bit_mul_93_sum), .A(A[22]), .B(B[11]),
    .Sum(n1_bit_mul_96_sum), .Carry(n1_bit_mul_96_carry));
  _1_bit_MUL u_1_bit_mul_97 (
    .Carry_In(n1_bit_mul_117_carry), .Sum_In(n1_bit_mul_95_sum), .A(A[20]), .B(B[12]),
    .Sum(n1_bit_mul_97_sum), .Carry(n1_bit_mul_97_carry));
  _1_bit_MUL u_1_bit_mul_98 (
    .Carry_In(n1_bit_mul_97_carry), .Sum_In(n1_bit_mul_96_sum), .A(A[21]), .B(B[12]),
    .Sum(n1_bit_mul_98_sum), .Carry(n1_bit_mul_98_carry));
  _1_bit_MUL u_1_bit_mul_99 (
    .Carry_In(n1_bit_mul_100_carry), .Sum_In(n1_bit_mul_98_sum), .A(A[20]), .B(B[13]),
    .Sum(n1_bit_mul_99_sum), .Carry(n1_bit_mul_99_carry));
  _1_bit_MUL u_1_bit_mul_100 (
    .Carry_In(n1_bit_mul_118_carry), .Sum_In(n1_bit_mul_97_sum), .A(A[19]), .B(B[13]),
    .Sum(n1_bit_mul_100_sum), .Carry(n1_bit_mul_100_carry));
  _1_bit_MUL u_1_bit_mul_101 (
    .Carry_In(n1_bit_mul_102_carry), .Sum_In(n1_bit_mul_99_sum), .A(A[19]), .B(B[14]),
    .Sum(n1_bit_mul_101_sum), .Carry(n1_bit_mul_101_carry));
  _1_bit_MUL u_1_bit_mul_102 (
    .Carry_In(n1_bit_mul_119_carry), .Sum_In(n1_bit_mul_100_sum), .A(A[18]), .B(B[14]),
    .Sum(n1_bit_mul_102_sum), .Carry(n1_bit_mul_102_carry));
  _1_bit_MUL u_1_bit_mul_103 (
    .Carry_In(n1_bit_mul_120_carry), .Sum_In(n1_bit_mul_102_sum), .A(A[17]), .B(B[15]),
    .Sum(n1_bit_mul_103_sum), .Carry(n1_bit_mul_103_carry));
  _1_bit_MUL u_1_bit_mul_104 (
    .Carry_In(n1_bit_mul_103_carry), .Sum_In(n1_bit_mul_101_sum), .A(A[18]), .B(B[15]),
    .Sum(n1_bit_mul_104_sum), .Carry(n1_bit_mul_104_carry));
  _1_bit_MUL u_1_bit_mul_105 (
    .Carry_In(n1_bit_mul_121_carry), .Sum_In(n1_bit_mul_104_sum), .A(A[17]), .B(B[16]),
    .Sum(n1_bit_mul_105_sum), .Carry(n1_bit_mul_105_carry));
  _1_bit_MUL u_1_bit_mul_106 (
    .Carry_In(n1_bit_mul_124_carry), .Sum_In(n1_bit_mul_105_sum), .A(A[16]), .B(B[17]),
    .Sum(n1_bit_mul_106_sum), .Carry(n1_bit_mul_106_carry));
  _1_bit_MUL u_1_bit_mul_107 (
    .Carry_In(n1_bit_mul_126_carry), .Sum_In(n1_bit_mul_106_sum), .A(A[15]), .B(B[18]),
    .Sum(n1_bit_mul_107_sum), .Carry(n1_bit_mul_107_carry));
  _1_bit_MUL u_1_bit_mul_108 (
    .Carry_In(n1_bit_mul_127_carry), .Sum_In(n1_bit_mul_107_sum), .A(A[14]), .B(B[19]),
    .Sum(n1_bit_mul_108_sum), .Carry(n1_bit_mul_108_carry));
  _1_bit_MUL u_1_bit_mul_109 (
    .Carry_In(n1_bit_mul_129_carry), .Sum_In(n1_bit_mul_108_sum), .A(A[13]), .B(B[20]),
    .Sum(n1_bit_mul_109_sum), .Carry(n1_bit_mul_109_carry));
  _1_bit_MUL u_1_bit_mul_110 (
    .Carry_In(n1_bit_mul_131_carry), .Sum_In(n1_bit_mul_109_sum), .A(A[12]), .B(B[21]),
    .Sum(n1_bit_mul_110_sum), .Carry(n1_bit_mul_110_carry));
  _1_bit_MUL u_1_bit_mul_111 (
    .Carry_In(n1_bit_mul_132_carry), .Sum_In(n1_bit_mul_110_sum), .A(A[11]), .B(B[22]),
    .Sum(n1_bit_mul_111_sum), .Carry(n1_bit_mul_111_carry));
  _1_bit_MUL u_1_bit_mul_112 (
    .Carry_In(n1_bit_mul_133_carry), .Sum_In(n1_bit_mul_111_sum), .A(A[10]), .B(B[23]), .Sum(HI[9]),
    .Carry(n1_bit_mul_112_carry));
  _1_bit_MUL u_1_bit_mul_113 (
    .Carry_In(n1_bit_mul_135_carry), .Sum_In(n1_bit_mul_134_carry), .A(A[23]), .B(B[8]),
    .Sum(n1_bit_mul_113_sum), .Carry(n1_bit_mul_113_carry));
  _1_bit_MUL u_1_bit_mul_114 (
    .Carry_In(n1_bit_mul_136_carry), .Sum_In(n1_bit_mul_113_sum), .A(A[22]), .B(B[9]),
    .Sum(n1_bit_mul_114_sum), .Carry(n1_bit_mul_114_carry));
  _1_bit_MUL u_1_bit_mul_115 (
    .Carry_In(n1_bit_mul_137_carry), .Sum_In(n1_bit_mul_114_sum), .A(A[21]), .B(B[10]),
    .Sum(n1_bit_mul_115_sum), .Carry(n1_bit_mul_115_carry));
  _1_bit_MUL u_1_bit_mul_116 (
    .Carry_In(n1_bit_mul_138_carry), .Sum_In(n1_bit_mul_115_sum), .A(A[20]), .B(B[11]),
    .Sum(n1_bit_mul_116_sum), .Carry(n1_bit_mul_116_carry));
  _1_bit_MUL u_1_bit_mul_117 (
    .Carry_In(n1_bit_mul_139_carry), .Sum_In(n1_bit_mul_116_sum), .A(A[19]), .B(B[12]),
    .Sum(n1_bit_mul_117_sum), .Carry(n1_bit_mul_117_carry));
  _1_bit_MUL u_1_bit_mul_118 (
    .Carry_In(n1_bit_mul_140_carry), .Sum_In(n1_bit_mul_117_sum), .A(A[18]), .B(B[13]),
    .Sum(n1_bit_mul_118_sum), .Carry(n1_bit_mul_118_carry));
  _1_bit_MUL u_1_bit_mul_119 (
    .Carry_In(n1_bit_mul_141_carry), .Sum_In(n1_bit_mul_118_sum), .A(A[17]), .B(B[14]),
    .Sum(n1_bit_mul_119_sum), .Carry(n1_bit_mul_119_carry));
  _1_bit_MUL u_1_bit_mul_120 (
    .Carry_In(n1_bit_mul_142_carry), .Sum_In(n1_bit_mul_119_sum), .A(A[16]), .B(B[15]),
    .Sum(n1_bit_mul_120_sum), .Carry(n1_bit_mul_120_carry));
  _1_bit_MUL u_1_bit_mul_121 (
    .Carry_In(n1_bit_mul_122_carry), .Sum_In(n1_bit_mul_103_sum), .A(A[16]), .B(B[16]),
    .Sum(n1_bit_mul_121_sum), .Carry(n1_bit_mul_121_carry));
  _1_bit_MUL u_1_bit_mul_122 (
    .Carry_In(n1_bit_mul_143_carry), .Sum_In(n1_bit_mul_120_sum), .A(A[15]), .B(B[16]),
    .Sum(n1_bit_mul_122_sum), .Carry(n1_bit_mul_122_carry));
  _1_bit_MUL u_1_bit_mul_123 (
    .Carry_In(n1_bit_mul_144_carry), .Sum_In(n1_bit_mul_122_sum), .A(A[14]), .B(B[17]),
    .Sum(n1_bit_mul_123_sum), .Carry(n1_bit_mul_123_carry));
  _1_bit_MUL u_1_bit_mul_124 (
    .Carry_In(n1_bit_mul_123_carry), .Sum_In(n1_bit_mul_121_sum), .A(A[15]), .B(B[17]),
    .Sum(n1_bit_mul_124_sum), .Carry(n1_bit_mul_124_carry));
  _1_bit_MUL u_1_bit_mul_125 (
    .Carry_In(n1_bit_mul_145_carry), .Sum_In(n1_bit_mul_123_sum), .A(A[13]), .B(B[18]),
    .Sum(n1_bit_mul_125_sum), .Carry(n1_bit_mul_125_carry));
  _1_bit_MUL u_1_bit_mul_126 (
    .Carry_In(n1_bit_mul_125_carry), .Sum_In(n1_bit_mul_124_sum), .A(A[14]), .B(B[18]),
    .Sum(n1_bit_mul_126_sum), .Carry(n1_bit_mul_126_carry));
  _1_bit_MUL u_1_bit_mul_127 (
    .Carry_In(n1_bit_mul_128_carry), .Sum_In(n1_bit_mul_126_sum), .A(A[13]), .B(B[19]),
    .Sum(n1_bit_mul_127_sum), .Carry(n1_bit_mul_127_carry));
  _1_bit_MUL u_1_bit_mul_128 (
    .Carry_In(n1_bit_mul_146_carry), .Sum_In(n1_bit_mul_125_sum), .A(A[12]), .B(B[19]),
    .Sum(n1_bit_mul_128_sum), .Carry(n1_bit_mul_128_carry));
  _1_bit_MUL u_1_bit_mul_129 (
    .Carry_In(n1_bit_mul_130_carry), .Sum_In(n1_bit_mul_127_sum), .A(A[12]), .B(B[20]),
    .Sum(n1_bit_mul_129_sum), .Carry(n1_bit_mul_129_carry));
  _1_bit_MUL u_1_bit_mul_130 (
    .Carry_In(n1_bit_mul_147_carry), .Sum_In(n1_bit_mul_128_sum), .A(A[11]), .B(B[20]),
    .Sum(n1_bit_mul_130_sum), .Carry(n1_bit_mul_130_carry));
  _1_bit_MUL u_1_bit_mul_131 (
    .Carry_In(n1_bit_mul_148_carry), .Sum_In(n1_bit_mul_129_sum), .A(A[11]), .B(B[21]),
    .Sum(n1_bit_mul_131_sum), .Carry(n1_bit_mul_131_carry));
  _1_bit_MUL u_1_bit_mul_132 (
    .Carry_In(n1_bit_mul_150_carry), .Sum_In(n1_bit_mul_131_sum), .A(A[10]), .B(B[22]),
    .Sum(n1_bit_mul_132_sum), .Carry(n1_bit_mul_132_carry));
  _1_bit_MUL u_1_bit_mul_133 (
    .Carry_In(n1_bit_mul_153_carry), .Sum_In(n1_bit_mul_132_sum), .A(A[9]), .B(B[23]), .Sum(HI[8]),
    .Carry(n1_bit_mul_133_carry));
  _1_bit_MUL u_1_bit_mul_134 (
    .Carry_In(n1_bit_mul_158_carry), .Sum_In(n1_bit_mul_155_carry), .A(A[23]), .B(B[7]),
    .Sum(n1_bit_mul_134_sum), .Carry(n1_bit_mul_134_carry));
  _1_bit_MUL u_1_bit_mul_135 (
    .Carry_In(n1_bit_mul_159_carry), .Sum_In(n1_bit_mul_134_sum), .A(A[22]), .B(B[8]),
    .Sum(n1_bit_mul_135_sum), .Carry(n1_bit_mul_135_carry));
  _1_bit_MUL u_1_bit_mul_136 (
    .Carry_In(n1_bit_mul_162_carry), .Sum_In(n1_bit_mul_135_sum), .A(A[21]), .B(B[9]),
    .Sum(n1_bit_mul_136_sum), .Carry(n1_bit_mul_136_carry));
  _1_bit_MUL u_1_bit_mul_137 (
    .Carry_In(n1_bit_mul_163_carry), .Sum_In(n1_bit_mul_136_sum), .A(A[20]), .B(B[10]),
    .Sum(n1_bit_mul_137_sum), .Carry(n1_bit_mul_137_carry));
  _1_bit_MUL u_1_bit_mul_138 (
    .Carry_In(n1_bit_mul_165_carry), .Sum_In(n1_bit_mul_137_sum), .A(A[19]), .B(B[11]),
    .Sum(n1_bit_mul_138_sum), .Carry(n1_bit_mul_138_carry));
  _1_bit_MUL u_1_bit_mul_139 (
    .Carry_In(n1_bit_mul_168_carry), .Sum_In(n1_bit_mul_138_sum), .A(A[18]), .B(B[12]),
    .Sum(n1_bit_mul_139_sum), .Carry(n1_bit_mul_139_carry));
  _1_bit_MUL u_1_bit_mul_140 (
    .Carry_In(n1_bit_mul_169_carry), .Sum_In(n1_bit_mul_139_sum), .A(A[17]), .B(B[13]),
    .Sum(n1_bit_mul_140_sum), .Carry(n1_bit_mul_140_carry));
  _1_bit_MUL u_1_bit_mul_141 (
    .Carry_In(n1_bit_mul_171_carry), .Sum_In(n1_bit_mul_140_sum), .A(A[16]), .B(B[14]),
    .Sum(n1_bit_mul_141_sum), .Carry(n1_bit_mul_141_carry));
  _1_bit_MUL u_1_bit_mul_142 (
    .Carry_In(n1_bit_mul_174_carry), .Sum_In(n1_bit_mul_141_sum), .A(A[15]), .B(B[15]),
    .Sum(n1_bit_mul_142_sum), .Carry(n1_bit_mul_142_carry));
  _1_bit_MUL u_1_bit_mul_143 (
    .Carry_In(n1_bit_mul_175_carry), .Sum_In(n1_bit_mul_142_sum), .A(A[14]), .B(B[16]),
    .Sum(n1_bit_mul_143_sum), .Carry(n1_bit_mul_143_carry));
  _1_bit_MUL u_1_bit_mul_144 (
    .Carry_In(n1_bit_mul_176_carry), .Sum_In(n1_bit_mul_143_sum), .A(A[13]), .B(B[17]),
    .Sum(n1_bit_mul_144_sum), .Carry(n1_bit_mul_144_carry));
  _1_bit_MUL u_1_bit_mul_145 (
    .Carry_In(n1_bit_mul_177_carry), .Sum_In(n1_bit_mul_144_sum), .A(A[12]), .B(B[18]),
    .Sum(n1_bit_mul_145_sum), .Carry(n1_bit_mul_145_carry));
  _1_bit_MUL u_1_bit_mul_146 (
    .Carry_In(n1_bit_mul_178_carry), .Sum_In(n1_bit_mul_145_sum), .A(A[11]), .B(B[19]),
    .Sum(n1_bit_mul_146_sum), .Carry(n1_bit_mul_146_carry));
  _1_bit_MUL u_1_bit_mul_147 (
    .Carry_In(n1_bit_mul_179_carry), .Sum_In(n1_bit_mul_146_sum), .A(A[10]), .B(B[20]),
    .Sum(n1_bit_mul_147_sum), .Carry(n1_bit_mul_147_carry));
  _1_bit_MUL u_1_bit_mul_148 (
    .Carry_In(n1_bit_mul_149_carry), .Sum_In(n1_bit_mul_130_sum), .A(A[10]), .B(B[21]),
    .Sum(n1_bit_mul_148_sum), .Carry(n1_bit_mul_148_carry));
  _1_bit_MUL u_1_bit_mul_149 (
    .Carry_In(n1_bit_mul_180_carry), .Sum_In(n1_bit_mul_147_sum), .A(A[9]), .B(B[21]),
    .Sum(n1_bit_mul_149_sum), .Carry(n1_bit_mul_149_carry));
  _1_bit_MUL u_1_bit_mul_150 (
    .Carry_In(n1_bit_mul_151_carry), .Sum_In(n1_bit_mul_148_sum), .A(A[9]), .B(B[22]),
    .Sum(n1_bit_mul_150_sum), .Carry(n1_bit_mul_150_carry));
  _1_bit_MUL u_1_bit_mul_151 (
    .Carry_In(n1_bit_mul_181_carry), .Sum_In(n1_bit_mul_149_sum), .A(A[8]), .B(B[22]),
    .Sum(n1_bit_mul_151_sum), .Carry(n1_bit_mul_151_carry));
  _1_bit_MUL u_1_bit_mul_152 (
    .Carry_In(n1_bit_mul_182_carry), .Sum_In(n1_bit_mul_151_sum), .A(A[7]), .B(B[23]), .Sum(HI[6]),
    .Carry(n1_bit_mul_152_carry));
  _1_bit_MUL u_1_bit_mul_153 (
    .Carry_In(n1_bit_mul_152_carry), .Sum_In(n1_bit_mul_150_sum), .A(A[8]), .B(B[23]), .Sum(HI[7]),
    .Carry(n1_bit_mul_153_carry));
  _1_bit_MUL u_1_bit_mul_154 (
    .Carry_In(n1_bit_mul_185_carry), .Sum_In(n1_bit_mul_184_carry), .A(A[23]), .B(B[5]),
    .Sum(n1_bit_mul_154_sum), .Carry(n1_bit_mul_154_carry));
  _1_bit_MUL u_1_bit_mul_155 (
    .Carry_In(n1_bit_mul_156_carry), .Sum_In(n1_bit_mul_154_carry), .A(A[23]), .B(B[6]),
    .Sum(n1_bit_mul_155_sum), .Carry(n1_bit_mul_155_carry));
  _1_bit_MUL u_1_bit_mul_156 (
    .Carry_In(n1_bit_mul_186_carry), .Sum_In(n1_bit_mul_154_sum), .A(A[22]), .B(B[6]),
    .Sum(n1_bit_mul_156_sum), .Carry(n1_bit_mul_156_carry));
  _1_bit_MUL u_1_bit_mul_157 (
    .Carry_In(n1_bit_mul_187_carry), .Sum_In(n1_bit_mul_156_sum), .A(A[21]), .B(B[7]),
    .Sum(n1_bit_mul_157_sum), .Carry(n1_bit_mul_157_carry));
  _1_bit_MUL u_1_bit_mul_158 (
    .Carry_In(n1_bit_mul_157_carry), .Sum_In(n1_bit_mul_155_sum), .A(A[22]), .B(B[7]),
    .Sum(n1_bit_mul_158_sum), .Carry(n1_bit_mul_158_carry));
  _1_bit_MUL u_1_bit_mul_159 (
    .Carry_In(n1_bit_mul_160_carry), .Sum_In(n1_bit_mul_158_sum), .A(A[21]), .B(B[8]),
    .Sum(n1_bit_mul_159_sum), .Carry(n1_bit_mul_159_carry));
  _1_bit_MUL u_1_bit_mul_160 (
    .Carry_In(n1_bit_mul_188_carry), .Sum_In(n1_bit_mul_157_sum), .A(A[20]), .B(B[8]),
    .Sum(n1_bit_mul_160_sum), .Carry(n1_bit_mul_160_carry));
  _1_bit_MUL u_1_bit_mul_161 (
    .Carry_In(n1_bit_mul_189_carry), .Sum_In(n1_bit_mul_160_sum), .A(A[19]), .B(B[9]),
    .Sum(n1_bit_mul_161_sum), .Carry(n1_bit_mul_161_carry));
  _1_bit_MUL u_1_bit_mul_162 (
    .Carry_In(n1_bit_mul_161_carry), .Sum_In(n1_bit_mul_159_sum), .A(A[20]), .B(B[9]),
    .Sum(n1_bit_mul_162_sum), .Carry(n1_bit_mul_162_carry));
  _1_bit_MUL u_1_bit_mul_163 (
    .Carry_In(n1_bit_mul_164_carry), .Sum_In(n1_bit_mul_162_sum), .A(A[19]), .B(B[10]),
    .Sum(n1_bit_mul_163_sum), .Carry(n1_bit_mul_163_carry));
  _1_bit_MUL u_1_bit_mul_164 (
    .Carry_In(n1_bit_mul_190_carry), .Sum_In(n1_bit_mul_161_sum), .A(A[18]), .B(B[10]),
    .Sum(n1_bit_mul_164_sum), .Carry(n1_bit_mul_164_carry));
  _1_bit_MUL u_1_bit_mul_165 (
    .Carry_In(n1_bit_mul_166_carry), .Sum_In(n1_bit_mul_163_sum), .A(A[18]), .B(B[11]),
    .Sum(n1_bit_mul_165_sum), .Carry(n1_bit_mul_165_carry));
  _1_bit_MUL u_1_bit_mul_166 (
    .Carry_In(n1_bit_mul_191_carry), .Sum_In(n1_bit_mul_164_sum), .A(A[17]), .B(B[11]),
    .Sum(n1_bit_mul_166_sum), .Carry(n1_bit_mul_166_carry));
  _1_bit_MUL u_1_bit_mul_167 (
    .Carry_In(n1_bit_mul_192_carry), .Sum_In(n1_bit_mul_166_sum), .A(A[16]), .B(B[12]),
    .Sum(n1_bit_mul_167_sum), .Carry(n1_bit_mul_167_carry));
  _1_bit_MUL u_1_bit_mul_168 (
    .Carry_In(n1_bit_mul_167_carry), .Sum_In(n1_bit_mul_165_sum), .A(A[17]), .B(B[12]),
    .Sum(n1_bit_mul_168_sum), .Carry(n1_bit_mul_168_carry));
  _1_bit_MUL u_1_bit_mul_169 (
    .Carry_In(n1_bit_mul_170_carry), .Sum_In(n1_bit_mul_168_sum), .A(A[16]), .B(B[13]),
    .Sum(n1_bit_mul_169_sum), .Carry(n1_bit_mul_169_carry));
  _1_bit_MUL u_1_bit_mul_170 (
    .Carry_In(n1_bit_mul_193_carry), .Sum_In(n1_bit_mul_167_sum), .A(A[15]), .B(B[13]),
    .Sum(n1_bit_mul_170_sum), .Carry(n1_bit_mul_170_carry));
  _1_bit_MUL u_1_bit_mul_171 (
    .Carry_In(n1_bit_mul_172_carry), .Sum_In(n1_bit_mul_169_sum), .A(A[15]), .B(B[14]),
    .Sum(n1_bit_mul_171_sum), .Carry(n1_bit_mul_171_carry));
  _1_bit_MUL u_1_bit_mul_172 (
    .Carry_In(n1_bit_mul_194_carry), .Sum_In(n1_bit_mul_170_sum), .A(A[14]), .B(B[14]),
    .Sum(n1_bit_mul_172_sum), .Carry(n1_bit_mul_172_carry));
  _1_bit_MUL u_1_bit_mul_173 (
    .Carry_In(n1_bit_mul_195_carry), .Sum_In(n1_bit_mul_172_sum), .A(A[13]), .B(B[15]),
    .Sum(n1_bit_mul_173_sum), .Carry(n1_bit_mul_173_carry));
  _1_bit_MUL u_1_bit_mul_174 (
    .Carry_In(n1_bit_mul_173_carry), .Sum_In(n1_bit_mul_171_sum), .A(A[14]), .B(B[15]),
    .Sum(n1_bit_mul_174_sum), .Carry(n1_bit_mul_174_carry));
  _1_bit_MUL u_1_bit_mul_175 (
    .Carry_In(n1_bit_mul_197_carry), .Sum_In(n1_bit_mul_174_sum), .A(A[13]), .B(B[16]),
    .Sum(n1_bit_mul_175_sum), .Carry(n1_bit_mul_175_carry));
  _1_bit_MUL u_1_bit_mul_176 (
    .Carry_In(n1_bit_mul_198_carry), .Sum_In(n1_bit_mul_175_sum), .A(A[12]), .B(B[17]),
    .Sum(n1_bit_mul_176_sum), .Carry(n1_bit_mul_176_carry));
  _1_bit_MUL u_1_bit_mul_177 (
    .Carry_In(n1_bit_mul_200_carry), .Sum_In(n1_bit_mul_176_sum), .A(A[11]), .B(B[18]),
    .Sum(n1_bit_mul_177_sum), .Carry(n1_bit_mul_177_carry));
  _1_bit_MUL u_1_bit_mul_178 (
    .Carry_In(n1_bit_mul_203_carry), .Sum_In(n1_bit_mul_177_sum), .A(A[10]), .B(B[19]),
    .Sum(n1_bit_mul_178_sum), .Carry(n1_bit_mul_178_carry));
  _1_bit_MUL u_1_bit_mul_179 (
    .Carry_In(n1_bit_mul_205_carry), .Sum_In(n1_bit_mul_178_sum), .A(A[9]), .B(B[20]),
    .Sum(n1_bit_mul_179_sum), .Carry(n1_bit_mul_179_carry));
  _1_bit_MUL u_1_bit_mul_180 (
    .Carry_In(n1_bit_mul_206_carry), .Sum_In(n1_bit_mul_179_sum), .A(A[8]), .B(B[21]),
    .Sum(n1_bit_mul_180_sum), .Carry(n1_bit_mul_180_carry));
  _1_bit_MUL u_1_bit_mul_181 (
    .Carry_In(n1_bit_mul_207_carry), .Sum_In(n1_bit_mul_180_sum), .A(A[7]), .B(B[22]),
    .Sum(n1_bit_mul_181_sum), .Carry(n1_bit_mul_181_carry));
  _1_bit_MUL u_1_bit_mul_182 (
    .Carry_In(n1_bit_mul_208_carry), .Sum_In(n1_bit_mul_181_sum), .A(A[6]), .B(B[23]), .Sum(HI[5]),
    .Carry(n1_bit_mul_182_carry));
  _1_bit_MUL u_1_bit_mul_183 (
    .Carry_In(n1_bit_mul_210_carry), .Sum_In(n1_bit_mul_209_carry), .A(A[23]), .B(B[3]),
    .Sum(n1_bit_mul_183_sum), .Carry(n1_bit_mul_183_carry));
  _1_bit_MUL u_1_bit_mul_184 (
    .Carry_In(n1_bit_mul_211_carry), .Sum_In(n1_bit_mul_183_carry), .A(A[23]), .B(B[4]),
    .Sum(n1_bit_mul_184_sum), .Carry(n1_bit_mul_184_carry));
  _1_bit_MUL u_1_bit_mul_185 (
    .Carry_In(n1_bit_mul_214_carry), .Sum_In(n1_bit_mul_184_sum), .A(A[22]), .B(B[5]),
    .Sum(n1_bit_mul_185_sum), .Carry(n1_bit_mul_185_carry));
  _1_bit_MUL u_1_bit_mul_186 (
    .Carry_In(n1_bit_mul_215_carry), .Sum_In(n1_bit_mul_185_sum), .A(A[21]), .B(B[6]),
    .Sum(n1_bit_mul_186_sum), .Carry(n1_bit_mul_186_carry));
  _1_bit_MUL u_1_bit_mul_187 (
    .Carry_In(n1_bit_mul_216_carry), .Sum_In(n1_bit_mul_186_sum), .A(A[20]), .B(B[7]),
    .Sum(n1_bit_mul_187_sum), .Carry(n1_bit_mul_187_carry));
  _1_bit_MUL u_1_bit_mul_188 (
    .Carry_In(n1_bit_mul_217_carry), .Sum_In(n1_bit_mul_187_sum), .A(A[19]), .B(B[8]),
    .Sum(n1_bit_mul_188_sum), .Carry(n1_bit_mul_188_carry));
  _1_bit_MUL u_1_bit_mul_189 (
    .Carry_In(n1_bit_mul_218_carry), .Sum_In(n1_bit_mul_188_sum), .A(A[18]), .B(B[9]),
    .Sum(n1_bit_mul_189_sum), .Carry(n1_bit_mul_189_carry));
  _1_bit_MUL u_1_bit_mul_190 (
    .Carry_In(n1_bit_mul_219_carry), .Sum_In(n1_bit_mul_189_sum), .A(A[17]), .B(B[10]),
    .Sum(n1_bit_mul_190_sum), .Carry(n1_bit_mul_190_carry));
  _1_bit_MUL u_1_bit_mul_191 (
    .Carry_In(n1_bit_mul_220_carry), .Sum_In(n1_bit_mul_190_sum), .A(A[16]), .B(B[11]),
    .Sum(n1_bit_mul_191_sum), .Carry(n1_bit_mul_191_carry));
  _1_bit_MUL u_1_bit_mul_192 (
    .Carry_In(n1_bit_mul_221_carry), .Sum_In(n1_bit_mul_191_sum), .A(A[15]), .B(B[12]),
    .Sum(n1_bit_mul_192_sum), .Carry(n1_bit_mul_192_carry));
  _1_bit_MUL u_1_bit_mul_193 (
    .Carry_In(n1_bit_mul_222_carry), .Sum_In(n1_bit_mul_192_sum), .A(A[14]), .B(B[13]),
    .Sum(n1_bit_mul_193_sum), .Carry(n1_bit_mul_193_carry));
  _1_bit_MUL u_1_bit_mul_194 (
    .Carry_In(n1_bit_mul_223_carry), .Sum_In(n1_bit_mul_193_sum), .A(A[13]), .B(B[14]),
    .Sum(n1_bit_mul_194_sum), .Carry(n1_bit_mul_194_carry));
  _1_bit_MUL u_1_bit_mul_195 (
    .Carry_In(n1_bit_mul_224_carry), .Sum_In(n1_bit_mul_194_sum), .A(A[12]), .B(B[15]),
    .Sum(n1_bit_mul_195_sum), .Carry(n1_bit_mul_195_carry));
  _1_bit_MUL u_1_bit_mul_196 (
    .Carry_In(n1_bit_mul_225_carry), .Sum_In(n1_bit_mul_195_sum), .A(A[11]), .B(B[16]),
    .Sum(n1_bit_mul_196_sum), .Carry(n1_bit_mul_196_carry));
  _1_bit_MUL u_1_bit_mul_197 (
    .Carry_In(n1_bit_mul_196_carry), .Sum_In(n1_bit_mul_173_sum), .A(A[12]), .B(B[16]),
    .Sum(n1_bit_mul_197_sum), .Carry(n1_bit_mul_197_carry));
  _1_bit_MUL u_1_bit_mul_198 (
    .Carry_In(n1_bit_mul_199_carry), .Sum_In(n1_bit_mul_197_sum), .A(A[11]), .B(B[17]),
    .Sum(n1_bit_mul_198_sum), .Carry(n1_bit_mul_198_carry));
  _1_bit_MUL u_1_bit_mul_199 (
    .Carry_In(n1_bit_mul_226_carry), .Sum_In(n1_bit_mul_196_sum), .A(A[10]), .B(B[17]),
    .Sum(n1_bit_mul_199_sum), .Carry(n1_bit_mul_199_carry));
  _1_bit_MUL u_1_bit_mul_200 (
    .Carry_In(n1_bit_mul_201_carry), .Sum_In(n1_bit_mul_198_sum), .A(A[10]), .B(B[18]),
    .Sum(n1_bit_mul_200_sum), .Carry(n1_bit_mul_200_carry));
  _1_bit_MUL u_1_bit_mul_201 (
    .Carry_In(n1_bit_mul_227_carry), .Sum_In(n1_bit_mul_199_sum), .A(A[9]), .B(B[18]),
    .Sum(n1_bit_mul_201_sum), .Carry(n1_bit_mul_201_carry));
  _1_bit_MUL u_1_bit_mul_202 (
    .Carry_In(n1_bit_mul_228_carry), .Sum_In(n1_bit_mul_201_sum), .A(A[8]), .B(B[19]),
    .Sum(n1_bit_mul_202_sum), .Carry(n1_bit_mul_202_carry));
  _1_bit_MUL u_1_bit_mul_203 (
    .Carry_In(n1_bit_mul_202_carry), .Sum_In(n1_bit_mul_200_sum), .A(A[9]), .B(B[19]),
    .Sum(n1_bit_mul_203_sum), .Carry(n1_bit_mul_203_carry));
  _1_bit_MUL u_1_bit_mul_204 (
    .Carry_In(n1_bit_mul_229_carry), .Sum_In(n1_bit_mul_202_sum), .A(A[7]), .B(B[20]),
    .Sum(n1_bit_mul_204_sum), .Carry(n1_bit_mul_204_carry));
  _1_bit_MUL u_1_bit_mul_205 (
    .Carry_In(n1_bit_mul_204_carry), .Sum_In(n1_bit_mul_203_sum), .A(A[8]), .B(B[20]),
    .Sum(n1_bit_mul_205_sum), .Carry(n1_bit_mul_205_carry));
  _1_bit_MUL u_1_bit_mul_206 (
    .Carry_In(n1_bit_mul_231_carry), .Sum_In(n1_bit_mul_205_sum), .A(A[7]), .B(B[21]),
    .Sum(n1_bit_mul_206_sum), .Carry(n1_bit_mul_206_carry));
  _1_bit_MUL u_1_bit_mul_207 (
    .Carry_In(n1_bit_mul_233_carry), .Sum_In(n1_bit_mul_206_sum), .A(A[6]), .B(B[22]),
    .Sum(n1_bit_mul_207_sum), .Carry(n1_bit_mul_207_carry));
  _1_bit_MUL u_1_bit_mul_208 (
    .Carry_In(n1_bit_mul_234_carry), .Sum_In(n1_bit_mul_207_sum), .A(A[5]), .B(B[23]), .Sum(HI[4]),
    .Carry(n1_bit_mul_208_carry));
  _1_bit_MUL u_1_bit_mul_209 (
    .Carry_In(n1_bit_mul_237_carry), .Sum_In(n1_bit_mul_236_carry), .A(A[23]), .B(B[2]),
    .Sum(n1_bit_mul_209_sum), .Carry(n1_bit_mul_209_carry));
  _1_bit_MUL u_1_bit_mul_210 (
    .Carry_In(n1_bit_mul_238_carry), .Sum_In(n1_bit_mul_209_sum), .A(A[22]), .B(B[3]),
    .Sum(n1_bit_mul_210_sum), .Carry(n1_bit_mul_210_carry));
  _1_bit_MUL u_1_bit_mul_211 (
    .Carry_In(n1_bit_mul_212_carry), .Sum_In(n1_bit_mul_183_sum), .A(A[22]), .B(B[4]),
    .Sum(n1_bit_mul_211_sum), .Carry(n1_bit_mul_211_carry));
  _1_bit_MUL u_1_bit_mul_212 (
    .Carry_In(n1_bit_mul_239_carry), .Sum_In(n1_bit_mul_210_sum), .A(A[21]), .B(B[4]),
    .Sum(n1_bit_mul_212_sum), .Carry(n1_bit_mul_212_carry));
  _1_bit_MUL u_1_bit_mul_213 (
    .Carry_In(n1_bit_mul_240_carry), .Sum_In(n1_bit_mul_212_sum), .A(A[20]), .B(B[5]),
    .Sum(n1_bit_mul_213_sum), .Carry(n1_bit_mul_213_carry));
  _1_bit_MUL u_1_bit_mul_214 (
    .Carry_In(n1_bit_mul_213_carry), .Sum_In(n1_bit_mul_211_sum), .A(A[21]), .B(B[5]),
    .Sum(n1_bit_mul_214_sum), .Carry(n1_bit_mul_214_carry));
  _1_bit_MUL u_1_bit_mul_215 (
    .Carry_In(n1_bit_mul_242_carry), .Sum_In(n1_bit_mul_214_sum), .A(A[20]), .B(B[6]),
    .Sum(n1_bit_mul_215_sum), .Carry(n1_bit_mul_215_carry));
  _1_bit_MUL u_1_bit_mul_216 (
    .Carry_In(n1_bit_mul_243_carry), .Sum_In(n1_bit_mul_215_sum), .A(A[19]), .B(B[7]),
    .Sum(n1_bit_mul_216_sum), .Carry(n1_bit_mul_216_carry));
  _1_bit_MUL u_1_bit_mul_217 (
    .Carry_In(n1_bit_mul_245_carry), .Sum_In(n1_bit_mul_216_sum), .A(A[18]), .B(B[8]),
    .Sum(n1_bit_mul_217_sum), .Carry(n1_bit_mul_217_carry));
  _1_bit_MUL u_1_bit_mul_218 (
    .Carry_In(n1_bit_mul_247_carry), .Sum_In(n1_bit_mul_217_sum), .A(A[17]), .B(B[9]),
    .Sum(n1_bit_mul_218_sum), .Carry(n1_bit_mul_218_carry));
  _1_bit_MUL u_1_bit_mul_219 (
    .Carry_In(n1_bit_mul_249_carry), .Sum_In(n1_bit_mul_218_sum), .A(A[16]), .B(B[10]),
    .Sum(n1_bit_mul_219_sum), .Carry(n1_bit_mul_219_carry));
  _1_bit_MUL u_1_bit_mul_220 (
    .Carry_In(n1_bit_mul_252_carry), .Sum_In(n1_bit_mul_219_sum), .A(A[15]), .B(B[11]),
    .Sum(n1_bit_mul_220_sum), .Carry(n1_bit_mul_220_carry));
  _1_bit_MUL u_1_bit_mul_221 (
    .Carry_In(n1_bit_mul_254_carry), .Sum_In(n1_bit_mul_220_sum), .A(A[14]), .B(B[12]),
    .Sum(n1_bit_mul_221_sum), .Carry(n1_bit_mul_221_carry));
  _1_bit_MUL u_1_bit_mul_222 (
    .Carry_In(n1_bit_mul_255_carry), .Sum_In(n1_bit_mul_221_sum), .A(A[13]), .B(B[13]),
    .Sum(n1_bit_mul_222_sum), .Carry(n1_bit_mul_222_carry));
  _1_bit_MUL u_1_bit_mul_223 (
    .Carry_In(n1_bit_mul_258_carry), .Sum_In(n1_bit_mul_222_sum), .A(A[12]), .B(B[14]),
    .Sum(n1_bit_mul_223_sum), .Carry(n1_bit_mul_223_carry));
  _1_bit_MUL u_1_bit_mul_224 (
    .Carry_In(n1_bit_mul_260_carry), .Sum_In(n1_bit_mul_223_sum), .A(A[11]), .B(B[15]),
    .Sum(n1_bit_mul_224_sum), .Carry(n1_bit_mul_224_carry));
  _1_bit_MUL u_1_bit_mul_225 (
    .Carry_In(n1_bit_mul_261_carry), .Sum_In(n1_bit_mul_224_sum), .A(A[10]), .B(B[16]),
    .Sum(n1_bit_mul_225_sum), .Carry(n1_bit_mul_225_carry));
  _1_bit_MUL u_1_bit_mul_226 (
    .Carry_In(n1_bit_mul_262_carry), .Sum_In(n1_bit_mul_225_sum), .A(A[9]), .B(B[17]),
    .Sum(n1_bit_mul_226_sum), .Carry(n1_bit_mul_226_carry));
  _1_bit_MUL u_1_bit_mul_227 (
    .Carry_In(n1_bit_mul_263_carry), .Sum_In(n1_bit_mul_226_sum), .A(A[8]), .B(B[18]),
    .Sum(n1_bit_mul_227_sum), .Carry(n1_bit_mul_227_carry));
  _1_bit_MUL u_1_bit_mul_228 (
    .Carry_In(n1_bit_mul_264_carry), .Sum_In(n1_bit_mul_227_sum), .A(A[7]), .B(B[19]),
    .Sum(n1_bit_mul_228_sum), .Carry(n1_bit_mul_228_carry));
  _1_bit_MUL u_1_bit_mul_229 (
    .Carry_In(n1_bit_mul_265_carry), .Sum_In(n1_bit_mul_228_sum), .A(A[6]), .B(B[20]),
    .Sum(n1_bit_mul_229_sum), .Carry(n1_bit_mul_229_carry));
  _1_bit_MUL u_1_bit_mul_230 (
    .Carry_In(n1_bit_mul_266_carry), .Sum_In(n1_bit_mul_229_sum), .A(A[5]), .B(B[21]),
    .Sum(n1_bit_mul_230_sum), .Carry(n1_bit_mul_230_carry));
  _1_bit_MUL u_1_bit_mul_231 (
    .Carry_In(n1_bit_mul_230_carry), .Sum_In(n1_bit_mul_204_sum), .A(A[6]), .B(B[21]),
    .Sum(n1_bit_mul_231_sum), .Carry(n1_bit_mul_231_carry));
  _1_bit_MUL u_1_bit_mul_232 (
    .Carry_In(n1_bit_mul_267_carry), .Sum_In(n1_bit_mul_230_sum), .A(A[4]), .B(B[22]),
    .Sum(n1_bit_mul_232_sum), .Carry(n1_bit_mul_232_carry));
  _1_bit_MUL u_1_bit_mul_233 (
    .Carry_In(n1_bit_mul_232_carry), .Sum_In(n1_bit_mul_231_sum), .A(A[5]), .B(B[22]),
    .Sum(n1_bit_mul_233_sum), .Carry(n1_bit_mul_233_carry));
  _1_bit_MUL u_1_bit_mul_234 (
    .Carry_In(n1_bit_mul_235_carry), .Sum_In(n1_bit_mul_233_sum), .A(A[4]), .B(B[23]), .Sum(HI[3]),
    .Carry(n1_bit_mul_234_carry));
  _1_bit_MUL u_1_bit_mul_235 (
    .Carry_In(n1_bit_mul_268_carry), .Sum_In(n1_bit_mul_232_sum), .A(A[3]), .B(B[23]), .Sum(HI[2]),
    .Carry(n1_bit_mul_235_carry));
  _1_bit_MUL u_1_bit_mul_236 (
    .Carry_In(n1_bit_mul_271_carry), .Sum_In(n1_bit_mul_269_carry), .A(A[23]), .B(B[1]),
    .Sum(n1_bit_mul_236_sum), .Carry(n1_bit_mul_236_carry));
  _1_bit_MUL u_1_bit_mul_237 (
    .Carry_In(n1_bit_mul_273_carry), .Sum_In(n1_bit_mul_236_sum), .A(A[22]), .B(B[2]),
    .Sum(n1_bit_mul_237_sum), .Carry(n1_bit_mul_237_carry));
  _1_bit_MUL u_1_bit_mul_238 (
    .Carry_In(n1_bit_mul_276_carry), .Sum_In(n1_bit_mul_237_sum), .A(A[21]), .B(B[3]),
    .Sum(n1_bit_mul_238_sum), .Carry(n1_bit_mul_238_carry));
  _1_bit_MUL u_1_bit_mul_239 (
    .Carry_In(n1_bit_mul_277_carry), .Sum_In(n1_bit_mul_238_sum), .A(A[20]), .B(B[4]),
    .Sum(n1_bit_mul_239_sum), .Carry(n1_bit_mul_239_carry));
  _1_bit_MUL u_1_bit_mul_240 (
    .Carry_In(n1_bit_mul_278_carry), .Sum_In(n1_bit_mul_239_sum), .A(A[19]), .B(B[5]),
    .Sum(n1_bit_mul_240_sum), .Carry(n1_bit_mul_240_carry));
  _1_bit_MUL u_1_bit_mul_241 (
    .Carry_In(n1_bit_mul_279_carry), .Sum_In(n1_bit_mul_240_sum), .A(A[18]), .B(B[6]),
    .Sum(n1_bit_mul_241_sum), .Carry(n1_bit_mul_241_carry));
  _1_bit_MUL u_1_bit_mul_242 (
    .Carry_In(n1_bit_mul_241_carry), .Sum_In(n1_bit_mul_213_sum), .A(A[19]), .B(B[6]),
    .Sum(n1_bit_mul_242_sum), .Carry(n1_bit_mul_242_carry));
  _1_bit_MUL u_1_bit_mul_243 (
    .Carry_In(n1_bit_mul_244_carry), .Sum_In(n1_bit_mul_242_sum), .A(A[18]), .B(B[7]),
    .Sum(n1_bit_mul_243_sum), .Carry(n1_bit_mul_243_carry));
  _1_bit_MUL u_1_bit_mul_244 (
    .Carry_In(n1_bit_mul_280_carry), .Sum_In(n1_bit_mul_241_sum), .A(A[17]), .B(B[7]),
    .Sum(n1_bit_mul_244_sum), .Carry(n1_bit_mul_244_carry));
  _1_bit_MUL u_1_bit_mul_245 (
    .Carry_In(n1_bit_mul_246_carry), .Sum_In(n1_bit_mul_243_sum), .A(A[17]), .B(B[8]),
    .Sum(n1_bit_mul_245_sum), .Carry(n1_bit_mul_245_carry));
  _1_bit_MUL u_1_bit_mul_246 (
    .Carry_In(n1_bit_mul_281_carry), .Sum_In(n1_bit_mul_244_sum), .A(A[16]), .B(B[8]),
    .Sum(n1_bit_mul_246_sum), .Carry(n1_bit_mul_246_carry));
  _1_bit_MUL u_1_bit_mul_247 (
    .Carry_In(n1_bit_mul_248_carry), .Sum_In(n1_bit_mul_245_sum), .A(A[16]), .B(B[9]),
    .Sum(n1_bit_mul_247_sum), .Carry(n1_bit_mul_247_carry));
  _1_bit_MUL u_1_bit_mul_248 (
    .Carry_In(n1_bit_mul_282_carry), .Sum_In(n1_bit_mul_246_sum), .A(A[15]), .B(B[9]),
    .Sum(n1_bit_mul_248_sum), .Carry(n1_bit_mul_248_carry));
  _1_bit_MUL u_1_bit_mul_249 (
    .Carry_In(n1_bit_mul_250_carry), .Sum_In(n1_bit_mul_247_sum), .A(A[15]), .B(B[10]),
    .Sum(n1_bit_mul_249_sum), .Carry(n1_bit_mul_249_carry));
  _1_bit_MUL u_1_bit_mul_250 (
    .Carry_In(n1_bit_mul_283_carry), .Sum_In(n1_bit_mul_248_sum), .A(A[14]), .B(B[10]),
    .Sum(n1_bit_mul_250_sum), .Carry(n1_bit_mul_250_carry));
  _1_bit_MUL u_1_bit_mul_251 (
    .Carry_In(n1_bit_mul_284_carry), .Sum_In(n1_bit_mul_250_sum), .A(A[13]), .B(B[1]),
    .Sum(n1_bit_mul_251_sum), .Carry(n1_bit_mul_251_carry));
  _1_bit_MUL u_1_bit_mul_252 (
    .Carry_In(n1_bit_mul_251_carry), .Sum_In(n1_bit_mul_249_sum), .A(A[14]), .B(B[11]),
    .Sum(n1_bit_mul_252_sum), .Carry(n1_bit_mul_252_carry));
  _1_bit_MUL u_1_bit_mul_253 (
    .Carry_In(n1_bit_mul_285_carry), .Sum_In(n1_bit_mul_251_sum), .A(A[12]), .B(B[12]),
    .Sum(n1_bit_mul_253_sum), .Carry(n1_bit_mul_253_carry));
  _1_bit_MUL u_1_bit_mul_254 (
    .Carry_In(n1_bit_mul_253_carry), .Sum_In(n1_bit_mul_252_sum), .A(A[13]), .B(B[12]),
    .Sum(n1_bit_mul_254_sum), .Carry(n1_bit_mul_254_carry));
  _1_bit_MUL u_1_bit_mul_255 (
    .Carry_In(n1_bit_mul_256_carry), .Sum_In(n1_bit_mul_254_sum), .A(A[12]), .B(B[13]),
    .Sum(n1_bit_mul_255_sum), .Carry(n1_bit_mul_255_carry));
  _1_bit_MUL u_1_bit_mul_256 (
    .Carry_In(n1_bit_mul_286_carry), .Sum_In(n1_bit_mul_253_sum), .A(A[11]), .B(B[13]),
    .Sum(n1_bit_mul_256_sum), .Carry(n1_bit_mul_256_carry));
  _1_bit_MUL u_1_bit_mul_257 (
    .Carry_In(n1_bit_mul_287_carry), .Sum_In(n1_bit_mul_256_sum), .A(A[10]), .B(B[14]),
    .Sum(n1_bit_mul_257_sum), .Carry(n1_bit_mul_257_carry));
  _1_bit_MUL u_1_bit_mul_258 (
    .Carry_In(n1_bit_mul_257_carry), .Sum_In(n1_bit_mul_255_sum), .A(A[11]), .B(B[14]),
    .Sum(n1_bit_mul_258_sum), .Carry(n1_bit_mul_258_carry));
  _1_bit_MUL u_1_bit_mul_259 (
    .Carry_In(n1_bit_mul_288_carry), .Sum_In(n1_bit_mul_257_sum), .A(A[9]), .B(B[15]),
    .Sum(n1_bit_mul_259_sum), .Carry(n1_bit_mul_259_carry));
  _1_bit_MUL u_1_bit_mul_260 (
    .Carry_In(n1_bit_mul_259_carry), .Sum_In(n1_bit_mul_258_sum), .A(A[10]), .B(B[15]),
    .Sum(n1_bit_mul_260_sum), .Carry(n1_bit_mul_260_carry));
  _1_bit_MUL u_1_bit_mul_261 (
    .Carry_In(n1_bit_mul_289_carry), .Sum_In(n1_bit_mul_260_sum), .A(A[9]), .B(B[16]),
    .Sum(n1_bit_mul_261_sum), .Carry(n1_bit_mul_261_carry));
  _1_bit_MUL u_1_bit_mul_262 (
    .Carry_In(n1_bit_mul_292_carry), .Sum_In(n1_bit_mul_261_sum), .A(A[8]), .B(B[17]),
    .Sum(n1_bit_mul_262_sum), .Carry(n1_bit_mul_262_carry));
  _1_bit_MUL u_1_bit_mul_263 (
    .Carry_In(n1_bit_mul_294_carry), .Sum_In(n1_bit_mul_262_sum), .A(A[7]), .B(B[18]),
    .Sum(n1_bit_mul_263_sum), .Carry(n1_bit_mul_263_carry));
  _1_bit_MUL u_1_bit_mul_264 (
    .Carry_In(n1_bit_mul_295_carry), .Sum_In(n1_bit_mul_263_sum), .A(A[6]), .B(B[19]),
    .Sum(n1_bit_mul_264_sum), .Carry(n1_bit_mul_264_carry));
  _1_bit_MUL u_1_bit_mul_265 (
    .Carry_In(n1_bit_mul_298_carry), .Sum_In(n1_bit_mul_264_sum), .A(A[5]), .B(B[20]),
    .Sum(n1_bit_mul_265_sum), .Carry(n1_bit_mul_265_carry));
  _1_bit_MUL u_1_bit_mul_266 (
    .Carry_In(n1_bit_mul_299_carry), .Sum_In(n1_bit_mul_265_sum), .A(A[4]), .B(B[21]),
    .Sum(n1_bit_mul_266_sum), .Carry(n1_bit_mul_266_carry));
  _1_bit_MUL u_1_bit_mul_267 (
    .Carry_In(n1_bit_mul_300_carry), .Sum_In(n1_bit_mul_266_sum), .A(A[3]), .B(B[22]),
    .Sum(n1_bit_mul_267_sum), .Carry(n1_bit_mul_267_carry));
  _1_bit_MUL u_1_bit_mul_268 (
    .Carry_In(n1_bit_mul_301_carry), .Sum_In(n1_bit_mul_267_sum), .A(A[2]), .B(B[23]), .Sum(HI[1]),
    .Carry(n1_bit_mul_268_carry));
  _1_bit_MUL u_1_bit_mul_269 (
    .Carry_In(n1_bit_mul_270_carry), .Sum_In(1'b0), .A(A[23]), .B(B[0]), .Sum(n1_bit_mul_269_sum),
    .Carry(n1_bit_mul_269_carry));
  _1_bit_MUL u_1_bit_mul_270 (
    .Carry_In(n1_bit_mul_302_carry), .Sum_In(1'b0), .A(A[22]), .B(B[0]), .Sum(n1_bit_mul_270_sum),
    .Carry(n1_bit_mul_270_carry));
  _1_bit_MUL u_1_bit_mul_271 (
    .Carry_In(n1_bit_mul_272_carry), .Sum_In(n1_bit_mul_269_sum), .A(A[22]), .B(B[1]),
    .Sum(n1_bit_mul_271_sum), .Carry(n1_bit_mul_271_carry));
  _1_bit_MUL u_1_bit_mul_272 (
    .Carry_In(n1_bit_mul_303_carry), .Sum_In(n1_bit_mul_270_sum), .A(A[21]), .B(B[1]),
    .Sum(n1_bit_mul_272_sum), .Carry(n1_bit_mul_272_carry));
  _1_bit_MUL u_1_bit_mul_273 (
    .Carry_In(n1_bit_mul_274_carry), .Sum_In(n1_bit_mul_271_sum), .A(A[21]), .B(B[2]),
    .Sum(n1_bit_mul_273_sum), .Carry(n1_bit_mul_273_carry));
  _1_bit_MUL u_1_bit_mul_274 (
    .Carry_In(n1_bit_mul_304_carry), .Sum_In(n1_bit_mul_272_sum), .A(A[20]), .B(B[2]),
    .Sum(n1_bit_mul_274_sum), .Carry(n1_bit_mul_274_carry));
  _1_bit_MUL u_1_bit_mul_275 (
    .Carry_In(n1_bit_mul_305_carry), .Sum_In(n1_bit_mul_274_sum), .A(A[19]), .B(B[3]),
    .Sum(n1_bit_mul_275_sum), .Carry(n1_bit_mul_275_carry));
  _1_bit_MUL u_1_bit_mul_276 (
    .Carry_In(n1_bit_mul_275_carry), .Sum_In(n1_bit_mul_273_sum), .A(A[20]), .B(B[3]),
    .Sum(n1_bit_mul_276_sum), .Carry(n1_bit_mul_276_carry));
  _1_bit_MUL u_1_bit_mul_277 (
    .Carry_In(n1_bit_mul_307_carry), .Sum_In(n1_bit_mul_276_sum), .A(A[19]), .B(B[4]),
    .Sum(n1_bit_mul_277_sum), .Carry(n1_bit_mul_277_carry));
  _1_bit_MUL u_1_bit_mul_278 (
    .Carry_In(n1_bit_mul_308_carry), .Sum_In(n1_bit_mul_277_sum), .A(A[18]), .B(B[5]),
    .Sum(n1_bit_mul_278_sum), .Carry(n1_bit_mul_278_carry));
  _1_bit_MUL u_1_bit_mul_279 (
    .Carry_In(n1_bit_mul_310_carry), .Sum_In(n1_bit_mul_278_sum), .A(A[17]), .B(B[6]),
    .Sum(n1_bit_mul_279_sum), .Carry(n1_bit_mul_279_carry));
  _1_bit_MUL u_1_bit_mul_280 (
    .Carry_In(n1_bit_mul_313_carry), .Sum_In(n1_bit_mul_279_sum), .A(A[16]), .B(B[7]),
    .Sum(n1_bit_mul_280_sum), .Carry(n1_bit_mul_280_carry));
  _1_bit_MUL u_1_bit_mul_281 (
    .Carry_In(n1_bit_mul_314_carry), .Sum_In(n1_bit_mul_280_sum), .A(A[15]), .B(B[8]),
    .Sum(n1_bit_mul_281_sum), .Carry(n1_bit_mul_281_carry));
  _1_bit_MUL u_1_bit_mul_282 (
    .Carry_In(n1_bit_mul_316_carry), .Sum_In(n1_bit_mul_281_sum), .A(A[14]), .B(B[9]),
    .Sum(n1_bit_mul_282_sum), .Carry(n1_bit_mul_282_carry));
  _1_bit_MUL u_1_bit_mul_283 (
    .Carry_In(n1_bit_mul_317_carry), .Sum_In(n1_bit_mul_282_sum), .A(A[13]), .B(B[10]),
    .Sum(n1_bit_mul_283_sum), .Carry(n1_bit_mul_283_carry));
  _1_bit_MUL u_1_bit_mul_284 (
    .Carry_In(n1_bit_mul_318_carry), .Sum_In(n1_bit_mul_283_sum), .A(A[12]), .B(B[11]),
    .Sum(n1_bit_mul_284_sum), .Carry(n1_bit_mul_284_carry));
  _1_bit_MUL u_1_bit_mul_285 (
    .Carry_In(n1_bit_mul_319_carry), .Sum_In(n1_bit_mul_284_sum), .A(A[11]), .B(B[12]),
    .Sum(n1_bit_mul_285_sum), .Carry(n1_bit_mul_285_carry));
  _1_bit_MUL u_1_bit_mul_286 (
    .Carry_In(n1_bit_mul_320_carry), .Sum_In(n1_bit_mul_285_sum), .A(A[10]), .B(B[13]),
    .Sum(n1_bit_mul_286_sum), .Carry(n1_bit_mul_286_carry));
  _1_bit_MUL u_1_bit_mul_287 (
    .Carry_In(n1_bit_mul_321_carry), .Sum_In(n1_bit_mul_286_sum), .A(A[9]), .B(B[14]),
    .Sum(n1_bit_mul_287_sum), .Carry(n1_bit_mul_287_carry));
  _1_bit_MUL u_1_bit_mul_288 (
    .Carry_In(n1_bit_mul_322_carry), .Sum_In(n1_bit_mul_287_sum), .A(A[8]), .B(B[15]),
    .Sum(n1_bit_mul_288_sum), .Carry(n1_bit_mul_288_carry));
  _1_bit_MUL u_1_bit_mul_289 (
    .Carry_In(n1_bit_mul_290_carry), .Sum_In(n1_bit_mul_259_sum), .A(A[8]), .B(B[16]),
    .Sum(n1_bit_mul_289_sum), .Carry(n1_bit_mul_289_carry));
  _1_bit_MUL u_1_bit_mul_290 (
    .Carry_In(n1_bit_mul_323_carry), .Sum_In(n1_bit_mul_288_sum), .A(A[7]), .B(B[16]),
    .Sum(n1_bit_mul_290_sum), .Carry(n1_bit_mul_290_carry));
  _1_bit_MUL u_1_bit_mul_291 (
    .Carry_In(n1_bit_mul_324_carry), .Sum_In(n1_bit_mul_290_sum), .A(A[6]), .B(B[17]),
    .Sum(n1_bit_mul_291_sum), .Carry(n1_bit_mul_291_carry));
  _1_bit_MUL u_1_bit_mul_292 (
    .Carry_In(n1_bit_mul_291_carry), .Sum_In(n1_bit_mul_289_sum), .A(A[7]), .B(B[17]),
    .Sum(n1_bit_mul_292_sum), .Carry(n1_bit_mul_292_carry));
  _1_bit_MUL u_1_bit_mul_293 (
    .Carry_In(n1_bit_mul_325_carry), .Sum_In(n1_bit_mul_291_sum), .A(A[5]), .B(B[18]),
    .Sum(n1_bit_mul_293_sum), .Carry(n1_bit_mul_293_carry));
  _1_bit_MUL u_1_bit_mul_294 (
    .Carry_In(n1_bit_mul_293_carry), .Sum_In(n1_bit_mul_292_sum), .A(A[6]), .B(B[18]),
    .Sum(n1_bit_mul_294_sum), .Carry(n1_bit_mul_294_carry));
  _1_bit_MUL u_1_bit_mul_295 (
    .Carry_In(n1_bit_mul_296_carry), .Sum_In(n1_bit_mul_294_sum), .A(A[5]), .B(B[19]),
    .Sum(n1_bit_mul_295_sum), .Carry(n1_bit_mul_295_carry));
  _1_bit_MUL u_1_bit_mul_296 (
    .Carry_In(n1_bit_mul_326_carry), .Sum_In(n1_bit_mul_293_sum), .A(A[4]), .B(B[19]),
    .Sum(n1_bit_mul_296_sum), .Carry(n1_bit_mul_296_carry));
  _1_bit_MUL u_1_bit_mul_297 (
    .Carry_In(n1_bit_mul_327_carry), .Sum_In(n1_bit_mul_296_sum), .A(A[3]), .B(B[20]),
    .Sum(n1_bit_mul_297_sum), .Carry(n1_bit_mul_297_carry));
  _1_bit_MUL u_1_bit_mul_298 (
    .Carry_In(n1_bit_mul_297_carry), .Sum_In(n1_bit_mul_295_sum), .A(A[4]), .B(B[20]),
    .Sum(n1_bit_mul_298_sum), .Carry(n1_bit_mul_298_carry));
  _1_bit_MUL u_1_bit_mul_299 (
    .Carry_In(n1_bit_mul_328_carry), .Sum_In(n1_bit_mul_298_sum), .A(A[3]), .B(B[21]),
    .Sum(n1_bit_mul_299_sum), .Carry(n1_bit_mul_299_carry));
  _1_bit_MUL u_1_bit_mul_300 (
    .Carry_In(n1_bit_mul_331_carry), .Sum_In(n1_bit_mul_299_sum), .A(A[2]), .B(B[22]),
    .Sum(n1_bit_mul_300_sum), .Carry(n1_bit_mul_300_carry));
  _1_bit_MUL u_1_bit_mul_301 (
    .Carry_In(n1_bit_mul_332_carry), .Sum_In(n1_bit_mul_300_sum), .A(A[1]), .B(B[23]), .Sum(HI[0]),
    .Carry(n1_bit_mul_301_carry));
  _1_bit_MUL u_1_bit_mul_302 (
    .Carry_In(n1_bit_mul_333_carry), .Sum_In(1'b0), .A(A[21]), .B(B[0]), .Sum(n1_bit_mul_302_sum),
    .Carry(n1_bit_mul_302_carry));
  _1_bit_MUL u_1_bit_mul_303 (
    .Carry_In(n1_bit_mul_334_carry), .Sum_In(n1_bit_mul_302_sum), .A(A[20]), .B(B[1]),
    .Sum(n1_bit_mul_303_sum), .Carry(n1_bit_mul_303_carry));
  _1_bit_MUL u_1_bit_mul_304 (
    .Carry_In(n1_bit_mul_335_carry), .Sum_In(n1_bit_mul_303_sum), .A(A[19]), .B(B[2]),
    .Sum(n1_bit_mul_304_sum), .Carry(n1_bit_mul_304_carry));
  _1_bit_MUL u_1_bit_mul_305 (
    .Carry_In(n1_bit_mul_336_carry), .Sum_In(n1_bit_mul_304_sum), .A(A[18]), .B(B[3]),
    .Sum(n1_bit_mul_305_sum), .Carry(n1_bit_mul_305_carry));
  _1_bit_MUL u_1_bit_mul_306 (
    .Carry_In(n1_bit_mul_337_carry), .Sum_In(n1_bit_mul_305_sum), .A(A[17]), .B(B[4]),
    .Sum(n1_bit_mul_306_sum), .Carry(n1_bit_mul_306_carry));
  _1_bit_MUL u_1_bit_mul_307 (
    .Carry_In(n1_bit_mul_306_carry), .Sum_In(n1_bit_mul_275_sum), .A(A[18]), .B(B[4]),
    .Sum(n1_bit_mul_307_sum), .Carry(n1_bit_mul_307_carry));
  _1_bit_MUL u_1_bit_mul_308 (
    .Carry_In(n1_bit_mul_309_carry), .Sum_In(n1_bit_mul_307_sum), .A(A[17]), .B(B[5]),
    .Sum(n1_bit_mul_308_sum), .Carry(n1_bit_mul_308_carry));
  _1_bit_MUL u_1_bit_mul_309 (
    .Carry_In(n1_bit_mul_338_carry), .Sum_In(n1_bit_mul_306_sum), .A(A[16]), .B(B[5]),
    .Sum(n1_bit_mul_309_sum), .Carry(n1_bit_mul_309_carry));
  _1_bit_MUL u_1_bit_mul_310 (
    .Carry_In(n1_bit_mul_311_carry), .Sum_In(n1_bit_mul_308_sum), .A(A[16]), .B(B[6]),
    .Sum(n1_bit_mul_310_sum), .Carry(n1_bit_mul_310_carry));
  _1_bit_MUL u_1_bit_mul_311 (
    .Carry_In(n1_bit_mul_339_carry), .Sum_In(n1_bit_mul_309_sum), .A(A[15]), .B(B[6]),
    .Sum(n1_bit_mul_311_sum), .Carry(n1_bit_mul_311_carry));
  _1_bit_MUL u_1_bit_mul_312 (
    .Carry_In(n1_bit_mul_340_carry), .Sum_In(n1_bit_mul_311_sum), .A(A[14]), .B(B[7]),
    .Sum(n1_bit_mul_312_sum), .Carry(n1_bit_mul_312_carry));
  _1_bit_MUL u_1_bit_mul_313 (
    .Carry_In(n1_bit_mul_312_carry), .Sum_In(n1_bit_mul_310_sum), .A(A[15]), .B(B[7]),
    .Sum(n1_bit_mul_313_sum), .Carry(n1_bit_mul_313_carry));
  _1_bit_MUL u_1_bit_mul_314 (
    .Carry_In(n1_bit_mul_315_carry), .Sum_In(n1_bit_mul_313_sum), .A(A[14]), .B(B[8]),
    .Sum(n1_bit_mul_314_sum), .Carry(n1_bit_mul_314_carry));
  _1_bit_MUL u_1_bit_mul_315 (
    .Carry_In(n1_bit_mul_341_carry), .Sum_In(n1_bit_mul_312_sum), .A(A[13]), .B(B[8]),
    .Sum(n1_bit_mul_315_sum), .Carry(n1_bit_mul_315_carry));
  _1_bit_MUL u_1_bit_mul_316 (
    .Carry_In(n1_bit_mul_343_carry), .Sum_In(n1_bit_mul_314_sum), .A(A[13]), .B(B[9]),
    .Sum(n1_bit_mul_316_sum), .Carry(n1_bit_mul_316_carry));
  _1_bit_MUL u_1_bit_mul_317 (
    .Carry_In(n1_bit_mul_344_carry), .Sum_In(n1_bit_mul_316_sum), .A(A[12]), .B(B[10]),
    .Sum(n1_bit_mul_317_sum), .Carry(n1_bit_mul_317_carry));
  _1_bit_MUL u_1_bit_mul_318 (
    .Carry_In(n1_bit_mul_347_carry), .Sum_In(n1_bit_mul_317_sum), .A(A[11]), .B(B[11]),
    .Sum(n1_bit_mul_318_sum), .Carry(n1_bit_mul_318_carry));
  _1_bit_MUL u_1_bit_mul_319 (
    .Carry_In(n1_bit_mul_349_carry), .Sum_In(n1_bit_mul_318_sum), .A(A[10]), .B(B[12]),
    .Sum(n1_bit_mul_319_sum), .Carry(n1_bit_mul_319_carry));
  _1_bit_MUL u_1_bit_mul_320 (
    .Carry_In(n1_bit_mul_351_carry), .Sum_In(n1_bit_mul_319_sum), .A(A[9]), .B(B[13]),
    .Sum(n1_bit_mul_320_sum), .Carry(n1_bit_mul_320_carry));
  _1_bit_MUL u_1_bit_mul_321 (
    .Carry_In(n1_bit_mul_353_carry), .Sum_In(n1_bit_mul_320_sum), .A(A[8]), .B(B[14]),
    .Sum(n1_bit_mul_321_sum), .Carry(n1_bit_mul_321_carry));
  _1_bit_MUL u_1_bit_mul_322 (
    .Carry_In(n1_bit_mul_355_carry), .Sum_In(n1_bit_mul_321_sum), .A(A[7]), .B(B[15]),
    .Sum(n1_bit_mul_322_sum), .Carry(n1_bit_mul_322_carry));
  _1_bit_MUL u_1_bit_mul_323 (
    .Carry_In(n1_bit_mul_356_carry), .Sum_In(n1_bit_mul_322_sum), .A(A[6]), .B(B[16]),
    .Sum(n1_bit_mul_323_sum), .Carry(n1_bit_mul_323_carry));
  _1_bit_MUL u_1_bit_mul_324 (
    .Carry_In(n1_bit_mul_357_carry), .Sum_In(n1_bit_mul_323_sum), .A(A[5]), .B(B[17]),
    .Sum(n1_bit_mul_324_sum), .Carry(n1_bit_mul_324_carry));
  _1_bit_MUL u_1_bit_mul_325 (
    .Carry_In(n1_bit_mul_358_carry), .Sum_In(n1_bit_mul_324_sum), .A(A[4]), .B(B[18]),
    .Sum(n1_bit_mul_325_sum), .Carry(n1_bit_mul_325_carry));
  _1_bit_MUL u_1_bit_mul_326 (
    .Carry_In(n1_bit_mul_359_carry), .Sum_In(n1_bit_mul_325_sum), .A(A[3]), .B(B[19]),
    .Sum(n1_bit_mul_326_sum), .Carry(n1_bit_mul_326_carry));
  _1_bit_MUL u_1_bit_mul_327 (
    .Carry_In(n1_bit_mul_360_carry), .Sum_In(n1_bit_mul_326_sum), .A(A[2]), .B(B[20]),
    .Sum(n1_bit_mul_327_sum), .Carry(n1_bit_mul_327_carry));
  _1_bit_MUL u_1_bit_mul_328 (
    .Carry_In(n1_bit_mul_329_carry), .Sum_In(n1_bit_mul_297_sum), .A(A[2]), .B(B[21]),
    .Sum(n1_bit_mul_328_sum), .Carry(n1_bit_mul_328_carry));
  _1_bit_MUL u_1_bit_mul_329 (
    .Carry_In(n1_bit_mul_361_carry), .Sum_In(n1_bit_mul_327_sum), .A(A[1]), .B(B[21]),
    .Sum(n1_bit_mul_329_sum), .Carry(n1_bit_mul_329_carry));
  _1_bit_MUL u_1_bit_mul_330 (
    .Carry_In(1'b0), .Sum_In(n1_bit_mul_329_sum), .A(A[0]), .B(B[22]), .Sum(LO[22]),
    .Carry(n1_bit_mul_330_carry));
  _1_bit_MUL u_1_bit_mul_331 (
    .Carry_In(n1_bit_mul_330_carry), .Sum_In(n1_bit_mul_328_sum), .A(A[1]), .B(B[22]),
    .Sum(n1_bit_mul_331_sum), .Carry(n1_bit_mul_331_carry));
  _1_bit_MUL u_1_bit_mul_332 (
    .Carry_In(1'b0), .Sum_In(n1_bit_mul_331_sum), .A(A[0]), .B(B[23]), .Sum(LO[23]),
    .Carry(n1_bit_mul_332_carry));
  _1_bit_MUL u_1_bit_mul_333 (
    .Carry_In(n1_bit_mul_362_carry), .Sum_In(1'b0), .A(A[20]), .B(B[0]), .Sum(n1_bit_mul_333_sum),
    .Carry(n1_bit_mul_333_carry));
  _1_bit_MUL u_1_bit_mul_334 (
    .Carry_In(n1_bit_mul_364_carry), .Sum_In(n1_bit_mul_333_sum), .A(A[19]), .B(B[1]),
    .Sum(n1_bit_mul_334_sum), .Carry(n1_bit_mul_334_carry));
  _1_bit_MUL u_1_bit_mul_335 (
    .Carry_In(n1_bit_mul_367_carry), .Sum_In(n1_bit_mul_334_sum), .A(A[18]), .B(B[2]),
    .Sum(n1_bit_mul_335_sum), .Carry(n1_bit_mul_335_carry));
  _1_bit_MUL u_1_bit_mul_336 (
    .Carry_In(n1_bit_mul_369_carry), .Sum_In(n1_bit_mul_335_sum), .A(A[17]), .B(B[3]),
    .Sum(n1_bit_mul_336_sum), .Carry(n1_bit_mul_336_carry));
  _1_bit_MUL u_1_bit_mul_337 (
    .Carry_In(n1_bit_mul_370_carry), .Sum_In(n1_bit_mul_336_sum), .A(A[16]), .B(B[4]),
    .Sum(n1_bit_mul_337_sum), .Carry(n1_bit_mul_337_carry));
  _1_bit_MUL u_1_bit_mul_338 (
    .Carry_In(n1_bit_mul_371_carry), .Sum_In(n1_bit_mul_337_sum), .A(A[15]), .B(B[5]),
    .Sum(n1_bit_mul_338_sum), .Carry(n1_bit_mul_338_carry));
  _1_bit_MUL u_1_bit_mul_339 (
    .Carry_In(n1_bit_mul_372_carry), .Sum_In(n1_bit_mul_338_sum), .A(A[14]), .B(B[6]),
    .Sum(n1_bit_mul_339_sum), .Carry(n1_bit_mul_339_carry));
  _1_bit_MUL u_1_bit_mul_340 (
    .Carry_In(n1_bit_mul_373_carry), .Sum_In(n1_bit_mul_339_sum), .A(A[13]), .B(B[7]),
    .Sum(n1_bit_mul_340_sum), .Carry(n1_bit_mul_340_carry));
  _1_bit_MUL u_1_bit_mul_341 (
    .Carry_In(n1_bit_mul_374_carry), .Sum_In(n1_bit_mul_340_sum), .A(A[12]), .B(B[8]),
    .Sum(n1_bit_mul_341_sum), .Carry(n1_bit_mul_341_carry));
  _1_bit_MUL u_1_bit_mul_342 (
    .Carry_In(n1_bit_mul_375_carry), .Sum_In(n1_bit_mul_341_sum), .A(A[11]), .B(B[9]),
    .Sum(n1_bit_mul_342_sum), .Carry(n1_bit_mul_342_carry));
  _1_bit_MUL u_1_bit_mul_343 (
    .Carry_In(n1_bit_mul_342_carry), .Sum_In(n1_bit_mul_315_sum), .A(A[12]), .B(B[9]),
    .Sum(n1_bit_mul_343_sum), .Carry(n1_bit_mul_343_carry));
  _1_bit_MUL u_1_bit_mul_344 (
    .Carry_In(n1_bit_mul_345_carry), .Sum_In(n1_bit_mul_343_sum), .A(A[11]), .B(B[10]),
    .Sum(n1_bit_mul_344_sum), .Carry(n1_bit_mul_344_carry));
  _1_bit_MUL u_1_bit_mul_345 (
    .Carry_In(n1_bit_mul_376_carry), .Sum_In(n1_bit_mul_342_sum), .A(A[10]), .B(B[10]),
    .Sum(n1_bit_mul_345_sum), .Carry(n1_bit_mul_345_carry));
  _1_bit_MUL u_1_bit_mul_346 (
    .Carry_In(n1_bit_mul_377_carry), .Sum_In(n1_bit_mul_345_sum), .A(A[9]), .B(B[11]),
    .Sum(n1_bit_mul_346_sum), .Carry(n1_bit_mul_346_carry));
  _1_bit_MUL u_1_bit_mul_347 (
    .Carry_In(n1_bit_mul_346_carry), .Sum_In(n1_bit_mul_344_sum), .A(A[10]), .B(B[11]),
    .Sum(n1_bit_mul_347_sum), .Carry(n1_bit_mul_347_carry));
  _1_bit_MUL u_1_bit_mul_348 (
    .Carry_In(n1_bit_mul_378_carry), .Sum_In(n1_bit_mul_346_sum), .A(A[8]), .B(B[12]),
    .Sum(n1_bit_mul_348_sum), .Carry(n1_bit_mul_348_carry));
  _1_bit_MUL u_1_bit_mul_349 (
    .Carry_In(n1_bit_mul_348_carry), .Sum_In(n1_bit_mul_347_sum), .A(A[9]), .B(B[12]),
    .Sum(n1_bit_mul_349_sum), .Carry(n1_bit_mul_349_carry));
  _1_bit_MUL u_1_bit_mul_350 (
    .Carry_In(n1_bit_mul_379_carry), .Sum_In(n1_bit_mul_348_sum), .A(A[7]), .B(B[13]),
    .Sum(n1_bit_mul_350_sum), .Carry(n1_bit_mul_350_carry));
  _1_bit_MUL u_1_bit_mul_351 (
    .Carry_In(n1_bit_mul_350_carry), .Sum_In(n1_bit_mul_349_sum), .A(A[8]), .B(B[13]),
    .Sum(n1_bit_mul_351_sum), .Carry(n1_bit_mul_351_carry));
  _1_bit_MUL u_1_bit_mul_352 (
    .Carry_In(n1_bit_mul_380_carry), .Sum_In(n1_bit_mul_350_sum), .A(A[6]), .B(B[14]),
    .Sum(n1_bit_mul_352_sum), .Carry(n1_bit_mul_352_carry));
  _1_bit_MUL u_1_bit_mul_353 (
    .Carry_In(n1_bit_mul_352_carry), .Sum_In(n1_bit_mul_351_sum), .A(A[7]), .B(B[14]),
    .Sum(n1_bit_mul_353_sum), .Carry(n1_bit_mul_353_carry));
  _1_bit_MUL u_1_bit_mul_354 (
    .Carry_In(n1_bit_mul_381_carry), .Sum_In(n1_bit_mul_352_sum), .A(A[5]), .B(B[15]),
    .Sum(n1_bit_mul_354_sum), .Carry(n1_bit_mul_354_carry));
  _1_bit_MUL u_1_bit_mul_355 (
    .Carry_In(n1_bit_mul_354_carry), .Sum_In(n1_bit_mul_353_sum), .A(A[6]), .B(B[15]),
    .Sum(n1_bit_mul_355_sum), .Carry(n1_bit_mul_355_carry));
  _1_bit_MUL u_1_bit_mul_356 (
    .Carry_In(n1_bit_mul_383_carry), .Sum_In(n1_bit_mul_355_sum), .A(A[5]), .B(B[16]),
    .Sum(n1_bit_mul_356_sum), .Carry(n1_bit_mul_356_carry));
  _1_bit_MUL u_1_bit_mul_357 (
    .Carry_In(n1_bit_mul_384_carry), .Sum_In(n1_bit_mul_356_sum), .A(A[4]), .B(B[17]),
    .Sum(n1_bit_mul_357_sum), .Carry(n1_bit_mul_357_carry));
  _1_bit_MUL u_1_bit_mul_358 (
    .Carry_In(n1_bit_mul_386_carry), .Sum_In(n1_bit_mul_357_sum), .A(A[3]), .B(B[18]),
    .Sum(n1_bit_mul_358_sum), .Carry(n1_bit_mul_358_carry));
  _1_bit_MUL u_1_bit_mul_359 (
    .Carry_In(n1_bit_mul_388_carry), .Sum_In(n1_bit_mul_358_sum), .A(A[2]), .B(B[19]),
    .Sum(n1_bit_mul_359_sum), .Carry(n1_bit_mul_359_carry));
  _1_bit_MUL u_1_bit_mul_360 (
    .Carry_In(n1_bit_mul_390_carry), .Sum_In(n1_bit_mul_359_sum), .A(A[1]), .B(B[20]),
    .Sum(n1_bit_mul_360_sum), .Carry(n1_bit_mul_360_carry));
  _1_bit_MUL u_1_bit_mul_361 (
    .Carry_In(1'b0), .Sum_In(n1_bit_mul_360_sum), .A(A[0]), .B(B[21]), .Sum(LO[21]),
    .Carry(n1_bit_mul_361_carry));
  _1_bit_MUL u_1_bit_mul_362 (
    .Carry_In(n1_bit_mul_363_carry), .Sum_In(1'b0), .A(A[19]), .B(B[0]), .Sum(n1_bit_mul_362_sum),
    .Carry(n1_bit_mul_362_carry));
  _1_bit_MUL u_1_bit_mul_363 (
    .Carry_In(n1_bit_mul_391_carry), .Sum_In(1'b0), .A(A[18]), .B(B[0]), .Sum(n1_bit_mul_363_sum),
    .Carry(n1_bit_mul_363_carry));
  _1_bit_MUL u_1_bit_mul_364 (
    .Carry_In(n1_bit_mul_365_carry), .Sum_In(n1_bit_mul_362_sum), .A(A[18]), .B(B[1]),
    .Sum(n1_bit_mul_364_sum), .Carry(n1_bit_mul_364_carry));
  _1_bit_MUL u_1_bit_mul_365 (
    .Carry_In(n1_bit_mul_392_carry), .Sum_In(n1_bit_mul_363_sum), .A(A[17]), .B(B[1]),
    .Sum(n1_bit_mul_365_sum), .Carry(n1_bit_mul_365_carry));
  _1_bit_MUL u_1_bit_mul_366 (
    .Carry_In(n1_bit_mul_393_carry), .Sum_In(n1_bit_mul_365_sum), .A(A[16]), .B(B[2]),
    .Sum(n1_bit_mul_366_sum), .Carry(n1_bit_mul_366_carry));
  _1_bit_MUL u_1_bit_mul_367 (
    .Carry_In(n1_bit_mul_366_carry), .Sum_In(n1_bit_mul_364_sum), .A(A[17]), .B(B[1]),
    .Sum(n1_bit_mul_367_sum), .Carry(n1_bit_mul_367_carry));
  _1_bit_MUL u_1_bit_mul_368 (
    .Carry_In(n1_bit_mul_394_carry), .Sum_In(n1_bit_mul_366_sum), .A(A[15]), .B(B[3]),
    .Sum(n1_bit_mul_368_sum), .Carry(n1_bit_mul_368_carry));
  _1_bit_MUL u_1_bit_mul_369 (
    .Carry_In(n1_bit_mul_368_carry), .Sum_In(n1_bit_mul_367_sum), .A(A[16]), .B(B[3]),
    .Sum(n1_bit_mul_369_sum), .Carry(n1_bit_mul_369_carry));
  _1_bit_MUL u_1_bit_mul_370 (
    .Carry_In(n1_bit_mul_396_carry), .Sum_In(n1_bit_mul_369_sum), .A(A[15]), .B(B[4]),
    .Sum(n1_bit_mul_370_sum), .Carry(n1_bit_mul_370_carry));
  _1_bit_MUL u_1_bit_mul_371 (
    .Carry_In(n1_bit_mul_398_carry), .Sum_In(n1_bit_mul_370_sum), .A(A[14]), .B(B[5]),
    .Sum(n1_bit_mul_371_sum), .Carry(n1_bit_mul_371_carry));
  _1_bit_MUL u_1_bit_mul_372 (
    .Carry_In(n1_bit_mul_400_carry), .Sum_In(n1_bit_mul_371_sum), .A(A[13]), .B(B[6]),
    .Sum(n1_bit_mul_372_sum), .Carry(n1_bit_mul_372_carry));
  _1_bit_MUL u_1_bit_mul_373 (
    .Carry_In(n1_bit_mul_401_carry), .Sum_In(n1_bit_mul_372_sum), .A(A[12]), .B(B[7]),
    .Sum(n1_bit_mul_373_sum), .Carry(n1_bit_mul_373_carry));
  _1_bit_MUL u_1_bit_mul_374 (
    .Carry_In(n1_bit_mul_404_carry), .Sum_In(n1_bit_mul_373_sum), .A(A[11]), .B(B[8]),
    .Sum(n1_bit_mul_374_sum), .Carry(n1_bit_mul_374_carry));
  _1_bit_MUL u_1_bit_mul_375 (
    .Carry_In(n1_bit_mul_405_carry), .Sum_In(n1_bit_mul_374_sum), .A(A[10]), .B(B[9]),
    .Sum(n1_bit_mul_375_sum), .Carry(n1_bit_mul_375_carry));
  _1_bit_MUL u_1_bit_mul_376 (
    .Carry_In(n1_bit_mul_406_carry), .Sum_In(n1_bit_mul_375_sum), .A(A[9]), .B(B[10]),
    .Sum(n1_bit_mul_376_sum), .Carry(n1_bit_mul_376_carry));
  _1_bit_MUL u_1_bit_mul_377 (
    .Carry_In(n1_bit_mul_407_carry), .Sum_In(n1_bit_mul_376_sum), .A(A[8]), .B(B[11]),
    .Sum(n1_bit_mul_377_sum), .Carry(n1_bit_mul_377_carry));
  _1_bit_MUL u_1_bit_mul_378 (
    .Carry_In(n1_bit_mul_408_carry), .Sum_In(n1_bit_mul_377_sum), .A(A[7]), .B(B[12]),
    .Sum(n1_bit_mul_378_sum), .Carry(n1_bit_mul_378_carry));
  _1_bit_MUL u_1_bit_mul_379 (
    .Carry_In(n1_bit_mul_409_carry), .Sum_In(n1_bit_mul_378_sum), .A(A[6]), .B(B[13]),
    .Sum(n1_bit_mul_379_sum), .Carry(n1_bit_mul_379_carry));
  _1_bit_MUL u_1_bit_mul_380 (
    .Carry_In(n1_bit_mul_410_carry), .Sum_In(n1_bit_mul_379_sum), .A(A[5]), .B(B[14]),
    .Sum(n1_bit_mul_380_sum), .Carry(n1_bit_mul_380_carry));
  _1_bit_MUL u_1_bit_mul_381 (
    .Carry_In(n1_bit_mul_411_carry), .Sum_In(n1_bit_mul_380_sum), .A(A[4]), .B(B[15]),
    .Sum(n1_bit_mul_381_sum), .Carry(n1_bit_mul_381_carry));
  _1_bit_MUL u_1_bit_mul_382 (
    .Carry_In(n1_bit_mul_412_carry), .Sum_In(n1_bit_mul_381_sum), .A(A[3]), .B(B[16]),
    .Sum(n1_bit_mul_382_sum), .Carry(n1_bit_mul_382_carry));
  _1_bit_MUL u_1_bit_mul_383 (
    .Carry_In(n1_bit_mul_382_carry), .Sum_In(n1_bit_mul_354_sum), .A(A[4]), .B(B[16]),
    .Sum(n1_bit_mul_383_sum), .Carry(n1_bit_mul_383_carry));
  _1_bit_MUL u_1_bit_mul_384 (
    .Carry_In(n1_bit_mul_385_carry), .Sum_In(n1_bit_mul_383_sum), .A(A[3]), .B(B[17]),
    .Sum(n1_bit_mul_384_sum), .Carry(n1_bit_mul_384_carry));
  _1_bit_MUL u_1_bit_mul_385 (
    .Carry_In(n1_bit_mul_413_carry), .Sum_In(n1_bit_mul_382_sum), .A(A[2]), .B(B[17]),
    .Sum(n1_bit_mul_385_sum), .Carry(n1_bit_mul_385_carry));
  _1_bit_MUL u_1_bit_mul_386 (
    .Carry_In(n1_bit_mul_387_carry), .Sum_In(n1_bit_mul_384_sum), .A(A[2]), .B(B[18]),
    .Sum(n1_bit_mul_386_sum), .Carry(n1_bit_mul_386_carry));
  _1_bit_MUL u_1_bit_mul_387 (
    .Carry_In(n1_bit_mul_414_carry), .Sum_In(n1_bit_mul_385_sum), .A(A[1]), .B(B[18]),
    .Sum(n1_bit_mul_387_sum), .Carry(n1_bit_mul_387_carry));
  _1_bit_MUL u_1_bit_mul_388 (
    .Carry_In(n1_bit_mul_389_carry), .Sum_In(n1_bit_mul_386_sum), .A(A[1]), .B(B[19]),
    .Sum(n1_bit_mul_388_sum), .Carry(n1_bit_mul_388_carry));
  _1_bit_MUL u_1_bit_mul_389 (
    .Carry_In(1'b0), .Sum_In(n1_bit_mul_387_sum), .A(A[0]), .B(B[19]), .Sum(LO[19]),
    .Carry(n1_bit_mul_389_carry));
  _1_bit_MUL u_1_bit_mul_390 (
    .Carry_In(1'b0), .Sum_In(n1_bit_mul_388_sum), .A(A[0]), .B(B[20]), .Sum(LO[20]),
    .Carry(n1_bit_mul_390_carry));
  _1_bit_MUL u_1_bit_mul_391 (
    .Carry_In(n1_bit_mul_415_carry), .Sum_In(1'b0), .A(A[17]), .B(B[0]), .Sum(n1_bit_mul_391_sum),
    .Carry(n1_bit_mul_391_carry));
  _1_bit_MUL u_1_bit_mul_392 (
    .Carry_In(n1_bit_mul_416_carry), .Sum_In(n1_bit_mul_391_sum), .A(A[16]), .B(B[1]),
    .Sum(n1_bit_mul_392_sum), .Carry(n1_bit_mul_392_carry));
  _1_bit_MUL u_1_bit_mul_393 (
    .Carry_In(n1_bit_mul_417_carry), .Sum_In(n1_bit_mul_392_sum), .A(A[15]), .B(B[2]),
    .Sum(n1_bit_mul_393_sum), .Carry(n1_bit_mul_393_carry));
  _1_bit_MUL u_1_bit_mul_394 (
    .Carry_In(n1_bit_mul_418_carry), .Sum_In(n1_bit_mul_393_sum), .A(A[14]), .B(B[3]),
    .Sum(n1_bit_mul_394_sum), .Carry(n1_bit_mul_394_carry));
  _1_bit_MUL u_1_bit_mul_395 (
    .Carry_In(n1_bit_mul_419_carry), .Sum_In(n1_bit_mul_394_sum), .A(A[13]), .B(B[4]),
    .Sum(n1_bit_mul_395_sum), .Carry(n1_bit_mul_395_carry));
  _1_bit_MUL u_1_bit_mul_396 (
    .Carry_In(n1_bit_mul_395_carry), .Sum_In(n1_bit_mul_368_sum), .A(A[14]), .B(B[4]),
    .Sum(n1_bit_mul_396_sum), .Carry(n1_bit_mul_396_carry));
  _1_bit_MUL u_1_bit_mul_397 (
    .Carry_In(n1_bit_mul_420_carry), .Sum_In(n1_bit_mul_395_sum), .A(A[12]), .B(B[5]),
    .Sum(n1_bit_mul_397_sum), .Carry(n1_bit_mul_397_carry));
  _1_bit_MUL u_1_bit_mul_398 (
    .Carry_In(n1_bit_mul_397_carry), .Sum_In(n1_bit_mul_396_sum), .A(A[13]), .B(B[5]),
    .Sum(n1_bit_mul_398_sum), .Carry(n1_bit_mul_398_carry));
  _1_bit_MUL u_1_bit_mul_399 (
    .Carry_In(n1_bit_mul_421_carry), .Sum_In(n1_bit_mul_397_sum), .A(A[11]), .B(B[6]),
    .Sum(n1_bit_mul_399_sum), .Carry(n1_bit_mul_399_carry));
  _1_bit_MUL u_1_bit_mul_400 (
    .Carry_In(n1_bit_mul_399_carry), .Sum_In(n1_bit_mul_398_sum), .A(A[12]), .B(B[6]),
    .Sum(n1_bit_mul_400_sum), .Carry(n1_bit_mul_400_carry));
  _1_bit_MUL u_1_bit_mul_401 (
    .Carry_In(n1_bit_mul_402_carry), .Sum_In(n1_bit_mul_400_sum), .A(A[11]), .B(B[7]),
    .Sum(n1_bit_mul_401_sum), .Carry(n1_bit_mul_401_carry));
  _1_bit_MUL u_1_bit_mul_402 (
    .Carry_In(n1_bit_mul_422_carry), .Sum_In(n1_bit_mul_399_sum), .A(A[10]), .B(B[7]),
    .Sum(n1_bit_mul_402_sum), .Carry(n1_bit_mul_402_carry));
  _1_bit_MUL u_1_bit_mul_403 (
    .Carry_In(n1_bit_mul_423_carry), .Sum_In(n1_bit_mul_402_sum), .A(A[9]), .B(B[8]),
    .Sum(n1_bit_mul_403_sum), .Carry(n1_bit_mul_403_carry));
  _1_bit_MUL u_1_bit_mul_404 (
    .Carry_In(n1_bit_mul_403_carry), .Sum_In(n1_bit_mul_401_sum), .A(A[10]), .B(B[8]),
    .Sum(n1_bit_mul_404_sum), .Carry(n1_bit_mul_404_carry));
  _1_bit_MUL u_1_bit_mul_405 (
    .Carry_In(n1_bit_mul_425_carry), .Sum_In(n1_bit_mul_404_sum), .A(A[9]), .B(B[9]),
    .Sum(n1_bit_mul_405_sum), .Carry(n1_bit_mul_405_carry));
  _1_bit_MUL u_1_bit_mul_406 (
    .Carry_In(n1_bit_mul_426_carry), .Sum_In(n1_bit_mul_405_sum), .A(A[8]), .B(B[10]),
    .Sum(n1_bit_mul_406_sum), .Carry(n1_bit_mul_406_carry));
  _1_bit_MUL u_1_bit_mul_407 (
    .Carry_In(n1_bit_mul_428_carry), .Sum_In(n1_bit_mul_406_sum), .A(A[7]), .B(B[11]),
    .Sum(n1_bit_mul_407_sum), .Carry(n1_bit_mul_407_carry));
  _1_bit_MUL u_1_bit_mul_408 (
    .Carry_In(n1_bit_mul_431_carry), .Sum_In(n1_bit_mul_407_sum), .A(A[6]), .B(B[12]),
    .Sum(n1_bit_mul_408_sum), .Carry(n1_bit_mul_408_carry));
  _1_bit_MUL u_1_bit_mul_409 (
    .Carry_In(n1_bit_mul_432_carry), .Sum_In(n1_bit_mul_408_sum), .A(A[5]), .B(B[13]),
    .Sum(n1_bit_mul_409_sum), .Carry(n1_bit_mul_409_carry));
  _1_bit_MUL u_1_bit_mul_410 (
    .Carry_In(n1_bit_mul_434_carry), .Sum_In(n1_bit_mul_409_sum), .A(A[4]), .B(B[14]),
    .Sum(n1_bit_mul_410_sum), .Carry(n1_bit_mul_410_carry));
  _1_bit_MUL u_1_bit_mul_411 (
    .Carry_In(n1_bit_mul_436_carry), .Sum_In(n1_bit_mul_410_sum), .A(A[3]), .B(B[15]),
    .Sum(n1_bit_mul_411_sum), .Carry(n1_bit_mul_411_carry));
  _1_bit_MUL u_1_bit_mul_412 (
    .Carry_In(n1_bit_mul_438_carry), .Sum_In(n1_bit_mul_411_sum), .A(A[2]), .B(B[16]),
    .Sum(n1_bit_mul_412_sum), .Carry(n1_bit_mul_412_carry));
  _1_bit_MUL u_1_bit_mul_413 (
    .Carry_In(n1_bit_mul_439_carry), .Sum_In(n1_bit_mul_412_sum), .A(A[1]), .B(B[17]),
    .Sum(n1_bit_mul_413_sum), .Carry(n1_bit_mul_413_carry));
  _1_bit_MUL u_1_bit_mul_414 (
    .Carry_In(1'b0), .Sum_In(n1_bit_mul_413_sum), .A(A[0]), .B(B[18]), .Sum(LO[18]),
    .Carry(n1_bit_mul_414_carry));
  _1_bit_MUL u_1_bit_mul_415 (
    .Carry_In(n1_bit_mul_441_carry), .Sum_In(1'b0), .A(A[16]), .B(B[0]), .Sum(n1_bit_mul_415_sum),
    .Carry(n1_bit_mul_415_carry));
  _1_bit_MUL u_1_bit_mul_416 (
    .Carry_In(n1_bit_mul_443_carry), .Sum_In(n1_bit_mul_415_sum), .A(A[15]), .B(B[1]),
    .Sum(n1_bit_mul_416_sum), .Carry(n1_bit_mul_416_carry));
  _1_bit_MUL u_1_bit_mul_417 (
    .Carry_In(n1_bit_mul_445_carry), .Sum_In(n1_bit_mul_416_sum), .A(A[14]), .B(B[2]),
    .Sum(n1_bit_mul_417_sum), .Carry(n1_bit_mul_417_carry));
  _1_bit_MUL u_1_bit_mul_418 (
    .Carry_In(n1_bit_mul_446_carry), .Sum_In(n1_bit_mul_417_sum), .A(A[13]), .B(B[3]),
    .Sum(n1_bit_mul_418_sum), .Carry(n1_bit_mul_418_carry));
  _1_bit_MUL u_1_bit_mul_419 (
    .Carry_In(n1_bit_mul_448_carry), .Sum_In(n1_bit_mul_418_sum), .A(A[12]), .B(B[4]),
    .Sum(n1_bit_mul_419_sum), .Carry(n1_bit_mul_419_carry));
  _1_bit_MUL u_1_bit_mul_420 (
    .Carry_In(n1_bit_mul_449_carry), .Sum_In(n1_bit_mul_419_sum), .A(A[11]), .B(B[5]),
    .Sum(n1_bit_mul_420_sum), .Carry(n1_bit_mul_420_carry));
  _1_bit_MUL u_1_bit_mul_421 (
    .Carry_In(n1_bit_mul_450_carry), .Sum_In(n1_bit_mul_420_sum), .A(A[10]), .B(B[6]),
    .Sum(n1_bit_mul_421_sum), .Carry(n1_bit_mul_421_carry));
  _1_bit_MUL u_1_bit_mul_422 (
    .Carry_In(n1_bit_mul_451_carry), .Sum_In(n1_bit_mul_421_sum), .A(A[9]), .B(B[7]),
    .Sum(n1_bit_mul_422_sum), .Carry(n1_bit_mul_422_carry));
  _1_bit_MUL u_1_bit_mul_423 (
    .Carry_In(n1_bit_mul_452_carry), .Sum_In(n1_bit_mul_422_sum), .A(A[8]), .B(B[8]),
    .Sum(n1_bit_mul_423_sum), .Carry(n1_bit_mul_423_carry));
  _1_bit_MUL u_1_bit_mul_424 (
    .Carry_In(n1_bit_mul_453_carry), .Sum_In(n1_bit_mul_423_sum), .A(A[7]), .B(B[9]),
    .Sum(n1_bit_mul_424_sum), .Carry(n1_bit_mul_424_carry));
  _1_bit_MUL u_1_bit_mul_425 (
    .Carry_In(n1_bit_mul_424_carry), .Sum_In(n1_bit_mul_403_sum), .A(A[8]), .B(B[9]),
    .Sum(n1_bit_mul_425_sum), .Carry(n1_bit_mul_425_carry));
  _1_bit_MUL u_1_bit_mul_426 (
    .Carry_In(n1_bit_mul_427_carry), .Sum_In(n1_bit_mul_425_sum), .A(A[7]), .B(B[10]),
    .Sum(n1_bit_mul_426_sum), .Carry(n1_bit_mul_426_carry));
  _1_bit_MUL u_1_bit_mul_427 (
    .Carry_In(n1_bit_mul_454_carry), .Sum_In(n1_bit_mul_424_sum), .A(A[6]), .B(B[10]),
    .Sum(n1_bit_mul_427_sum), .Carry(n1_bit_mul_427_carry));
  _1_bit_MUL u_1_bit_mul_428 (
    .Carry_In(n1_bit_mul_429_carry), .Sum_In(n1_bit_mul_426_sum), .A(A[6]), .B(B[11]),
    .Sum(n1_bit_mul_428_sum), .Carry(n1_bit_mul_428_carry));
  _1_bit_MUL u_1_bit_mul_429 (
    .Carry_In(n1_bit_mul_455_carry), .Sum_In(n1_bit_mul_427_sum), .A(A[5]), .B(B[11]),
    .Sum(n1_bit_mul_429_sum), .Carry(n1_bit_mul_429_carry));
  _1_bit_MUL u_1_bit_mul_430 (
    .Carry_In(n1_bit_mul_456_carry), .Sum_In(n1_bit_mul_429_sum), .A(A[4]), .B(B[12]),
    .Sum(n1_bit_mul_430_sum), .Carry(n1_bit_mul_430_carry));
  _1_bit_MUL u_1_bit_mul_431 (
    .Carry_In(n1_bit_mul_430_carry), .Sum_In(n1_bit_mul_428_sum), .A(A[5]), .B(B[12]),
    .Sum(n1_bit_mul_431_sum), .Carry(n1_bit_mul_431_carry));
  _1_bit_MUL u_1_bit_mul_432 (
    .Carry_In(n1_bit_mul_433_carry), .Sum_In(n1_bit_mul_431_sum), .A(A[4]), .B(B[13]),
    .Sum(n1_bit_mul_432_sum), .Carry(n1_bit_mul_432_carry));
  _1_bit_MUL u_1_bit_mul_433 (
    .Carry_In(n1_bit_mul_457_carry), .Sum_In(n1_bit_mul_430_sum), .A(A[3]), .B(B[13]),
    .Sum(n1_bit_mul_433_sum), .Carry(n1_bit_mul_433_carry));
  _1_bit_MUL u_1_bit_mul_434 (
    .Carry_In(n1_bit_mul_435_carry), .Sum_In(n1_bit_mul_432_sum), .A(A[3]), .B(B[14]),
    .Sum(n1_bit_mul_434_sum), .Carry(n1_bit_mul_434_carry));
  _1_bit_MUL u_1_bit_mul_435 (
    .Carry_In(n1_bit_mul_458_carry), .Sum_In(n1_bit_mul_433_sum), .A(A[2]), .B(B[14]),
    .Sum(n1_bit_mul_435_sum), .Carry(n1_bit_mul_435_carry));
  _1_bit_MUL u_1_bit_mul_436 (
    .Carry_In(n1_bit_mul_437_carry), .Sum_In(n1_bit_mul_434_sum), .A(A[2]), .B(B[15]),
    .Sum(n1_bit_mul_436_sum), .Carry(n1_bit_mul_436_carry));
  _1_bit_MUL u_1_bit_mul_437 (
    .Carry_In(n1_bit_mul_459_carry), .Sum_In(n1_bit_mul_435_sum), .A(A[1]), .B(B[15]),
    .Sum(n1_bit_mul_437_sum), .Carry(n1_bit_mul_437_carry));
  _1_bit_MUL u_1_bit_mul_438 (
    .Carry_In(n1_bit_mul_460_carry), .Sum_In(n1_bit_mul_436_sum), .A(A[1]), .B(B[16]),
    .Sum(n1_bit_mul_438_sum), .Carry(n1_bit_mul_438_carry));
  _1_bit_MUL u_1_bit_mul_439 (
    .Carry_In(1'b0), .Sum_In(n1_bit_mul_438_sum), .A(A[0]), .B(B[17]), .Sum(LO[17]),
    .Carry(n1_bit_mul_439_carry));
  _1_bit_MUL u_1_bit_mul_440 (
    .Carry_In(n1_bit_mul_461_carry), .Sum_In(1'b0), .A(A[14]), .B(B[0]), .Sum(n1_bit_mul_440_sum),
    .Carry(n1_bit_mul_440_carry));
  _1_bit_MUL u_1_bit_mul_441 (
    .Carry_In(n1_bit_mul_440_carry), .Sum_In(1'b0), .A(A[15]), .B(B[0]), .Sum(n1_bit_mul_441_sum),
    .Carry(n1_bit_mul_441_carry));
  _1_bit_MUL u_1_bit_mul_442 (
    .Carry_In(n1_bit_mul_462_carry), .Sum_In(n1_bit_mul_440_sum), .A(A[13]), .B(B[1]),
    .Sum(n1_bit_mul_442_sum), .Carry(n1_bit_mul_442_carry));
  _1_bit_MUL u_1_bit_mul_443 (
    .Carry_In(n1_bit_mul_442_carry), .Sum_In(n1_bit_mul_441_sum), .A(A[14]), .B(B[1]),
    .Sum(n1_bit_mul_443_sum), .Carry(n1_bit_mul_443_carry));
  _1_bit_MUL u_1_bit_mul_444 (
    .Carry_In(n1_bit_mul_463_carry), .Sum_In(n1_bit_mul_442_sum), .A(A[12]), .B(B[2]),
    .Sum(n1_bit_mul_444_sum), .Carry(n1_bit_mul_444_carry));
  _1_bit_MUL u_1_bit_mul_445 (
    .Carry_In(n1_bit_mul_444_carry), .Sum_In(n1_bit_mul_443_sum), .A(A[13]), .B(B[2]),
    .Sum(n1_bit_mul_445_sum), .Carry(n1_bit_mul_445_carry));
  _1_bit_MUL u_1_bit_mul_446 (
    .Carry_In(n1_bit_mul_447_carry), .Sum_In(n1_bit_mul_445_sum), .A(A[12]), .B(B[3]),
    .Sum(n1_bit_mul_446_sum), .Carry(n1_bit_mul_446_carry));
  _1_bit_MUL u_1_bit_mul_447 (
    .Carry_In(n1_bit_mul_464_carry), .Sum_In(n1_bit_mul_444_sum), .A(A[11]), .B(B[3]),
    .Sum(n1_bit_mul_447_sum), .Carry(n1_bit_mul_447_carry));
  _1_bit_MUL u_1_bit_mul_448 (
    .Carry_In(n1_bit_mul_465_carry), .Sum_In(n1_bit_mul_446_sum), .A(A[11]), .B(B[4]),
    .Sum(n1_bit_mul_448_sum), .Carry(n1_bit_mul_448_carry));
  _1_bit_MUL u_1_bit_mul_449 (
    .Carry_In(n1_bit_mul_468_carry), .Sum_In(n1_bit_mul_448_sum), .A(A[10]), .B(B[5]),
    .Sum(n1_bit_mul_449_sum), .Carry(n1_bit_mul_449_carry));
  _1_bit_MUL u_1_bit_mul_450 (
    .Carry_In(n1_bit_mul_470_carry), .Sum_In(n1_bit_mul_449_sum), .A(A[9]), .B(B[6]),
    .Sum(n1_bit_mul_450_sum), .Carry(n1_bit_mul_450_carry));
  _1_bit_MUL u_1_bit_mul_451 (
    .Carry_In(n1_bit_mul_472_carry), .Sum_In(n1_bit_mul_450_sum), .A(A[8]), .B(B[7]),
    .Sum(n1_bit_mul_451_sum), .Carry(n1_bit_mul_451_carry));
  _1_bit_MUL u_1_bit_mul_452 (
    .Carry_In(n1_bit_mul_473_carry), .Sum_In(n1_bit_mul_451_sum), .A(A[7]), .B(B[8]),
    .Sum(n1_bit_mul_452_sum), .Carry(n1_bit_mul_452_carry));
  _1_bit_MUL u_1_bit_mul_453 (
    .Carry_In(n1_bit_mul_475_carry), .Sum_In(n1_bit_mul_452_sum), .A(A[6]), .B(B[9]),
    .Sum(n1_bit_mul_453_sum), .Carry(n1_bit_mul_453_carry));
  _1_bit_MUL u_1_bit_mul_454 (
    .Carry_In(n1_bit_mul_476_carry), .Sum_In(n1_bit_mul_453_sum), .A(A[5]), .B(B[10]),
    .Sum(n1_bit_mul_454_sum), .Carry(n1_bit_mul_454_carry));
  _1_bit_MUL u_1_bit_mul_455 (
    .Carry_In(n1_bit_mul_477_carry), .Sum_In(n1_bit_mul_454_sum), .A(A[4]), .B(B[11]),
    .Sum(n1_bit_mul_455_sum), .Carry(n1_bit_mul_455_carry));
  _1_bit_MUL u_1_bit_mul_456 (
    .Carry_In(n1_bit_mul_478_carry), .Sum_In(n1_bit_mul_455_sum), .A(A[3]), .B(B[12]),
    .Sum(n1_bit_mul_456_sum), .Carry(n1_bit_mul_456_carry));
  _1_bit_MUL u_1_bit_mul_457 (
    .Carry_In(n1_bit_mul_479_carry), .Sum_In(n1_bit_mul_456_sum), .A(A[2]), .B(B[1]),
    .Sum(n1_bit_mul_457_sum), .Carry(n1_bit_mul_457_carry));
  _1_bit_MUL u_1_bit_mul_458 (
    .Carry_In(n1_bit_mul_480_carry), .Sum_In(n1_bit_mul_457_sum), .A(A[1]), .B(B[14]),
    .Sum(n1_bit_mul_458_sum), .Carry(n1_bit_mul_458_carry));
  _1_bit_MUL u_1_bit_mul_459 (
    .Carry_In(1'b0), .Sum_In(n1_bit_mul_458_sum), .A(A[0]), .B(B[15]), .Sum(LO[15]),
    .Carry(n1_bit_mul_459_carry));
  _1_bit_MUL u_1_bit_mul_460 (
    .Carry_In(1'b0), .Sum_In(n1_bit_mul_437_sum), .A(A[0]), .B(B[16]), .Sum(LO[16]),
    .Carry(n1_bit_mul_460_carry));
  _1_bit_MUL u_1_bit_mul_461 (
    .Carry_In(n1_bit_mul_481_carry), .Sum_In(1'b0), .A(A[13]), .B(B[0]), .Sum(n1_bit_mul_461_sum),
    .Carry(n1_bit_mul_461_carry));
  _1_bit_MUL u_1_bit_mul_462 (
    .Carry_In(n1_bit_mul_482_carry), .Sum_In(n1_bit_mul_461_sum), .A(A[12]), .B(B[1]),
    .Sum(n1_bit_mul_462_sum), .Carry(n1_bit_mul_462_carry));
  _1_bit_MUL u_1_bit_mul_463 (
    .Carry_In(n1_bit_mul_483_carry), .Sum_In(n1_bit_mul_462_sum), .A(A[11]), .B(B[2]),
    .Sum(n1_bit_mul_463_sum), .Carry(n1_bit_mul_463_carry));
  _1_bit_MUL u_1_bit_mul_464 (
    .Carry_In(n1_bit_mul_484_carry), .Sum_In(n1_bit_mul_463_sum), .A(A[10]), .B(B[3]),
    .Sum(n1_bit_mul_464_sum), .Carry(n1_bit_mul_464_carry));
  _1_bit_MUL u_1_bit_mul_465 (
    .Carry_In(n1_bit_mul_466_carry), .Sum_In(n1_bit_mul_447_sum), .A(A[10]), .B(B[4]),
    .Sum(n1_bit_mul_465_sum), .Carry(n1_bit_mul_465_carry));
  _1_bit_MUL u_1_bit_mul_466 (
    .Carry_In(n1_bit_mul_485_carry), .Sum_In(n1_bit_mul_464_sum), .A(A[9]), .B(B[4]),
    .Sum(n1_bit_mul_466_sum), .Carry(n1_bit_mul_466_carry));
  _1_bit_MUL u_1_bit_mul_467 (
    .Carry_In(n1_bit_mul_486_carry), .Sum_In(n1_bit_mul_466_sum), .A(A[8]), .B(B[5]),
    .Sum(n1_bit_mul_467_sum), .Carry(n1_bit_mul_467_carry));
  _1_bit_MUL u_1_bit_mul_468 (
    .Carry_In(n1_bit_mul_467_carry), .Sum_In(n1_bit_mul_465_sum), .A(A[9]), .B(B[5]),
    .Sum(n1_bit_mul_468_sum), .Carry(n1_bit_mul_468_carry));
  _1_bit_MUL u_1_bit_mul_469 (
    .Carry_In(n1_bit_mul_487_carry), .Sum_In(n1_bit_mul_467_sum), .A(A[7]), .B(B[6]),
    .Sum(n1_bit_mul_469_sum), .Carry(n1_bit_mul_469_carry));
  _1_bit_MUL u_1_bit_mul_470 (
    .Carry_In(n1_bit_mul_469_carry), .Sum_In(n1_bit_mul_468_sum), .A(A[8]), .B(B[6]),
    .Sum(n1_bit_mul_470_sum), .Carry(n1_bit_mul_470_carry));
  _1_bit_MUL u_1_bit_mul_471 (
    .Carry_In(n1_bit_mul_488_carry), .Sum_In(n1_bit_mul_469_sum), .A(A[6]), .B(B[7]),
    .Sum(n1_bit_mul_471_sum), .Carry(n1_bit_mul_471_carry));
  _1_bit_MUL u_1_bit_mul_472 (
    .Carry_In(n1_bit_mul_471_carry), .Sum_In(n1_bit_mul_470_sum), .A(A[7]), .B(B[7]),
    .Sum(n1_bit_mul_472_sum), .Carry(n1_bit_mul_472_carry));
  _1_bit_MUL u_1_bit_mul_473 (
    .Carry_In(n1_bit_mul_474_carry), .Sum_In(n1_bit_mul_472_sum), .A(A[6]), .B(B[8]),
    .Sum(n1_bit_mul_473_sum), .Carry(n1_bit_mul_473_carry));
  _1_bit_MUL u_1_bit_mul_474 (
    .Carry_In(n1_bit_mul_489_carry), .Sum_In(n1_bit_mul_471_sum), .A(A[5]), .B(B[8]),
    .Sum(n1_bit_mul_474_sum), .Carry(n1_bit_mul_474_carry));
  _1_bit_MUL u_1_bit_mul_475 (
    .Carry_In(n1_bit_mul_491_carry), .Sum_In(n1_bit_mul_473_sum), .A(A[5]), .B(B[9]),
    .Sum(n1_bit_mul_475_sum), .Carry(n1_bit_mul_475_carry));
  _1_bit_MUL u_1_bit_mul_476 (
    .Carry_In(n1_bit_mul_492_carry), .Sum_In(n1_bit_mul_475_sum), .A(A[4]), .B(B[10]),
    .Sum(n1_bit_mul_476_sum), .Carry(n1_bit_mul_476_carry));
  _1_bit_MUL u_1_bit_mul_477 (
    .Carry_In(n1_bit_mul_494_carry), .Sum_In(n1_bit_mul_476_sum), .A(A[3]), .B(B[11]),
    .Sum(n1_bit_mul_477_sum), .Carry(n1_bit_mul_477_carry));
  _1_bit_MUL u_1_bit_mul_478 (
    .Carry_In(n1_bit_mul_497_carry), .Sum_In(n1_bit_mul_477_sum), .A(A[2]), .B(B[12]),
    .Sum(n1_bit_mul_478_sum), .Carry(n1_bit_mul_478_carry));
  _1_bit_MUL u_1_bit_mul_479 (
    .Carry_In(n1_bit_mul_498_carry), .Sum_In(n1_bit_mul_478_sum), .A(A[1]), .B(B[13]),
    .Sum(n1_bit_mul_479_sum), .Carry(n1_bit_mul_479_carry));
  _1_bit_MUL u_1_bit_mul_480 (
    .Carry_In(1'b0), .Sum_In(n1_bit_mul_479_sum), .A(A[0]), .B(B[14]), .Sum(LO[14]),
    .Carry(n1_bit_mul_480_carry));
  _1_bit_MUL u_1_bit_mul_481 (
    .Carry_In(n1_bit_mul_500_carry), .Sum_In(1'b0), .A(A[12]), .B(B[0]), .Sum(n1_bit_mul_481_sum),
    .Carry(n1_bit_mul_481_carry));
  _1_bit_MUL u_1_bit_mul_482 (
    .Carry_In(n1_bit_mul_501_carry), .Sum_In(n1_bit_mul_481_sum), .A(A[11]), .B(B[1]),
    .Sum(n1_bit_mul_482_sum), .Carry(n1_bit_mul_482_carry));
  _1_bit_MUL u_1_bit_mul_483 (
    .Carry_In(n1_bit_mul_503_carry), .Sum_In(n1_bit_mul_482_sum), .A(A[10]), .B(B[2]),
    .Sum(n1_bit_mul_483_sum), .Carry(n1_bit_mul_483_carry));
  _1_bit_MUL u_1_bit_mul_484 (
    .Carry_In(n1_bit_mul_506_carry), .Sum_In(n1_bit_mul_483_sum), .A(A[9]), .B(B[3]),
    .Sum(n1_bit_mul_484_sum), .Carry(n1_bit_mul_484_carry));
  _1_bit_MUL u_1_bit_mul_485 (
    .Carry_In(n1_bit_mul_507_carry), .Sum_In(n1_bit_mul_484_sum), .A(A[8]), .B(B[4]),
    .Sum(n1_bit_mul_485_sum), .Carry(n1_bit_mul_485_carry));
  _1_bit_MUL u_1_bit_mul_486 (
    .Carry_In(n1_bit_mul_508_carry), .Sum_In(n1_bit_mul_485_sum), .A(A[7]), .B(B[5]),
    .Sum(n1_bit_mul_486_sum), .Carry(n1_bit_mul_486_carry));
  _1_bit_MUL u_1_bit_mul_487 (
    .Carry_In(n1_bit_mul_509_carry), .Sum_In(n1_bit_mul_486_sum), .A(A[6]), .B(B[6]),
    .Sum(n1_bit_mul_487_sum), .Carry(n1_bit_mul_487_carry));
  _1_bit_MUL u_1_bit_mul_488 (
    .Carry_In(n1_bit_mul_510_carry), .Sum_In(n1_bit_mul_487_sum), .A(A[5]), .B(B[7]),
    .Sum(n1_bit_mul_488_sum), .Carry(n1_bit_mul_488_carry));
  _1_bit_MUL u_1_bit_mul_489 (
    .Carry_In(n1_bit_mul_511_carry), .Sum_In(n1_bit_mul_488_sum), .A(A[4]), .B(B[8]),
    .Sum(n1_bit_mul_489_sum), .Carry(n1_bit_mul_489_carry));
  _1_bit_MUL u_1_bit_mul_490 (
    .Carry_In(n1_bit_mul_512_carry), .Sum_In(n1_bit_mul_489_sum), .A(A[3]), .B(B[9]),
    .Sum(n1_bit_mul_490_sum), .Carry(n1_bit_mul_490_carry));
  _1_bit_MUL u_1_bit_mul_491 (
    .Carry_In(n1_bit_mul_490_carry), .Sum_In(n1_bit_mul_474_sum), .A(A[4]), .B(B[9]),
    .Sum(n1_bit_mul_491_sum), .Carry(n1_bit_mul_491_carry));
  _1_bit_MUL u_1_bit_mul_492 (
    .Carry_In(n1_bit_mul_493_carry), .Sum_In(n1_bit_mul_491_sum), .A(A[3]), .B(B[10]),
    .Sum(n1_bit_mul_492_sum), .Carry(n1_bit_mul_492_carry));
  _1_bit_MUL u_1_bit_mul_493 (
    .Carry_In(n1_bit_mul_513_carry), .Sum_In(n1_bit_mul_490_sum), .A(A[2]), .B(B[10]),
    .Sum(n1_bit_mul_493_sum), .Carry(n1_bit_mul_493_carry));
  _1_bit_MUL u_1_bit_mul_494 (
    .Carry_In(n1_bit_mul_495_carry), .Sum_In(n1_bit_mul_492_sum), .A(A[2]), .B(B[11]),
    .Sum(n1_bit_mul_494_sum), .Carry(n1_bit_mul_494_carry));
  _1_bit_MUL u_1_bit_mul_495 (
    .Carry_In(n1_bit_mul_514_carry), .Sum_In(n1_bit_mul_493_sum), .A(A[1]), .B(B[11]),
    .Sum(n1_bit_mul_495_sum), .Carry(n1_bit_mul_495_carry));
  _1_bit_MUL u_1_bit_mul_496 (
    .Carry_In(1'b0), .Sum_In(n1_bit_mul_495_sum), .A(A[0]), .B(B[12]), .Sum(LO[12]),
    .Carry(n1_bit_mul_496_carry));
  _1_bit_MUL u_1_bit_mul_497 (
    .Carry_In(n1_bit_mul_496_carry), .Sum_In(n1_bit_mul_494_sum), .A(A[1]), .B(B[12]),
    .Sum(n1_bit_mul_497_sum), .Carry(n1_bit_mul_497_carry));
  _1_bit_MUL u_1_bit_mul_498 (
    .Carry_In(1'b0), .Sum_In(n1_bit_mul_497_sum), .A(A[0]), .B(B[13]), .Sum(LO[13]),
    .Carry(n1_bit_mul_498_carry));
  _1_bit_MUL u_1_bit_mul_499 (
    .Carry_In(n1_bit_mul_515_carry), .Sum_In(1'b0), .A(A[10]), .B(B[0]), .Sum(n1_bit_mul_499_sum),
    .Carry(n1_bit_mul_499_carry));
  _1_bit_MUL u_1_bit_mul_500 (
    .Carry_In(n1_bit_mul_499_carry), .Sum_In(1'b0), .A(A[11]), .B(B[0]), .Sum(n1_bit_mul_500_sum),
    .Carry(n1_bit_mul_500_carry));
  _1_bit_MUL u_1_bit_mul_501 (
    .Carry_In(n1_bit_mul_502_carry), .Sum_In(n1_bit_mul_500_sum), .A(A[10]), .B(B[1]),
    .Sum(n1_bit_mul_501_sum), .Carry(n1_bit_mul_501_carry));
  _1_bit_MUL u_1_bit_mul_502 (
    .Carry_In(n1_bit_mul_516_carry), .Sum_In(n1_bit_mul_499_sum), .A(A[9]), .B(B[1]),
    .Sum(n1_bit_mul_502_sum), .Carry(n1_bit_mul_502_carry));
  _1_bit_MUL u_1_bit_mul_503 (
    .Carry_In(n1_bit_mul_504_carry), .Sum_In(n1_bit_mul_501_sum), .A(A[9]), .B(B[2]),
    .Sum(n1_bit_mul_503_sum), .Carry(n1_bit_mul_503_carry));
  _1_bit_MUL u_1_bit_mul_504 (
    .Carry_In(n1_bit_mul_517_carry), .Sum_In(n1_bit_mul_502_sum), .A(A[8]), .B(B[2]),
    .Sum(n1_bit_mul_504_sum), .Carry(n1_bit_mul_504_carry));
  _1_bit_MUL u_1_bit_mul_505 (
    .Carry_In(n1_bit_mul_518_carry), .Sum_In(n1_bit_mul_504_sum), .A(A[7]), .B(B[3]),
    .Sum(n1_bit_mul_505_sum), .Carry(n1_bit_mul_505_carry));
  _1_bit_MUL u_1_bit_mul_506 (
    .Carry_In(n1_bit_mul_505_carry), .Sum_In(n1_bit_mul_503_sum), .A(A[8]), .B(B[3]),
    .Sum(n1_bit_mul_506_sum), .Carry(n1_bit_mul_506_carry));
  _1_bit_MUL u_1_bit_mul_507 (
    .Carry_In(n1_bit_mul_520_carry), .Sum_In(n1_bit_mul_506_sum), .A(A[7]), .B(B[4]),
    .Sum(n1_bit_mul_507_sum), .Carry(n1_bit_mul_507_carry));
  _1_bit_MUL u_1_bit_mul_508 (
    .Carry_In(n1_bit_mul_522_carry), .Sum_In(n1_bit_mul_507_sum), .A(A[6]), .B(B[5]),
    .Sum(n1_bit_mul_508_sum), .Carry(n1_bit_mul_508_carry));
  _1_bit_MUL u_1_bit_mul_509 (
    .Carry_In(n1_bit_mul_524_carry), .Sum_In(n1_bit_mul_508_sum), .A(A[5]), .B(B[6]),
    .Sum(n1_bit_mul_509_sum), .Carry(n1_bit_mul_509_carry));
  _1_bit_MUL u_1_bit_mul_510 (
    .Carry_In(n1_bit_mul_526_carry), .Sum_In(n1_bit_mul_509_sum), .A(A[4]), .B(B[7]),
    .Sum(n1_bit_mul_510_sum), .Carry(n1_bit_mul_510_carry));
  _1_bit_MUL u_1_bit_mul_511 (
    .Carry_In(n1_bit_mul_527_carry), .Sum_In(n1_bit_mul_510_sum), .A(A[3]), .B(B[8]),
    .Sum(n1_bit_mul_511_sum), .Carry(n1_bit_mul_511_carry));
  _1_bit_MUL u_1_bit_mul_512 (
    .Carry_In(n1_bit_mul_529_carry), .Sum_In(n1_bit_mul_511_sum), .A(A[2]), .B(B[9]),
    .Sum(n1_bit_mul_512_sum), .Carry(n1_bit_mul_512_carry));
  _1_bit_MUL u_1_bit_mul_513 (
    .Carry_In(n1_bit_mul_530_carry), .Sum_In(n1_bit_mul_512_sum), .A(A[1]), .B(B[10]),
    .Sum(n1_bit_mul_513_sum), .Carry(n1_bit_mul_513_carry));
  _1_bit_MUL u_1_bit_mul_514 (
    .Carry_In(1'b0), .Sum_In(n1_bit_mul_513_sum), .A(A[0]), .B(B[11]), .Sum(LO[11]),
    .Carry(n1_bit_mul_514_carry));
  _1_bit_MUL u_1_bit_mul_515 (
    .Carry_In(n1_bit_mul_531_carry), .Sum_In(1'b0), .A(A[9]), .B(B[0]), .Sum(n1_bit_mul_515_sum),
    .Carry(n1_bit_mul_515_carry));
  _1_bit_MUL u_1_bit_mul_516 (
    .Carry_In(n1_bit_mul_532_carry), .Sum_In(n1_bit_mul_515_sum), .A(A[8]), .B(B[1]),
    .Sum(n1_bit_mul_516_sum), .Carry(n1_bit_mul_516_carry));
  _1_bit_MUL u_1_bit_mul_517 (
    .Carry_In(n1_bit_mul_533_carry), .Sum_In(n1_bit_mul_516_sum), .A(A[7]), .B(B[2]),
    .Sum(n1_bit_mul_517_sum), .Carry(n1_bit_mul_517_carry));
  _1_bit_MUL u_1_bit_mul_518 (
    .Carry_In(n1_bit_mul_534_carry), .Sum_In(n1_bit_mul_517_sum), .A(A[6]), .B(B[3]),
    .Sum(n1_bit_mul_518_sum), .Carry(n1_bit_mul_518_carry));
  _1_bit_MUL u_1_bit_mul_519 (
    .Carry_In(n1_bit_mul_535_carry), .Sum_In(n1_bit_mul_518_sum), .A(A[5]), .B(B[4]),
    .Sum(n1_bit_mul_519_sum), .Carry(n1_bit_mul_519_carry));
  _1_bit_MUL u_1_bit_mul_520 (
    .Carry_In(n1_bit_mul_519_carry), .Sum_In(n1_bit_mul_505_sum), .A(A[6]), .B(B[4]),
    .Sum(n1_bit_mul_520_sum), .Carry(n1_bit_mul_520_carry));
  _1_bit_MUL u_1_bit_mul_521 (
    .Carry_In(n1_bit_mul_536_carry), .Sum_In(n1_bit_mul_519_sum), .A(A[4]), .B(B[5]),
    .Sum(n1_bit_mul_521_sum), .Carry(n1_bit_mul_521_carry));
  _1_bit_MUL u_1_bit_mul_522 (
    .Carry_In(n1_bit_mul_521_carry), .Sum_In(n1_bit_mul_520_sum), .A(A[5]), .B(B[5]),
    .Sum(n1_bit_mul_522_sum), .Carry(n1_bit_mul_522_carry));
  _1_bit_MUL u_1_bit_mul_523 (
    .Carry_In(n1_bit_mul_537_carry), .Sum_In(n1_bit_mul_521_sum), .A(A[3]), .B(B[6]),
    .Sum(n1_bit_mul_523_sum), .Carry(n1_bit_mul_523_carry));
  _1_bit_MUL u_1_bit_mul_524 (
    .Carry_In(n1_bit_mul_523_carry), .Sum_In(n1_bit_mul_522_sum), .A(A[4]), .B(B[6]),
    .Sum(n1_bit_mul_524_sum), .Carry(n1_bit_mul_524_carry));
  _1_bit_MUL u_1_bit_mul_525 (
    .Carry_In(n1_bit_mul_538_carry), .Sum_In(n1_bit_mul_523_sum), .A(A[2]), .B(B[7]),
    .Sum(n1_bit_mul_525_sum), .Carry(n1_bit_mul_525_carry));
  _1_bit_MUL u_1_bit_mul_526 (
    .Carry_In(n1_bit_mul_525_carry), .Sum_In(n1_bit_mul_524_sum), .A(A[3]), .B(B[7]),
    .Sum(n1_bit_mul_526_sum), .Carry(n1_bit_mul_526_carry));
  _1_bit_MUL u_1_bit_mul_527 (
    .Carry_In(n1_bit_mul_528_carry), .Sum_In(n1_bit_mul_526_sum), .A(A[2]), .B(B[8]),
    .Sum(n1_bit_mul_527_sum), .Carry(n1_bit_mul_527_carry));
  _1_bit_MUL u_1_bit_mul_528 (
    .Carry_In(n1_bit_mul_539_carry), .Sum_In(n1_bit_mul_525_sum), .A(A[1]), .B(B[8]),
    .Sum(n1_bit_mul_528_sum), .Carry(n1_bit_mul_528_carry));
  _1_bit_MUL u_1_bit_mul_529 (
    .Carry_In(n1_bit_mul_540_carry), .Sum_In(n1_bit_mul_527_sum), .A(A[1]), .B(B[9]),
    .Sum(n1_bit_mul_529_sum), .Carry(n1_bit_mul_529_carry));
  _1_bit_MUL u_1_bit_mul_530 (
    .Carry_In(1'b0), .Sum_In(n1_bit_mul_529_sum), .A(A[0]), .B(B[10]), .Sum(LO[10]),
    .Carry(n1_bit_mul_530_carry));
  _1_bit_MUL u_1_bit_mul_531 (
    .Carry_In(n1_bit_mul_541_carry), .Sum_In(1'b0), .A(A[8]), .B(B[0]), .Sum(n1_bit_mul_531_sum),
    .Carry(n1_bit_mul_531_carry));
  _1_bit_MUL u_1_bit_mul_532 (
    .Carry_In(n1_bit_mul_543_carry), .Sum_In(n1_bit_mul_531_sum), .A(A[7]), .B(B[1]),
    .Sum(n1_bit_mul_532_sum), .Carry(n1_bit_mul_532_carry));
  _1_bit_MUL u_1_bit_mul_533 (
    .Carry_In(n1_bit_mul_546_carry), .Sum_In(n1_bit_mul_532_sum), .A(A[6]), .B(B[2]),
    .Sum(n1_bit_mul_533_sum), .Carry(n1_bit_mul_533_carry));
  _1_bit_MUL u_1_bit_mul_534 (
    .Carry_In(n1_bit_mul_547_carry), .Sum_In(n1_bit_mul_533_sum), .A(A[5]), .B(B[3]),
    .Sum(n1_bit_mul_534_sum), .Carry(n1_bit_mul_534_carry));
  _1_bit_MUL u_1_bit_mul_535 (
    .Carry_In(n1_bit_mul_549_carry), .Sum_In(n1_bit_mul_534_sum), .A(A[4]), .B(B[4]),
    .Sum(n1_bit_mul_535_sum), .Carry(n1_bit_mul_535_carry));
  _1_bit_MUL u_1_bit_mul_536 (
    .Carry_In(n1_bit_mul_550_carry), .Sum_In(n1_bit_mul_535_sum), .A(A[3]), .B(B[5]),
    .Sum(n1_bit_mul_536_sum), .Carry(n1_bit_mul_536_carry));
  _1_bit_MUL u_1_bit_mul_537 (
    .Carry_In(n1_bit_mul_551_carry), .Sum_In(n1_bit_mul_536_sum), .A(A[2]), .B(B[6]),
    .Sum(n1_bit_mul_537_sum), .Carry(n1_bit_mul_537_carry));
  _1_bit_MUL u_1_bit_mul_538 (
    .Carry_In(n1_bit_mul_552_carry), .Sum_In(n1_bit_mul_537_sum), .A(A[1]), .B(B[7]),
    .Sum(n1_bit_mul_538_sum), .Carry(n1_bit_mul_538_carry));
  _1_bit_MUL u_1_bit_mul_539 (
    .Carry_In(1'b0), .Sum_In(n1_bit_mul_538_sum), .A(A[0]), .B(B[8]), .Sum(LO[8]),
    .Carry(n1_bit_mul_539_carry));
  _1_bit_MUL u_1_bit_mul_540 (
    .Carry_In(1'b0), .Sum_In(n1_bit_mul_528_sum), .A(A[0]), .B(B[9]), .Sum(LO[9]),
    .Carry(n1_bit_mul_540_carry));
  _1_bit_MUL u_1_bit_mul_541 (
    .Carry_In(n1_bit_mul_542_carry), .Sum_In(1'b0), .A(A[7]), .B(B[0]), .Sum(n1_bit_mul_541_sum),
    .Carry(n1_bit_mul_541_carry));
  _1_bit_MUL u_1_bit_mul_542 (
    .Carry_In(n1_bit_mul_553_carry), .Sum_In(1'b0), .A(A[6]), .B(B[0]), .Sum(n1_bit_mul_542_sum),
    .Carry(n1_bit_mul_542_carry));
  _1_bit_MUL u_1_bit_mul_543 (
    .Carry_In(n1_bit_mul_544_carry), .Sum_In(n1_bit_mul_541_sum), .A(A[6]), .B(B[1]),
    .Sum(n1_bit_mul_543_sum), .Carry(n1_bit_mul_543_carry));
  _1_bit_MUL u_1_bit_mul_544 (
    .Carry_In(n1_bit_mul_554_carry), .Sum_In(n1_bit_mul_542_sum), .A(A[5]), .B(B[1]),
    .Sum(n1_bit_mul_544_sum), .Carry(n1_bit_mul_544_carry));
  _1_bit_MUL u_1_bit_mul_545 (
    .Carry_In(n1_bit_mul_555_carry), .Sum_In(n1_bit_mul_544_sum), .A(A[4]), .B(B[2]),
    .Sum(n1_bit_mul_545_sum), .Carry(n1_bit_mul_545_carry));
  _1_bit_MUL u_1_bit_mul_546 (
    .Carry_In(n1_bit_mul_545_carry), .Sum_In(n1_bit_mul_543_sum), .A(A[5]), .B(B[2]),
    .Sum(n1_bit_mul_546_sum), .Carry(n1_bit_mul_546_carry));
  _1_bit_MUL u_1_bit_mul_547 (
    .Carry_In(n1_bit_mul_548_carry), .Sum_In(n1_bit_mul_546_sum), .A(A[4]), .B(B[3]),
    .Sum(n1_bit_mul_547_sum), .Carry(n1_bit_mul_547_carry));
  _1_bit_MUL u_1_bit_mul_548 (
    .Carry_In(n1_bit_mul_556_carry), .Sum_In(n1_bit_mul_545_sum), .A(A[3]), .B(B[3]),
    .Sum(n1_bit_mul_548_sum), .Carry(n1_bit_mul_548_carry));
  _1_bit_MUL u_1_bit_mul_549 (
    .Carry_In(n1_bit_mul_557_carry), .Sum_In(n1_bit_mul_547_sum), .A(A[3]), .B(B[4]),
    .Sum(n1_bit_mul_549_sum), .Carry(n1_bit_mul_549_carry));
  _1_bit_MUL u_1_bit_mul_550 (
    .Carry_In(n1_bit_mul_559_carry), .Sum_In(n1_bit_mul_549_sum), .A(A[2]), .B(B[5]),
    .Sum(n1_bit_mul_550_sum), .Carry(n1_bit_mul_550_carry));
  _1_bit_MUL u_1_bit_mul_551 (
    .Carry_In(n1_bit_mul_561_carry), .Sum_In(n1_bit_mul_550_sum), .A(A[1]), .B(B[6]),
    .Sum(n1_bit_mul_551_sum), .Carry(n1_bit_mul_551_carry));
  _1_bit_MUL u_1_bit_mul_552 (
    .Carry_In(1'b0), .Sum_In(n1_bit_mul_551_sum), .A(A[0]), .B(B[7]), .Sum(LO[7]),
    .Carry(n1_bit_mul_552_carry));
  _1_bit_MUL u_1_bit_mul_553 (
    .Carry_In(n1_bit_mul_562_carry), .Sum_In(1'b0), .A(A[5]), .B(B[0]), .Sum(n1_bit_mul_553_sum),
    .Carry(n1_bit_mul_553_carry));
  _1_bit_MUL u_1_bit_mul_554 (
    .Carry_In(n1_bit_mul_563_carry), .Sum_In(n1_bit_mul_553_sum), .A(A[4]), .B(B[1]),
    .Sum(n1_bit_mul_554_sum), .Carry(n1_bit_mul_554_carry));
  _1_bit_MUL u_1_bit_mul_555 (
    .Carry_In(n1_bit_mul_564_carry), .Sum_In(n1_bit_mul_554_sum), .A(A[3]), .B(B[2]),
    .Sum(n1_bit_mul_555_sum), .Carry(n1_bit_mul_555_carry));
  _1_bit_MUL u_1_bit_mul_556 (
    .Carry_In(n1_bit_mul_565_carry), .Sum_In(n1_bit_mul_555_sum), .A(A[2]), .B(B[3]),
    .Sum(n1_bit_mul_556_sum), .Carry(n1_bit_mul_556_carry));
  _1_bit_MUL u_1_bit_mul_557 (
    .Carry_In(n1_bit_mul_558_carry), .Sum_In(n1_bit_mul_548_sum), .A(A[2]), .B(B[4]),
    .Sum(n1_bit_mul_557_sum), .Carry(n1_bit_mul_557_carry));
  _1_bit_MUL u_1_bit_mul_558 (
    .Carry_In(n1_bit_mul_566_carry), .Sum_In(n1_bit_mul_556_sum), .A(A[1]), .B(B[4]),
    .Sum(n1_bit_mul_558_sum), .Carry(n1_bit_mul_558_carry));
  _1_bit_MUL u_1_bit_mul_559 (
    .Carry_In(n1_bit_mul_560_carry), .Sum_In(n1_bit_mul_557_sum), .A(A[1]), .B(B[5]),
    .Sum(n1_bit_mul_559_sum), .Carry(n1_bit_mul_559_carry));
  _1_bit_MUL u_1_bit_mul_560 (
    .Carry_In(1'b0), .Sum_In(n1_bit_mul_558_sum), .A(A[0]), .B(B[5]), .Sum(LO[5]),
    .Carry(n1_bit_mul_560_carry));
  _1_bit_MUL u_1_bit_mul_561 (
    .Carry_In(1'b0), .Sum_In(n1_bit_mul_559_sum), .A(A[0]), .B(B[6]), .Sum(LO[6]),
    .Carry(n1_bit_mul_561_carry));
  _1_bit_MUL u_1_bit_mul_562 (
    .Carry_In(n1_bit_mul_567_carry), .Sum_In(1'b0), .A(A[4]), .B(B[0]), .Sum(n1_bit_mul_562_sum),
    .Carry(n1_bit_mul_562_carry));
  _1_bit_MUL u_1_bit_mul_563 (
    .Carry_In(n1_bit_mul_570_carry), .Sum_In(n1_bit_mul_562_sum), .A(A[3]), .B(B[1]),
    .Sum(n1_bit_mul_563_sum), .Carry(n1_bit_mul_563_carry));
  _1_bit_MUL u_1_bit_mul_564 (
    .Carry_In(n1_bit_mul_571_carry), .Sum_In(n1_bit_mul_563_sum), .A(A[2]), .B(B[2]),
    .Sum(n1_bit_mul_564_sum), .Carry(n1_bit_mul_564_carry));
  _1_bit_MUL u_1_bit_mul_565 (
    .Carry_In(n1_bit_mul_573_carry), .Sum_In(n1_bit_mul_564_sum), .A(A[1]), .B(B[3]),
    .Sum(n1_bit_mul_565_sum), .Carry(n1_bit_mul_565_carry));
  _1_bit_MUL u_1_bit_mul_566 (
    .Carry_In(1'b0), .Sum_In(n1_bit_mul_565_sum), .A(A[0]), .B(B[4]), .Sum(LO[4]),
    .Carry(n1_bit_mul_566_carry));
  _1_bit_MUL u_1_bit_mul_567 (
    .Carry_In(n1_bit_mul_568_carry), .Sum_In(1'b0), .A(A[3]), .B(B[0]), .Sum(n1_bit_mul_567_sum),
    .Carry(n1_bit_mul_567_carry));
  _1_bit_MUL u_1_bit_mul_568 (
    .Carry_In(n1_bit_mul_574_carry), .Sum_In(1'b0), .A(A[2]), .B(B[0]), .Sum(n1_bit_mul_568_sum),
    .Carry(n1_bit_mul_568_carry));
  _1_bit_MUL u_1_bit_mul_569 (
    .Carry_In(n1_bit_mul_575_carry), .Sum_In(n1_bit_mul_568_sum), .A(A[1]), .B(B[1]),
    .Sum(n1_bit_mul_569_sum), .Carry(n1_bit_mul_569_carry));
  _1_bit_MUL u_1_bit_mul_570 (
    .Carry_In(n1_bit_mul_569_carry), .Sum_In(n1_bit_mul_567_sum), .A(A[2]), .B(B[1]),
    .Sum(n1_bit_mul_570_sum), .Carry(n1_bit_mul_570_carry));
  _1_bit_MUL u_1_bit_mul_571 (
    .Carry_In(n1_bit_mul_572_carry), .Sum_In(n1_bit_mul_570_sum), .A(A[1]), .B(B[2]),
    .Sum(n1_bit_mul_571_sum), .Carry(n1_bit_mul_571_carry));
  _1_bit_MUL u_1_bit_mul_572 (
    .Carry_In(1'b0), .Sum_In(n1_bit_mul_569_sum), .A(A[0]), .B(B[2]), .Sum(LO[2]),
    .Carry(n1_bit_mul_572_carry));
  _1_bit_MUL u_1_bit_mul_573 (
    .Carry_In(1'b0), .Sum_In(n1_bit_mul_571_sum), .A(A[0]), .B(B[3]), .Sum(LO[3]),
    .Carry(n1_bit_mul_573_carry));
  _1_bit_MUL u_1_bit_mul_574 (
    .Carry_In(n1_bit_mul_576_carry), .Sum_In(1'b0), .A(A[1]), .B(B[0]), .Sum(n1_bit_mul_574_sum),
    .Carry(n1_bit_mul_574_carry));
  _1_bit_MUL u_1_bit_mul_575 (
    .Carry_In(1'b0), .Sum_In(n1_bit_mul_574_sum), .A(A[0]), .B(B[1]), .Sum(LO[1]),
    .Carry(n1_bit_mul_575_carry));
  _1_bit_MUL u_1_bit_mul_576 (
    .Carry_In(1'b0), .Sum_In(1'b0), .A(A[0]), .B(B[0]), .Sum(LO[0]), .Carry(n1_bit_mul_576_carry));

  // Other names for the same wires on the sheet: _24 = HI[0]; _25 = HI[1]; _26 = HI[2]; _27 = HI[3]; _28 = HI[4];
  //   _29 = HI[5]; _30 = HI[6]; _31 = HI[7]; _32 = HI[8]; _33 = HI[9]; _34 = HI[10]; _35 = HI[11]; _36 = HI[12];
  //   _37 = HI[13]; _38 = HI[14]; _39 = HI[15]; _40 = HI[16]; _41 = HI[17]; _42 = HI[18]; _43 = HI[19]; _44 = HI[20];
  //   _45 = HI[21]; _46 = HI[22]; _47 = HI[23]; _0 = LO[0]; _1 = LO[1]; _2 = LO[2]; _3 = LO[3]; _4 = LO[4];
  //   _5 = LO[5]; _6 = LO[6]; _7 = LO[7]; _8 = LO[8]; _9 = LO[9]; _10 = LO[10]; _11 = LO[11]; _12 = LO[12];
  //   _13 = LO[13]; _14 = LO[14]; _15 = LO[15]; _16 = LO[16]; _17 = LO[17]; _18 = LO[18]; _19 = LO[19]; _20 = LO[20];
  //   _21 = LO[21]; _22 = LO[22]; _23 = LO[23]

  // Notes on the sheet:
  //   x
endmodule

module CLA (
  input  Carry_in,
  input  A,
  input  B,
  output S,
  output Pi,
  output Gi
);

  wire xor_1_out;

  xor xor_1 (xor_1_out, A, B);
  or or_1 (Pi, A, B);
  and and_1 (Gi, A, B);
  xor xor_2 (S, Carry_in, xor_1_out);

  // Notes on the sheet:
  //   CLA
endmodule

module Carry_Look_ahead (
  input  G0,
  input  P0,
  input  C0,
  input  G1,
  input  P1,
  input  P2,
  input  G2,
  input  P3,
  input  G3,
  output C1,
  output C2,
  output C3,
  output C4
);

  wire and_1_out, and_2_out, and_3_out, and_4_out, and_5_out, and_6_out, and_7_out, and_8_out, and_9_out,
       and_10_out;

  and and_1 (and_1_out, P0, C0);
  or or_1 (C1, G0, and_1_out);
  and and_2 (and_2_out, and_1_out, P1);
  or or_2 (C2, and_2_out, and_3_out, G1);
  and and_3 (and_3_out, P1, G0);
  and and_4 (and_4_out, and_3_out, P2);
  and and_5 (and_5_out, and_2_out, P2);
  or or_3 (C3, and_4_out, and_5_out, and_7_out, G2);
  and and_6 (and_6_out, G2, P3);
  and and_7 (and_7_out, P2, G1);
  and and_8 (and_8_out, and_7_out, P3);
  and and_9 (and_9_out, and_4_out, P3);
  and and_10 (and_10_out, and_5_out, P3);
  or or_4 (C4, and_10_out, and_9_out, and_8_out, and_6_out, G3);
endmodule

// CLA
module _24_bit_CLA (
  input  Add_0__Sub_1,
  input  [23:0] A,
  input  [23:0] B,
  output [23:0] RESULT,
  output CLA_Carry_Out,
  output Overflow
);

  wire and_1_out, and_2_out, B0, B1, B2, B3, B4, B5, B6, B7, B8, B9, B10, B11, B12, B13, B14, B15, B16, B17,
       B18, B19, B20, B21, B22, B23, C1, C2, C3, C4, C5, C6, C7, C8, C9, C10, C11, C12, C13, C14, C15, C16,
       C17, C18, C19, C20, C21, C22, C23, cla_1_gi, cla_1_pi, cla_2_gi, cla_2_pi, cla_3_gi, cla_3_pi,
       cla_4_gi, cla_4_pi, cla_5_gi, cla_5_pi, cla_6_gi, cla_6_pi, cla_7_gi, cla_7_pi, cla_8_gi, cla_8_pi,
       cla_9_gi, cla_9_pi, cla_10_gi, cla_10_pi, cla_11_gi, cla_11_pi, cla_12_gi, cla_12_pi, cla_13_gi,
       cla_13_pi, cla_14_gi, cla_14_pi, cla_15_gi, cla_15_pi, cla_16_gi, cla_16_pi, cla_17_gi, cla_17_pi,
       cla_18_gi, cla_18_pi, cla_19_gi, cla_19_pi, cla_20_gi, cla_20_pi, cla_21_gi, cla_21_pi, cla_22_gi,
       cla_22_pi, cla_23_gi, cla_23_pi, cla_24_gi, cla_24_pi, not_1_out, not_2_out, not_3_out;

  CLA cla_1 (.Carry_in(Add_0__Sub_1), .A(A[0]), .B(B0), .S(RESULT[0]), .Pi(cla_1_pi), .Gi(cla_1_gi));
  CLA cla_2 (.Carry_in(C16), .A(A[16]), .B(B16), .S(RESULT[16]), .Pi(cla_2_pi), .Gi(cla_2_gi));
  CLA cla_3 (.Carry_in(C1), .A(A[1]), .B(B1), .S(RESULT[1]), .Pi(cla_3_pi), .Gi(cla_3_gi));
  Carry_Look_ahead carry_look_ahead_1 (
    .G0(cla_1_gi), .P0(cla_1_pi), .C0(Add_0__Sub_1), .G1(cla_3_gi), .P1(cla_3_pi), .P2(cla_5_pi),
    .G2(cla_5_gi), .P3(cla_7_pi), .G3(cla_7_gi), .C1(C1), .C2(C2), .C3(C3), .C4(C4));
  CLA cla_4 (.Carry_in(C17), .A(A[17]), .B(B17), .S(RESULT[17]), .Pi(cla_4_pi), .Gi(cla_4_gi));
  Carry_Look_ahead carry_look_ahead_2 (
    .G0(cla_2_gi), .P0(cla_2_pi), .C0(C16), .G1(cla_4_gi), .P1(cla_4_pi), .P2(cla_6_pi), .G2(cla_6_gi),
    .P3(cla_8_pi), .G3(cla_8_gi), .C1(C17), .C2(C18), .C3(C19), .C4(C20));
  CLA cla_5 (.Carry_in(C2), .A(A[2]), .B(B2), .S(RESULT[2]), .Pi(cla_5_pi), .Gi(cla_5_gi));
  CLA cla_6 (.Carry_in(C18), .A(A[18]), .B(B18), .S(RESULT[18]), .Pi(cla_6_pi), .Gi(cla_6_gi));
  CLA cla_7 (.Carry_in(C3), .A(A[3]), .B(B3), .S(RESULT[3]), .Pi(cla_7_pi), .Gi(cla_7_gi));
  CLA cla_8 (.Carry_in(C19), .A(A[19]), .B(B19), .S(RESULT[19]), .Pi(cla_8_pi), .Gi(cla_8_gi));
  not not_1 (not_1_out, B23);
  not not_2 (not_2_out, C23);
  CLA cla_9 (.Carry_in(C5), .A(A[5]), .B(B5), .S(RESULT[5]), .Pi(cla_9_pi), .Gi(cla_9_gi));
  CLA cla_10 (.Carry_in(C4), .A(A[4]), .B(B4), .S(RESULT[4]), .Pi(cla_10_pi), .Gi(cla_10_gi));
  Carry_Look_ahead carry_look_ahead_3 (
    .G0(cla_10_gi), .P0(cla_10_pi), .C0(C4), .G1(cla_9_gi), .P1(cla_9_pi), .P2(cla_13_pi), .G2(cla_13_gi),
    .P3(cla_15_pi), .G3(cla_15_gi), .C1(C5), .C2(C6), .C3(C7), .C4(C8));
  CLA cla_11 (.Carry_in(C20), .A(A[20]), .B(B20), .S(RESULT[20]), .Pi(cla_11_pi), .Gi(cla_11_gi));
  CLA cla_12 (.Carry_in(C21), .A(A[21]), .B(B21), .S(RESULT[21]), .Pi(cla_12_pi), .Gi(cla_12_gi));
  Carry_Look_ahead carry_look_ahead_4 (
    .G0(cla_11_gi), .P0(cla_11_pi), .C0(C20), .G1(cla_12_gi), .P1(cla_12_pi), .P2(cla_14_pi), .G2(cla_14_gi),
    .P3(cla_16_pi), .G3(cla_16_gi), .C1(C21), .C2(C22), .C3(C23), .C4(CLA_Carry_Out));
  not not_3 (not_3_out, A[23]);
  and and_1 (and_1_out, not_3_out, not_1_out, C23);
  and and_2 (and_2_out, not_2_out, B23, A[23]);
  CLA cla_13 (.Carry_in(C6), .A(A[6]), .B(B6), .S(RESULT[6]), .Pi(cla_13_pi), .Gi(cla_13_gi));
  CLA cla_14 (.Carry_in(C22), .A(A[22]), .B(B22), .S(RESULT[22]), .Pi(cla_14_pi), .Gi(cla_14_gi));
  or or_1 (Overflow, and_1_out, and_2_out);
  xor xor_1 (B23, B[23], Add_0__Sub_1);
  CLA cla_15 (.Carry_in(C7), .A(A[7]), .B(B7), .S(RESULT[7]), .Pi(cla_15_pi), .Gi(cla_15_gi));
  CLA cla_16 (.Carry_in(C23), .A(A[23]), .B(B23), .S(RESULT[23]), .Pi(cla_16_pi), .Gi(cla_16_gi));
  xor xor_2 (B21, B[21], Add_0__Sub_1);
  xor xor_3 (B20, B[20], Add_0__Sub_1);
  xor xor_4 (B22, B[22], Add_0__Sub_1);
  CLA cla_17 (.Carry_in(C8), .A(A[8]), .B(B8), .S(RESULT[8]), .Pi(cla_17_pi), .Gi(cla_17_gi));
  xor xor_5 (B18, B[18], Add_0__Sub_1);
  xor xor_6 (B17, B[17], Add_0__Sub_1);
  xor xor_7 (B19, B[19], Add_0__Sub_1);
  CLA cla_18 (.Carry_in(C9), .A(A[9]), .B(B9), .S(RESULT[9]), .Pi(cla_18_pi), .Gi(cla_18_gi));
  Carry_Look_ahead carry_look_ahead_5 (
    .G0(cla_17_gi), .P0(cla_17_pi), .C0(C8), .G1(cla_18_gi), .P1(cla_18_pi), .P2(cla_20_pi), .G2(cla_20_gi),
    .P3(cla_19_pi), .G3(cla_19_gi), .C1(C9), .C2(C10), .C3(C11), .C4(C12));
  xor xor_8 (B16, B[16], Add_0__Sub_1);
  xor xor_9 (B15, B[15], Add_0__Sub_1);
  CLA cla_19 (.Carry_in(C11), .A(A[11]), .B(B11), .S(RESULT[11]), .Pi(cla_19_pi), .Gi(cla_19_gi));
  CLA cla_20 (.Carry_in(C10), .A(A[10]), .B(B10), .S(RESULT[10]), .Pi(cla_20_pi), .Gi(cla_20_gi));
  xor xor_10 (B13, B[13], Add_0__Sub_1);
  xor xor_11 (B12, B[12], Add_0__Sub_1);
  xor xor_12 (B14, B[14], Add_0__Sub_1);
  CLA cla_21 (.Carry_in(C12), .A(A[12]), .B(B12), .S(RESULT[12]), .Pi(cla_21_pi), .Gi(cla_21_gi));
  CLA cla_22 (.Carry_in(C13), .A(A[13]), .B(B13), .S(RESULT[13]), .Pi(cla_22_pi), .Gi(cla_22_gi));
  Carry_Look_ahead carry_look_ahead_6 (
    .G0(cla_21_gi), .P0(cla_21_pi), .C0(C12), .G1(cla_22_gi), .P1(cla_22_pi), .P2(cla_23_pi), .G2(cla_23_gi),
    .P3(cla_24_pi), .G3(cla_24_gi), .C1(C13), .C2(C14), .C3(C15), .C4(C16));
  xor xor_13 (B10, B[10], Add_0__Sub_1);
  xor xor_14 (B11, B[11], Add_0__Sub_1);
  CLA cla_23 (.Carry_in(C14), .A(A[14]), .B(B14), .S(RESULT[14]), .Pi(cla_23_pi), .Gi(cla_23_gi));
  xor xor_15 (B8, B[8], Add_0__Sub_1);
  xor xor_16 (B9, B[9], Add_0__Sub_1);
  xor xor_17 (B7, B[7], Add_0__Sub_1);
  CLA cla_24 (.Carry_in(C15), .A(A[15]), .B(B15), .S(RESULT[15]), .Pi(cla_24_pi), .Gi(cla_24_gi));
  xor xor_18 (B5, B[5], Add_0__Sub_1);
  xor xor_19 (B6, B[6], Add_0__Sub_1);
  xor xor_20 (B4, B[4], Add_0__Sub_1);
  xor xor_21 (B2, B[2], Add_0__Sub_1);
  xor xor_22 (B3, B[3], Add_0__Sub_1);
  xor xor_23 (B1, B[1], Add_0__Sub_1);
  xor xor_24 (B0, B[0], Add_0__Sub_1);

  // Other names for the same wires on the sheet: A_S = Add_0__Sub_1; _0 = RESULT[0]; _1 = RESULT[1]; _2 = RESULT[2];
  //   _3 = RESULT[3]; _4 = RESULT[4]; _5 = RESULT[5]; _6 = RESULT[6]; _7 = RESULT[7]; _8 = RESULT[8]; _9 = RESULT[9];
  //   _10 = RESULT[10]; _11 = RESULT[11]; _12 = RESULT[12]; _13 = RESULT[13]; _14 = RESULT[14]; _15 = RESULT[15];
  //   _16 = RESULT[16]; _17 = RESULT[17]; _18 = RESULT[18]; _19 = RESULT[19]; _20 = RESULT[20]; _21 = RESULT[21];
  //   _22 = RESULT[22]; _23 = RESULT[23]

  // Notes on the sheet:
  //   CLA 24 bit Add/Sub
endmodule

module _24_bit_ALU (
  input  [23:0] A,
  input  [23:0] B,
  input  ADD_0__SUB_1,
  input  [2:0] SECIM,
  output [23:0] RESULT,
  output Zero,
  output Overflow,
  output Carry,
  output CLA_Overflow,
  output CLA_Carry,
  output Negative
);

  wire [23:0] ADD_SUB_result, AND_result, n24_bit_cla_1_result, n24_bit_mul_1_hi, n24_bit_mul_1_lo,
       NOR_result, OR_result, XOR_result;

  _24_bit_ADD_SUB ADD_SUB (
    .Overflow(Overflow), .A(A), .B(B), .RESULT(ADD_SUB_result), .Add_0__Sub_1(ADD_0__SUB_1), .Carry_Out(Carry));
  _24_bit_CLA u_24_bit_cla_1 (
    .Overflow(CLA_Overflow), .A(A), .RESULT(n24_bit_cla_1_result), .CLA_Carry_Out(CLA_Carry),
    .Add_0__Sub_1(ADD_0__SUB_1), .B(B));
  _24_BIT_MUL u_24_bit_mul_1 (.A(A), .HI(n24_bit_mul_1_hi), .B(B), .LO(n24_bit_mul_1_lo));
  _24_bit_AND AND (.A(A), .B(B), .Result(AND_result));
  _24_bit_OR OR (.A(A), .B(B), .Result(OR_result));
  _24_bit_XOR XOR (.A(A), .B(B), .Result(XOR_result));
  _24_bit_NOR NOR (.A(A), .B(B), .Result(NOR_result));
  Multiplexer #(.select(3), .width(24)) multiplexer_1 (
    .in0(AND_result), .in1(OR_result), .in2(XOR_result), .in3(NOR_result), .in4(ADD_SUB_result),
    .in5(n24_bit_cla_1_result), .in6(n24_bit_mul_1_lo), .in7(n24_bit_mul_1_hi),
    .out({Negative, RESULT[22:0]}), .sel(SECIM));  // open: en
  nor nor_2 (Zero, RESULT[0], RESULT[1], RESULT[2], RESULT[3], RESULT[4], RESULT[5], RESULT[6], RESULT[7], RESULT[8], RESULT[9], RESULT[10], RESULT[11], RESULT[12], RESULT[13], RESULT[14], RESULT[15], RESULT[16], RESULT[17], RESULT[18], RESULT[19], RESULT[20], RESULT[21], RESULT[22], Negative);

  assign RESULT[23] = Negative;

  // Notes on the sheet:
  //   Salih YESİR 1850144004
  //   000:AND
  //   001: OR
  //   010:XOR
  //   011:NOR
  //   100:Ripple
  //   101:CLA
  //   110:Multiply LO
  //   111:Multiply HI
  //   not carry add/sub için
endmodule
